// Logisim project ALU_32.circ as structural Verilog: 3 circuits, main circuit main
module main (
  input  [31:0] in_1,
  input  [31:0] in_2,
  input  [3:0] in_3,
  output [31:0] out_4,
  output zero,
  output neg
);

  wire adder_1_cout, comparator_1_lt, comparator_2_lt, subtractor_1_bout;
  wire [31:0] adder_1_out, and_1_out, bit_extender_1_out, bit_extender_2_out, bit_extender_3_out,
       bit_extender_4_out, divider_1_out, divider_1_rem, divu_1_out_3, divu_1_out_4, multiplier_1_out,
       mulu_1_out_3, nor_1_out, or_1_out, subtractor_1_out, xor_1_out;

  Adder #(.width(32)) adder_1 (.a(in_1), .b(in_2), .out(adder_1_out), .cout(adder_1_cout));  // open: cin
  Subtractor #(.width(32)) subtractor_1 (
    .a(in_1), .b(in_2), .out(subtractor_1_out), .bout(subtractor_1_bout));  // open: bin
  Multiplier #(.width(32)) multiplier_1 (.a(in_1), .b(in_2), .out(multiplier_1_out));  // open: cin, cout
  mulu mulu_1 (.in_1(in_2), .in_2(in_1), .out_3(mulu_1_out_3));
  Divider #(.width(32)) divider_1 (.a(in_1), .b(in_2), .out(divider_1_out), .rem(divider_1_rem));  // open: upper
  divu divu_1 (.in_1(in_1), .in_2(in_2), .out_3(divu_1_out_3), .out_4(divu_1_out_4));
  Comparator #(.width(32)) comparator_1 (.a(in_1), .b(in_2), .lt(comparator_1_lt));  // open: gt, eq
  Comparator #(.width(32), .mode("unsigned")) comparator_2 (.a(in_1), .b(in_2), .lt(comparator_2_lt));  // open: gt, eq
  assign nor_1_out = ~(in_1 | in_2);  // NOR_Gate nor_1, 32 bits wide
  assign and_1_out = in_1 & in_2;  // AND_Gate and_1, 32 bits wide
  assign or_1_out = in_1 | in_2;  // OR_Gate or_1, 32 bits wide
  assign xor_1_out = in_1 ^ in_2;  // XOR_Gate xor_1, 32 bits wide
  assign bit_extender_1_out = {{31{1'b0}}, adder_1_cout};  // Bit_Extender bit_extender_1
  assign bit_extender_2_out = {{31{1'b0}}, subtractor_1_bout};  // Bit_Extender bit_extender_2
  assign bit_extender_3_out = {{31{1'b0}}, comparator_1_lt};  // Bit_Extender bit_extender_3
  assign bit_extender_4_out = {{31{1'b0}}, comparator_2_lt};  // Bit_Extender bit_extender_4
  Multiplexer #(.select(4), .width(32), .enable("false")) multiplexer_1 (
    .in0(adder_1_out), .in1(bit_extender_1_out), .in2(subtractor_1_out), .in3(bit_extender_2_out),
    .in4(multiplier_1_out), .in5(mulu_1_out_3), .in6(divider_1_out), .in7(divider_1_rem), .in8(divu_1_out_3),
    .in9(divu_1_out_4), .in10(bit_extender_3_out), .in11(bit_extender_4_out), .in12(nor_1_out),
    .in13(and_1_out), .in14(or_1_out), .in15(xor_1_out), .out(out_4), .sel(in_3));
  Comparator #(.width(32), .mode("unsigned")) comparator_3 (
    .a(out_4), .b({32{1'b0}}), .eq(zero), .lt(neg));  // open: gt
endmodule

module mulu (
  input  [31:0] in_1,
  input  [31:0] in_2,
  output [31:0] out_3
);
endmodule

module divu (
  input  [31:0] in_1,
  input  [31:0] in_2,
  output [31:0] out_3,
  output [31:0] out_4
);
endmodule
