// Logisim project micro.circ as structural Verilog: 1 circuit, main circuit main
module main (
  input  [31:0] in_1,
  input  [4:0] in_2,
  input  [4:0] in_3,
  input  [4:0] in_4,
  input  in_5
);

  wire clock_1_out;
  wire [31:0] main_1_out_7, main_1_out_8;

  Clock clock_1 (.out(clock_1_out));
  // Probe on main_1_out_7
  RF_main main_1 (
    .out_7(main_1_out_7), .out_8(main_1_out_8), .Data(in_1), .dir_dest(in_2), .dir_a(in_4), .dir_b(in_3),
    .CLK(clock_1_out), .R_W(in_5));
  // Probe on main_1_out_8
endmodule
