// Logisim project s-mips.circ as structural Verilog: 18 circuits, main circuit S-MIPS Board
module S_MIPS_Board (
  output halt
);

  wire button_1_out, CLK, CS, d_ff_1_q, R_W, Reset_out, RST, TTY_EN;
  wire [2:0] KDB;
  wire [3:0] Mask, ram_1_read_time, ram_1_write_time;
  wire [6:0] KDB_DATA, TTY_DATA;
  wire [15:0] Addr;
  wire [31:0] ram_1_data_out_0, ram_1_data_out_1, ram_1_data_out_2, ram_1_data_out_3, s_mips_1_ram_in_0,
       s_mips_1_ram_in_1, s_mips_1_ram_in_2, s_mips_1_ram_in_3;

  TTY #(.rows(25), .cols(80)) tty_1 (.data(TTY_DATA), .clk(CLK), .we(TTY_EN), .clr(RST));
  RAM ram_1 (
    .Address(Addr), .Data_Out_0(ram_1_data_out_0), .Data_Out_1(ram_1_data_out_1),
    .Data_Out_2(ram_1_data_out_2), .Data_Out_3(ram_1_data_out_3), .Data_In_0(s_mips_1_ram_in_0),
    .Data_In_1(s_mips_1_ram_in_1), .Data_In_2(s_mips_1_ram_in_2), .Data_In_3(s_mips_1_ram_in_3), .Mask(Mask),
    .nRead_Write(R_W), .Chip_Select(CS), .Read_Time(ram_1_read_time), .Reset(button_1_out),
    .Write_Time(ram_1_write_time));
  Button button_1 (.out(button_1_out));
  Keyboard #(.buflen(64)) keyboard_1 (.clk(CLK), .re(KDB[0]), .avail(KDB[2]), .data(KDB_DATA));  // open: clr
  S_MIPS s_mips_1 (
    .Kbd_Enable(KDB[0]), .Address(Addr), .Kbd_Clear(KDB[1]), .Kbd_Available(KDB[2]),
    .RAM_In_0(s_mips_1_ram_in_0), .Kbd_ASCII_Data(KDB_DATA), .RAM_In_1(s_mips_1_ram_in_1),
    .TTY_Enable(TTY_EN), .RAM_In_2(s_mips_1_ram_in_2), .RAM_In_3(s_mips_1_ram_in_3),
    .TTY_ASCII_Data(TTY_DATA), .Reset(RST), .RAM_Out_0(ram_1_data_out_0), .Clock(CLK),
    .RAM_Out_1(ram_1_data_out_1), .Stop(halt), .RAM_Out_2(ram_1_data_out_2), .RAM_Out_3(ram_1_data_out_3),
    .Mask(Mask), .Read_Time(ram_1_read_time), .Write_Time(ram_1_write_time), .nRead_Write(R_W),
    .Chip_Select(CS));
  D_Flip_Flop d_ff_1 (.clk(CLK), .D(1'b1), .Q(d_ff_1_q), .reset(Reset_out));  // open: Qn, preset, en
  Button Reset (.out(Reset_out));
  Clock clock_1 (.out(CLK));
  D_Flip_Flop d_ff_2 (.clk(CLK), .D(d_ff_1_q), .Qn(RST), .reset(Reset_out));  // open: Q, preset, en

  // Notes on the sheet:
  //   NO MODIFICAR
  //   Keyboard
endmodule

module RAM (
  input  [15:0] Address,
  input  [31:0] Data_In_0,
  input  [31:0] Data_In_1,
  input  [31:0] Data_In_2,
  input  [31:0] Data_In_3,
  input  [3:0] Mask,
  input  nRead_Write,
  input  Chip_Select,
  input  Reset,
  output [31:0] Data_Out_0,
  output [31:0] Data_Out_1,
  output [31:0] Data_Out_2,
  output [31:0] Data_Out_3,
  output [3:0] Read_Time,
  output [3:0] Write_Time
);

  wire and_2_out, and_3_out, and_4_out, and_5_out, and_6_out, and_7_out, and_8_out, and_9_out, Changed, CLK,
       comparator_2_eq, comparator_3_eq, comparator_4_eq, comparator_5_eq, comparator_6_eq, Count,
       demultiplexer_3_out0, Idle, Idle_q, Load, Load0, Load1, nand_1_out, or_1_out, or_2_out, or_3_out,
       or_4_out, or_5_out, or_6_out, or_7_out, or_8_out, or_9_out, or_10_out, Proc_q, Update_Mem, Zero_Time;
  wire [3:0] counter_1_q, multiplexer_1_out, subtractor_1_out;
  wire [31:0] register_1_q, register_2_q, register_3_q, register_4_q, register_5_q;

  // Probe on 4'b0011
  // Probe on 4'b0101
  Multiplexer #(.width(4), .enable("false")) multiplexer_1 (
    .in0(4'b0011), .in1(4'b0101), .out(multiplexer_1_out), .sel(nRead_Write));
  or or_1 (or_1_out, Idle, Update_Mem);
  or or_2 (or_2_out, ~Chip_Select, Reset);  // OR_Gate
  Subtractor #(.width(4)) subtractor_1 (.a(multiplexer_1_out), .b(4'b0010), .out(subtractor_1_out));  // open: bin, bout
  D_Flip_Flop u_Idle (.clk(CLK), .D(or_1_out), .Q(Idle_q), .preset(or_2_out));  // open: Qn, en, reset
  Demultiplexer #(.enable("false")) demultiplexer_1 (.out0(Idle), .out1(Load0), .in(Idle_q), .sel(Changed));
  // Probe on counter_1_q
  Counter #(.width(4), .max('hf)) counter_1 (
    .load(Load), .D(subtractor_1_out), .count(Count), .Q(counter_1_q), .clk(CLK), .clr(or_3_out));  // open: carry
  or or_3 (or_3_out, ~Chip_Select, Reset);  // OR_Gate
  Comparator #(.width(4), .mode("unsigned")) comparator_1 (
    .a(4'b0000), .b(counter_1_q), .eq(Zero_Time));  // open: gt, lt
  or or_4 (or_4_out, Count, Load0, Load1);
  Register #(.width(32)) register_1 (.D(Data_In_0), .en(Chip_Select), .Q(register_1_q), .clk(CLK), .clr(or_5_out));
  or or_5 (or_5_out, ~Chip_Select, Reset);  // OR_Gate
  Register #(.width(32)) register_2 (.D(Data_In_1), .en(Chip_Select), .Q(register_2_q), .clk(CLK), .clr(or_6_out));
  or or_6 (or_6_out, ~Chip_Select, Reset);  // OR_Gate
  Register #(.width(32)) register_3 (.D(Data_In_2), .en(Chip_Select), .Q(register_3_q), .clk(CLK), .clr(or_7_out));
  or or_7 (or_7_out, ~Chip_Select, Reset);  // OR_Gate
  Register #(.width(32)) register_4 (.D(Data_In_3), .en(Chip_Select), .Q(register_4_q), .clk(CLK), .clr(or_8_out));
  or or_8 (or_8_out, ~Chip_Select, Reset);  // OR_Gate
  Register #(.width(32)) register_5 (
    .D({{11{1'b1}}, nRead_Write, Mask, Address}), .en(Chip_Select), .Q(register_5_q), .clk(CLK),
    .clr(or_9_out));
  or or_9 (or_9_out, ~Chip_Select, Reset);  // OR_Gate
  D_Flip_Flop Proc (.clk(CLK), .D(or_4_out), .Q(Proc_q), .reset(or_10_out));  // open: Qn, preset, en
  or or_10 (or_10_out, ~Chip_Select, Reset);  // OR_Gate
  Demultiplexer #(.enable("false")) demultiplexer_2 (
    .out0(Count), .out1(Update_Mem), .in(demultiplexer_3_out0), .sel(Zero_Time));
  Demultiplexer #(.enable("false")) demultiplexer_3 (
    .out0(demultiplexer_3_out0), .out1(Load1), .in(Proc_q), .sel(Changed));
  Clock clock_1 (.out(CLK));
  Comparator #(.width(32)) comparator_2 (.a(register_1_q), .b(Data_In_0), .eq(comparator_2_eq));  // open: gt, lt
  Comparator #(.width(32)) comparator_3 (.a(register_2_q), .b(Data_In_1), .eq(comparator_3_eq));  // open: gt, lt
  Comparator #(.width(32)) comparator_4 (.a(register_3_q), .b(Data_In_2), .eq(comparator_4_eq));  // open: gt, lt
  Comparator #(.width(32)) comparator_5 (.a(register_4_q), .b(Data_In_3), .eq(comparator_5_eq));  // open: gt, lt
  Comparator #(.width(32)) comparator_6 (
    .a(register_5_q), .b({{11{1'b1}}, nRead_Write, Mask, Address}), .eq(comparator_6_eq));  // open: gt, lt
  nand nand_1 (nand_1_out, comparator_6_eq, comparator_2_eq, comparator_3_eq, comparator_4_eq, comparator_5_eq);
  and and_1 (Changed, nand_1_out, Chip_Select);
  or or_11 (Load, Count, Load1, Load0);
  and and_2 (and_2_out, Mask[0], Update_Mem, nRead_Write);
  and and_3 (and_3_out, Mask[1], Update_Mem, nRead_Write);
  and and_4 (and_4_out, Mask[2], Update_Mem, nRead_Write);
  and and_5 (and_5_out, Mask[3], Update_Mem, nRead_Write);
  RAM_part #(.addrWidth(16), .dataWidth(32), .bus("separate")) ram_1 (
    .addr(Address), .din(Data_In_0), .data(Data_Out_0), .str(and_2_out), .sel(Chip_Select), .clk(CLK),
    .ld(and_6_out), .clr(Reset));
  and and_6 (and_6_out, ~nRead_Write, Idle);  // AND_Gate
  RAM_part #(.addrWidth(16), .dataWidth(32), .bus("separate")) ram_2 (
    .addr(Address), .din(Data_In_1), .data(Data_Out_1), .str(and_3_out), .sel(Chip_Select), .clk(CLK),
    .ld(and_7_out), .clr(Reset));
  and and_7 (and_7_out, ~nRead_Write, Idle);  // AND_Gate
  RAM_part #(.addrWidth(16), .dataWidth(32), .bus("separate")) ram_3 (
    .addr(Address), .din(Data_In_2), .data(Data_Out_2), .str(and_4_out), .sel(Chip_Select), .clk(CLK),
    .ld(and_8_out), .clr(Reset));
  and and_8 (and_8_out, ~nRead_Write, Idle);  // AND_Gate
  RAM_part #(.addrWidth(16), .dataWidth(32), .bus("separate")) ram_4 (
    .addr(Address), .din(Data_In_3), .data(Data_Out_3), .str(and_5_out), .sel(Chip_Select), .clk(CLK),
    .ld(and_9_out), .clr(Reset));
  and and_9 (and_9_out, ~nRead_Write, Idle);  // AND_Gate

  assign Read_Time = 4'b0011;
  assign Write_Time = 4'b0101;

  // Other names for the same wires on the sheet: M0 = Mask[0]; M1 = Mask[1]; M2 = Mask[2]; M3 = Mask[3];
  //   RW = nRead_Write; CLR = Reset; CS = Chip_Select; Load2 = Count

  // Notes on the sheet:
  //   NO MODIFICAR
  //   excepto quizás los valores RT y WT
  //   BANK0
  //   BANK1
  //   BANK2
  //   BANK3
endmodule

module S_MIPS (
  input  Kbd_Available,
  input  [6:0] Kbd_ASCII_Data,
  input  [31:0] RAM_Out_0,
  input  [31:0] RAM_Out_1,
  input  Reset,
  input  [31:0] RAM_Out_2,
  input  Clock,
  input  [31:0] RAM_Out_3,
  input  [3:0] Read_Time,
  input  [3:0] Write_Time,
  output Kbd_Enable,
  output [15:0] Address,
  output Kbd_Clear,
  output TTY_Enable,
  output [6:0] TTY_ASCII_Data,
  output Stop,
  output [31:0] RAM_In_0,
  output [31:0] RAM_In_1,
  output [31:0] RAM_In_2,
  output [31:0] RAM_In_3,
  output [3:0] Mask,
  output nRead_Write,
  output Chip_Select
);

  wire _0, add, addi, alu, ALU_B_sel, \and , and_1_out, andi, beq, bgtz, blez, bltz, bne, CLK, CS_1, CS_2,
       div, divu, enInst, enRead, enRND, enSP, enWrite, halt, InstEnab, j, jr, kbd, lw, mem, mfhi, mflo,
       minus_1, mul, mulu, Next, NextInst, nop, \nor , o_beq, o_bgtz, o_blez, o_bltz, o_bne, o_j, o_jr, \or ,
       or_1_out, or_2_out, or_3_out, or_4_out, or_9_out, or_16_out, ori, pop, pop_RF, push, push_RF, R_W, RD,
       Ready, ready_1, ready_2, ready_Mem, readyR, readyW, rnd_t, Sign, slt, slt_sol, slti, sltiu, sltu, sub,
       sw, tty, tunnel, \xor , xori, Zero, ZF;
  wire [2:0] OpCode, SelData;
  wire [4:0] multiplexer_5_out, SelRd, SelRs, SelRt;
  wire [15:0] InstAddr, MemAddr;
  wire [25:0] Dest;
  wire [31:0] adder_1_out, CACHE_INST_OUTPUT_0, CACHE_INST_OUTPUT_1, CACHE_INST_OUTPUT_2,
       CACHE_INST_OUTPUT_3, Cte, Data, Dir, Hi, instruction_fetch_1_out_9, KBD_Data_end, Lo, MemData,
       multiplexer_2_out, multiplexer_3_out, PC_in, PC_out, Res, RND, Rt, slt_res_end, SP, Value;
  wire [31:7] Rs;

  and and_1 (and_1_out, enRead, ~ready_2);  // AND_Gate
  or or_1 (or_1_out, enWrite, push_RF);
  Adder #(.width(32)) adder_1 (.a({Rs, TTY_ASCII_Data}), .b(Cte), .out(adder_1_out));  // open: cin, cout
  or or_2 (or_2_out, enInst, Reset);
  or or_3 (or_3_out, and_1_out, or_1_out);
  Multiplexer #(.width(32), .enable("false")) multiplexer_1 (.in0(adder_1_out), .in1(SP), .out(Dir), .sel(or_4_out));
  or or_4 (or_4_out, push, pop);
  CacheInst cacheinst_1 (
    .in_1(InstEnab), .in_2(Reset), .in_3(CLK), .RAM_Out_0(RAM_Out_0), .CacheOut0(CACHE_INST_OUTPUT_0),
    .RAM_Out_1(RAM_Out_1), .CacheOut1(CACHE_INST_OUTPUT_1), .RAM_Out_2(RAM_Out_2),
    .CacheOut2(CACHE_INST_OUTPUT_2), .RAM_Out_3(RAM_Out_3), .CacheOut3(CACHE_INST_OUTPUT_3),
    .Address(PC_out), .AddressOut(InstAddr), .ReadTime(Read_Time), .Finish(Ready), .out_16(CS_1));
  and and_2 (InstEnab, or_2_out, ~or_3_out);  // AND_Gate
  and and_3 (CLK, Clock, ~Stop);  // AND_Gate
  Multiplexer #(.width(32), .enable("false")) multiplexer_2 (
    .in0(Rt), .in1(Cte), .out(multiplexer_2_out), .sel(ALU_B_sel));
  or or_5 (Zero, blez, bgtz, bltz);
  or or_6 (ALU_B_sel, andi, addi, slti, sltiu, xori, ori);
  Multiplexer #(.width(32), .enable("false")) multiplexer_3 (
    .in0(multiplexer_2_out), .in1({32{1'b0}}), .out(multiplexer_3_out), .sel(Zero));
  or or_7 (Chip_Select, CS_1, CS_1);
  ALU alu_1 (
    .in_1({Rs, TTY_ASCII_Data}), .in_2(multiplexer_3_out), .CLK(CLK), .RST(Reset), .Sign(Sign), .Op(OpCode),
    .out_7(Res), .out_8(Hi), .out_9(Lo), .out_10(ZF), .out_11(_0), .out_12(slt_sol), .out_13(tunnel));
  Instruction_Fetch instruction_fetch_1 (
    .in_1(CLK), .in_2(Reset), .in_3(Ready), .in_4(PC_out), .in_5(CACHE_INST_OUTPUT_0),
    .in_6(CACHE_INST_OUTPUT_1), .in_7(CACHE_INST_OUTPUT_2), .in_8(CACHE_INST_OUTPUT_3),
    .out_9(instruction_fetch_1_out_9), .out_10(ready_1));
  // Probe on Res
  Multiplexer #(.width(16), .enable("false")) multiplexer_4 (.in0(MemAddr), .in1(InstAddr), .out(Address), .sel(CS_1));
  or or_8 (alu, div, andi, addi, add, sub, mul, mulu, divu, \and , \or , \nor , ori, xori, \xor );
  // Probe on instruction_fetch_1_out_9
  ReadMem readmem_1 (
    .in_1(CLK), .in_2(Reset), .in_3(readyR), .in_4(Dir), .in_5(RAM_In_0), .in_6(RAM_In_1), .in_7(RAM_In_2),
    .in_8(RAM_In_3), .out_9(MemData), .out_10(ready_2));
  or or_9 (or_9_out, enRead, enWrite);
  assign slt_res_end = {{31{1'b0}}, slt_sol};  // Bit_Extender bit_extender_1
  assign KBD_Data_end = {{25{1'b0}}, Kbd_ASCII_Data};  // Bit_Extender bit_extender_2
  // Probe on multiplexer_5_out
  CacheData cachedata_1 (
    .Address(Dir), .in_2(or_9_out), .in_3(Reset), .in_4(CLK), .in_5(enWrite), .RAM_Out_0(RAM_Out_0),
    .RAM_Out_1(RAM_Out_1), .RAM_Out_2(RAM_Out_2), .RAM_Out_3(RAM_Out_3), .Value(Value), .ReadTime(Read_Time),
    .WriteTime(Write_Time), .AddressOut(MemAddr), .CacheOut0(RAM_In_0), .CacheOut1(RAM_In_1),
    .CacheOut2(RAM_In_2), .CacheOut3(RAM_In_3), .CS(CS_2), .FinishRead(readyR), .RAM_R_W(nRead_Write),
    .FinishWrt(readyW), .Mask(Mask));
  and and_4 (minus_1, ~Kbd_Available, kbd);  // AND_Gate
  or or_10 (mem, pop, lw);
  ID id_1 (
    .Instruction(instruction_fetch_1_out_9), .Dest(Dest), .out_6(pop), .out_7(mfhi), .out_8(\and ),
    .out_9(sltu), .out_10(push), .out_11(mflo), .out_12(\or ), .out_13(kbd), .out_14(jr), .out_15(sub),
    .out_16(tty), .out_17(mulu), .out_18(\nor ), .out_19(rnd_t), .out_20(div), .out_21(\xor ), .out_22(halt),
    .out_23(divu), .out_24(slt), .\const (Cte), .out_40(SelRs), .out_25(addi), .out_35(sw), .out_38(j),
    .out_41(SelRd), .add(add), .out_42(SelRt), .out_26(slti), .out_36(beq), .mul(mul), .out_27(sltiu),
    .out_37(bne), .nop(nop), .out_28(andi), .out_32(blez), .out_29(ori), .out_33(bgtz), .out_30(xori),
    .out_34(bltz), .out_31(lw));
  // Probe on Data
  Multiplexer #(.width(5), .enable("false")) multiplexer_5 (
    .in0(SelRt), .in1(SelRd), .out(multiplexer_5_out), .sel(RD));
  // Probe on SelRt
  Multiplexer #(.width(32), .enable("false")) multiplexer_6 (
    .in0(Rt), .in1({Rs, TTY_ASCII_Data}), .out(Value), .sel(push));
  RF rf_1 (
    .out_11({Rs, TTY_ASCII_Data}), .out_12(Rt), .Data(Data), .dir_dest(multiplexer_5_out), .dir_a(SelRs),
    .dir_b(SelRt), .CLK(CLK), .R_W(R_W), .out_13(SP), .in_8(enSP), .in_9(push_RF), .in_10(pop_RF), .RST(Reset));
  or or_11 (SelData[1], kbd, minus_1, alu, mfhi);
  or or_12 (SelData[2], mflo, kbd, mem, minus_1);
  // Probe on {Rs, TTY_ASCII_Data}
  or or_13 (ready_Mem, readyW, ready_2);
  or or_14 (SelData[0], mfhi, rnd_t, mem, minus_1);
  // Probe on Rt
  or or_15 (NextInst, Next, ready_Mem);
  and and_5 (RD, or_16_out, ~ALU_B_sel);  // AND_Gate
  multiplexer_3x8 multiplexer_3x8_1 (
    .in_1(slt_res_end), .in_2(RND), .in_3(Res), .in_4(Hi), .in_5(Lo), .in_6(MemData), .in_7(KBD_Data_end),
    .in_8(SelData), .in_9({32{1'b1}}), .out_10(Data));
  or or_16 (or_16_out, sltu, pop, kbd, mflo, alu, rnd_t, mfhi, slt);
  PC pc_1 (.RST(Reset), .CLK(CLK), .En(NextInst), .PC_Inp(PC_in), .out_5(PC_out));
  Branch_Control branch_control_1 (
    .in_1(o_beq), .in_2(o_bne), .in_3(ZF), .in_4(tunnel), .in_5(o_blez), .in_6(o_bgtz), .in_7(_0),
    .in_8(o_bltz), .in_9(o_j), .in_10(o_jr), .in_11(CLK), .in_12(NextInst), .in_13(Dest),
    .in_14({Rs, TTY_ASCII_Data}), .in_15(Cte), .in_16(PC_out), .PC_Out(PC_in));
  Random random_1 (.CLK(CLK), .En(enRND), .out_3(RND));
  Control_Unit control_unit_1 (
    .nop(nop), .divu(divu), .pop(pop), .halt(halt), .andi(andi), .sw(sw), .ready_mem(ready_Mem), .Next(Next),
    .ready_inst(ready_1), .add(add), .\and (\and ), .slt(slt), .kbd(kbd), .ori(ori), .beq(beq),
    .OpCode(OpCode), .CLK(CLK), .sub(sub), .\or (\or ), .sltu(sltu), .rnd(rnd_t), .xori(xori), .bne(bne),
    .Sign(Sign), .mul(mul), .\nor (\nor ), .jr(jr), .tty(tty), .slti(slti), .blez(blez), .beq_2(o_beq),
    .bne_2(o_bne), .mulu(mulu), .\xor (\xor ), .mfhi(mfhi), .j(j), .sltiu(sltiu), .bgtz(bgtz),
    .blez_2(o_blez), .bgtz_2(o_bgtz), .div(div), .push(push), .mflo(mflo), .addi(addi), .lw(lw), .bltz(bltz),
    .bltz_2(o_bltz), .j_2(o_j), .jr_2(o_jr), .enRND(enRND), .STOP(Stop), .enRead(enRead), .enWrite(enWrite),
    .pushRF(push_RF), .popRF(pop_RF), .enSP(enSP), .R_W(R_W), .InstEnab(enInst), .TTYEnab(TTY_Enable),
    .KBDEnab(Kbd_Enable));
  // Probe on PC_out
  // Probe on {Rs, TTY_ASCII_Data}
  // Probe on OpCode

  assign Kbd_Clear = Reset;

  // Other names for the same wires on the sheet: CS = Chip_Select; KBD_AVAIL = Kbd_Available; CLR = Reset;
  //   KBD_CLR = Reset; KBD_DATA[6:0] = Kbd_ASCII_Data; RAM_A[15:0] = Address; CACHE_OUTPUT_0[31:0] = RAM_In_0;
  //   RAM_INPUT_0[31:0] = RAM_In_0; CACHE_OUTPUT_1[31:0] = RAM_In_1; RAM_INPUT_1[31:0] = RAM_In_1;
  //   CACHE_OUTPUT_2[31:0] = RAM_In_2; RAM_INPUT_2[31:0] = RAM_In_2; CACHE_OUTPUT_3[31:0] = RAM_In_3;
  //   RAM_INPUT_3[31:0] = RAM_In_3; RAM_MASK[3:0] = Mask; RAM_OUTPUT_0[31:0] = RAM_Out_0;
  //   RAM_OUTPUT_1[31:0] = RAM_Out_1; RAM_OUTPUT_2[31:0] = RAM_Out_2; RAM_OUTPUT_3[31:0] = RAM_Out_3;
  //   Rs[6:0] = TTY_ASCII_Data; TTY_DATA[6:0] = TTY_ASCII_Data; RW = nRead_Write

  // Notes on the sheet:
  //   RAM ADDRESS
  //   DATA FROM RAM
  //   DATA TO RAM
  //   DATA WRITE MASK
  //   RAM TIMING
  //   RAM CONTROL
  //   KEYBOARD
  //   TTY
  //   SEQUENCING
endmodule

module Control_Unit (
  input  nop,
  input  divu,
  input  pop,
  input  halt,
  input  andi,
  input  sw,
  input  ready_mem,
  input  ready_inst,
  input  add,
  input  \and ,
  input  slt,
  input  kbd,
  input  ori,
  input  beq,
  input  CLK,
  input  sub,
  input  \or ,
  input  sltu,
  input  rnd,
  input  xori,
  input  bne,
  input  mul,
  input  \nor ,
  input  jr,
  input  tty,
  input  slti,
  input  blez,
  input  mulu,
  input  \xor ,
  input  mfhi,
  input  j,
  input  sltiu,
  input  bgtz,
  input  div,
  input  push,
  input  mflo,
  input  addi,
  input  lw,
  input  bltz,
  output Next,
  output [2:0] OpCode,
  output Sign,
  output beq_2,
  output bne_2,
  output blez_2,
  output bgtz_2,
  output bltz_2,
  output j_2,
  output jr_2,
  output enRND,
  output STOP,
  output enRead,
  output enWrite,
  output pushRF,
  output popRF,
  output enSP,
  output R_W,
  output InstEnab,
  output TTYEnab,
  output KBDEnab
);

  wire _0, _0_t, _0_t_t, _0_t_t_t, _0_t_t_t_t, _0_t_t_t_t_t, _0_t_t_t_t_t_t, _1, _1_t, _1_t_t, _1_t_t_t,
       _1_t_t_t_t, _1_t_t_t_t_t, _1_t_t_t_t_t_t, _2, _2_t, _3, _4, and_37_out, d_ff_2_q, d_ff_2_qn,
       demultiplexer_1_out0, En, En_8, EnRead_0, EnRead_1, EnWrt_0, EnWrt_1, j_end, jr_end, mfhi_end,
       mflo_end, NextInstruction, nop_end, or_1_out, or_2_out, R_W_14, R_W_15, R_W_16, R_W_17, R_W_22, Sel,
       tunnel_t, tunnel_t_t, tunnel_t_t_t, tunnel_t_t_t_t, tunnel_t_t_t_t_t, tunnel_t_t_t_t_t_t,
       tunnel_t_t_t_t_t_t_t;
  wire [2:0] priority_encoder_1_out;

  and and_1 (_0_t_t, NextInstruction, add);
  and and_2 (_0_t_t_t, NextInstruction, sub);
  and and_3 (_0_t, NextInstruction, mul);
  and and_4 (_1_t, NextInstruction, mulu);
  and and_5 (_0_t_t_t_t, NextInstruction, div);
  and and_6 (_1_t_t_t_t, NextInstruction, divu);
  and and_7 (_0, NextInstruction, \and );
  and and_8 (_0_t_t_t_t_t_t, NextInstruction, \or );
  and and_9 (En_8, NextInstruction, \nor );
  and and_10 (_0_t_t_t_t_t, NextInstruction, \xor );
  and and_11 (_1_t_t, NextInstruction, addi);
  and and_12 (_1, NextInstruction, andi);
  and and_13 (_1_t_t_t_t_t_t, NextInstruction, ori);
  and and_14 (_1_t_t_t_t_t, NextInstruction, xori);
  and and_15 (R_W_14, NextInstruction, slt);
  and and_16 (R_W_15, NextInstruction, sltu);
  and and_17 (R_W_16, NextInstruction, slti);
  and and_18 (R_W_17, NextInstruction, sltiu);
  and and_19 (jr_end, NextInstruction, jr);
  and and_20 (_1_t_t_t, NextInstruction, beq);
  and and_21 (_2_t, NextInstruction, bne);
  and and_22 (_2, NextInstruction, blez);
  and and_23 (_3, NextInstruction, bgtz);
  and and_24 (_4, NextInstruction, bltz);
  and and_25 (mfhi_end, NextInstruction, mfhi);
  and and_26 (mflo_end, NextInstruction, mflo);
  and and_27 (enRND, NextInstruction, rnd);
  and and_28 (STOP, NextInstruction, halt);
  and and_29 (EnRead_0, NextInstruction, pop);
  and and_30 (pushRF, NextInstruction, push);
  and and_31 (EnRead_1, NextInstruction, lw);
  and and_32 (EnWrt_1, NextInstruction, sw);
  and and_33 (nop_end, NextInstruction, nop);
  and and_34 (j_end, NextInstruction, j);
  and and_35 (TTYEnab, NextInstruction, tty);
  and and_36 (KBDEnab, NextInstruction, kbd);
  D_Flip_Flop d_ff_1 (.clk(CLK), .D(and_37_out), .Q(EnWrt_0));  // open: Qn, preset, en, reset
  and and_37 (and_37_out, ~EnWrt_0, pushRF);  // AND_Gate
  or or_1 (or_1_out, demultiplexer_1_out0, Next);
  and and_38 (popRF, ready_mem, pop);
  and and_39 (R_W_22, lw, ready_mem);
  Demultiplexer #(.enable("false")) demultiplexer_1 (
    .out0(demultiplexer_1_out0), .out1(InstEnab), .in(d_ff_2_q), .sel(or_2_out));
  D_Flip_Flop d_ff_2 (.clk(CLK), .D(or_1_out), .Q(d_ff_2_q), .Qn(d_ff_2_qn), .preset(d_ff_2_qn));  // open: en, reset
  or or_2 (or_2_out, ready_inst, ready_mem);
  or or_3 (Sign, _0_t, _0_t_t_t_t, R_W_14, R_W_16, _1_t_t_t, _2_t, _2, _3, _4);
  or or_4 (enRead, EnRead_0, EnRead_1);
  or or_5 (enWrite, EnWrt_0, EnWrt_1);
  or or_6 (En, _0_t_t, _0_t_t_t, _0_t, _1_t, _0_t_t_t_t, _1_t_t_t_t, _0, _0_t_t_t_t_t_t, En_8, _0_t_t_t_t_t, _1_t_t, _1, _1_t_t_t_t_t_t, _1_t_t_t_t_t, _1_t_t_t, _2_t, _2, _3, _4);
  or or_7 (R_W, _0_t_t, _0_t_t_t, _0_t, _1_t, _0_t_t_t_t, _1_t_t_t_t, _0, _0_t_t_t_t_t_t, En_8, _0_t_t_t_t_t, _1_t_t, _1, _1_t_t_t_t_t_t, _1_t_t_t_t_t, R_W_14, R_W_15, R_W_16, R_W_17, jr_end, mfhi_end, mflo_end, popRF, R_W_22, KBDEnab);
  and and_40 (NextInstruction, InstEnab, ~ready_mem);  // AND_Gate
  or or_8 (tunnel_t_t_t, _0_t_t, _1_t_t, _2, _3, _4);
  or or_9 (tunnel_t_t_t_t, _0_t_t_t, _1_t_t_t, _2_t);
  or or_10 (tunnel_t_t, _0_t, _1_t);
  or or_11 (tunnel_t_t_t_t_t, _0_t_t_t_t, _1_t_t_t_t);
  or or_12 (tunnel_t, _0, _1);
  or or_13 (tunnel_t_t_t_t_t_t_t, _0_t_t_t_t_t_t, _1_t_t_t_t_t_t);
  or or_14 (tunnel_t_t_t_t_t_t, _0_t_t_t_t_t, _1_t_t_t_t_t);
  or or_15 (enSP, popRF, pushRF);
  nor nor_1 (Sel, tunnel_t_t_t, tunnel_t_t_t_t, tunnel_t, En_8, tunnel_t_t_t_t_t_t_t, tunnel_t_t_t_t_t_t, tunnel_t_t, tunnel_t_t_t_t_t);
  or or_16 (Next, mflo_end, nop_end, _0_t_t, _0_t_t_t, _0_t, _1_t, _0_t_t_t_t, _1_t_t_t_t, _0, _0_t_t_t_t_t_t, En_8, _0_t_t_t_t_t, _1_t_t, _1, _1_t_t_t_t_t_t, _1_t_t_t_t_t, R_W_14, R_W_15, R_W_16, R_W_17, jr_end, j_end, _1_t_t_t, _2_t, _2, _3, _4, STOP, enRND, mfhi_end, KBDEnab, TTYEnab);
  Priority_Encoder priority_encoder_1 (
    .in0(tunnel_t_t_t), .in1(tunnel_t_t_t_t), .in2(tunnel_t), .in3(En_8), .in4(tunnel_t_t_t_t_t_t_t),
    .in5(tunnel_t_t_t_t_t_t), .in6(tunnel_t_t), .in7(tunnel_t_t_t_t_t), .out(priority_encoder_1_out),
    .en_in(En));  // open: gs, en_out
  Multiplexer #(.width(3), .enable("false")) multiplexer_1 (
    .in0(priority_encoder_1_out), .in1(3'b000), .out(OpCode), .sel(Sel));

  assign beq_2 = beq;
  assign bgtz_2 = bgtz;
  assign blez_2 = blez;
  assign bltz_2 = bltz;
  assign bne_2 = bne;
  assign j_2 = j;
  assign jr_2 = jr;

  // Other names for the same wires on the sheet: En_7 = _0_t_t_t_t_t_t; or_end = _0_t_t_t_t_t_t;
  //   R_W_7 = _0_t_t_t_t_t_t; En_12 = _1_t_t_t_t_t_t; ori_end = _1_t_t_t_t_t_t; R_W_12 = _1_t_t_t_t_t_t;
  //   add_end = _0_t_t; En_0 = _0_t_t; R_W_0 = _0_t_t; addi_end = _1_t_t; En_10 = _1_t_t; R_W_10 = _1_t_t;
  //   and_end = _0; En_6 = _0; R_W_6 = _0; andi_end = _1; En_11 = _1; R_W_11 = _1; beq_end = _1_t_t_t;
  //   En_14 = _1_t_t_t; Sign_4 = _1_t_t_t; bgtz_end = _3; En_17 = _3; Sign_7 = _3; blez_end = _2; En_16 = _2;
  //   Sign_6 = _2; bltz_end = _4; En_18 = _4; Sign_8 = _4; bne_end = _2_t; En_15 = _2_t; Sign_5 = _2_t;
  //   div_end = _0_t_t_t_t; En_4 = _0_t_t_t_t; R_W_4 = _0_t_t_t_t; Sign_1 = _0_t_t_t_t; divu_end = _1_t_t_t_t;
  //   En_5 = _1_t_t_t_t; R_W_5 = _1_t_t_t_t; enSP_0 = popRF; R_W_21 = popRF; enSP_1 = pushRF; EnWrt = enWrite;
  //   halt_end = STOP; R_W_18 = jr_end; kbd_enab = KBDEnab; kbd_end = KBDEnab; R_W_23 = KBDEnab; lw_end = EnRead_1;
  //   mem_ready = ready_mem; R_W_19 = mfhi_end; R_W_20 = mflo_end; En_2 = _0_t; mul_end = _0_t; R_W_2 = _0_t;
  //   Sign_0 = _0_t; En_3 = _1_t; mulu_end = _1_t; R_W_3 = _1_t; nor_end = En_8; R_W_8 = En_8; tunnel = En_8;
  //   pop_end = EnRead_0; push_end = EnWrt_0; rnd_end = enRND; Sign_2 = R_W_14; slt_end = R_W_14; Sign_3 = R_W_16;
  //   slti_end = R_W_16; sltiu_end = R_W_17; sltu_end = R_W_15; En_1 = _0_t_t_t; R_W_1 = _0_t_t_t; sub_end = _0_t_t_t;
  //   sw_end = EnWrt_1; time_ready = ready_inst; tty_enab = TTYEnab; tty_end = TTYEnab; En_9 = _0_t_t_t_t_t;
  //   R_W_9 = _0_t_t_t_t_t; xor_end = _0_t_t_t_t_t; En_13 = _1_t_t_t_t_t; R_W_13 = _1_t_t_t_t_t;
  //   xori_end = _1_t_t_t_t_t
endmodule

module multiplexer (
  input  [31:0] in_1,
  input  [31:0] in_2,
  input  [31:0] in_3,
  input  [31:0] in_4,
  input  [31:0] in_5,
  input  [31:0] in_6,
  input  [31:0] in_7,
  input  [31:0] in_8,
  input  [31:0] in_9,
  input  [31:0] in_10,
  input  [31:0] in_11,
  input  [31:0] in_12,
  input  [31:0] in_13,
  input  [31:0] in_14,
  input  [31:0] in_15,
  input  [31:0] in_16,
  input  [31:0] in_17,
  input  [31:0] in_18,
  input  [31:0] in_19,
  input  [31:0] in_20,
  input  [31:0] in_21,
  input  [31:0] in_22,
  input  [31:0] in_23,
  input  [31:0] in_24,
  input  [31:0] in_25,
  input  [31:0] in_26,
  input  [31:0] in_27,
  input  [31:0] in_28,
  input  [4:0] in_29,
  input  [31:0] in_30,
  input  [31:0] in_31,
  input  [31:0] in_32,
  input  [31:0] in_33,
  output [31:0] out_34
);

  wire a00, a01, a02, a03, a04, a05, a06, a07, a08, a09, a10, a11, a12, a13, a14, a15, a16, a17, a18, a19,
       a20, a21, a22, a23, a24, a25, a26, a27, a28, a29, a30, a31;

  assign out_34 = a00 ? in_1 : 32'bz;  // Controlled_Buffer controlled_buffer_1
  assign out_34 = a01 ? in_5 : 32'bz;  // Controlled_Buffer controlled_buffer_2
  assign out_34 = a02 ? in_9 : 32'bz;  // Controlled_Buffer controlled_buffer_3
  assign out_34 = a03 ? in_13 : 32'bz;  // Controlled_Buffer controlled_buffer_4
  assign out_34 = a04 ? in_17 : 32'bz;  // Controlled_Buffer controlled_buffer_5
  assign out_34 = a05 ? in_21 : 32'bz;  // Controlled_Buffer controlled_buffer_6
  assign out_34 = a06 ? in_25 : 32'bz;  // Controlled_Buffer controlled_buffer_7
  assign out_34 = a07 ? in_30 : 32'bz;  // Controlled_Buffer controlled_buffer_8
  assign out_34 = a08 ? in_2 : 32'bz;  // Controlled_Buffer controlled_buffer_9
  assign out_34 = a09 ? in_6 : 32'bz;  // Controlled_Buffer controlled_buffer_10
  assign out_34 = a10 ? in_10 : 32'bz;  // Controlled_Buffer controlled_buffer_11
  assign out_34 = a11 ? in_14 : 32'bz;  // Controlled_Buffer controlled_buffer_12
  assign out_34 = a12 ? in_18 : 32'bz;  // Controlled_Buffer controlled_buffer_13
  assign out_34 = a13 ? in_22 : 32'bz;  // Controlled_Buffer controlled_buffer_14
  assign out_34 = a14 ? in_26 : 32'bz;  // Controlled_Buffer controlled_buffer_15
  assign out_34 = a15 ? in_31 : 32'bz;  // Controlled_Buffer controlled_buffer_16
  assign out_34 = a16 ? in_3 : 32'bz;  // Controlled_Buffer controlled_buffer_17
  assign out_34 = a17 ? in_7 : 32'bz;  // Controlled_Buffer controlled_buffer_18
  assign out_34 = a18 ? in_11 : 32'bz;  // Controlled_Buffer controlled_buffer_19
  assign out_34 = a19 ? in_15 : 32'bz;  // Controlled_Buffer controlled_buffer_20
  assign out_34 = a20 ? in_19 : 32'bz;  // Controlled_Buffer controlled_buffer_21
  assign out_34 = a21 ? in_23 : 32'bz;  // Controlled_Buffer controlled_buffer_22
  assign out_34 = a22 ? in_27 : 32'bz;  // Controlled_Buffer controlled_buffer_23
  assign out_34 = a23 ? in_32 : 32'bz;  // Controlled_Buffer controlled_buffer_24
  assign out_34 = a24 ? in_4 : 32'bz;  // Controlled_Buffer controlled_buffer_25
  assign out_34 = a25 ? in_8 : 32'bz;  // Controlled_Buffer controlled_buffer_26
  assign out_34 = a26 ? in_12 : 32'bz;  // Controlled_Buffer controlled_buffer_27
  assign out_34 = a27 ? in_16 : 32'bz;  // Controlled_Buffer controlled_buffer_28
  assign out_34 = a28 ? in_20 : 32'bz;  // Controlled_Buffer controlled_buffer_29
  assign out_34 = a29 ? in_24 : 32'bz;  // Controlled_Buffer controlled_buffer_30
  assign out_34 = a30 ? in_28 : 32'bz;  // Controlled_Buffer controlled_buffer_31
  assign out_34 = a31 ? in_33 : 32'bz;  // Controlled_Buffer controlled_buffer_32
  Decoder #(.select(5)) decoder_1 (
    .out0(a00), .out1(a01), .out2(a02), .out3(a03), .out4(a04), .out5(a05), .out6(a06), .out7(a07),
    .out8(a08), .out9(a09), .out10(a10), .out11(a11), .out12(a12), .out13(a13), .out14(a14), .out15(a15),
    .out16(a16), .out17(a17), .out18(a18), .out19(a19), .out20(a20), .out21(a21), .out22(a22), .out23(a23),
    .out24(a24), .out25(a25), .out26(a26), .out27(a27), .out28(a28), .out29(a29), .out30(a30), .out31(a31),
    .sel(in_29));  // open: en

  // Other names for the same wires on the sheet: out[31:0] = out_34
endmodule

module RF (
  input  [31:0] Data,
  input  CLK,
  input  R_W,
  input  RST,
  input  [4:0] dir_dest,
  input  [4:0] dir_a,
  input  [4:0] dir_b,
  input  in_8,
  input  in_9,
  input  in_10,
  output [31:0] out_11,
  output [31:0] out_12,
  output [31:0] out_13
);

  wire and_1_out, and_2_out, and_3_out, and_4_out, and_5_out, and_6_out, and_7_out, and_8_out, and_9_out,
       and_10_out, and_11_out, and_12_out, and_13_out, and_14_out, and_15_out, and_16_out, and_17_out,
       and_18_out, and_19_out, and_20_out, and_21_out, and_22_out, and_23_out, and_24_out, and_25_out,
       and_26_out, and_27_out, and_28_out, and_29_out, and_30_out, and_31_out, decoder_1_out0,
       decoder_1_out1, decoder_1_out2, decoder_1_out3, decoder_1_out4, decoder_1_out5, decoder_1_out6,
       decoder_1_out7, decoder_1_out8, decoder_1_out9, decoder_1_out10, decoder_1_out11, decoder_1_out12,
       decoder_1_out13, decoder_1_out14, decoder_1_out15, decoder_1_out16, decoder_1_out17, decoder_1_out18,
       decoder_1_out19, decoder_1_out20, decoder_1_out21, decoder_1_out22, decoder_1_out23, decoder_1_out24,
       decoder_1_out25, decoder_1_out26, decoder_1_out27, decoder_1_out28, decoder_1_out29, decoder_1_out30,
       EnSp, mod, SP_sel;
  wire [31:0] adder_1_out, multiplexer_1_out, register_1_q, register_2_q, register_3_q, register_4_q,
       register_5_q, register_6_q, register_7_q, register_8_q, register_9_q, register_10_q, register_11_q,
       register_12_q, register_13_q, register_14_q, register_15_q, register_16_q, register_17_q,
       register_18_q, register_19_q, register_20_q, register_21_q, register_22_q, register_23_q,
       register_24_q, register_25_q, register_26_q, register_27_q, register_28_q, register_29_q,
       register_30_q, register_31_q, SP_load, subtractor_1_out;

  Decoder #(.select(5), .enable("false")) decoder_1 (
    .out0(decoder_1_out0), .out1(decoder_1_out1), .out2(decoder_1_out2), .out3(decoder_1_out3),
    .out4(decoder_1_out4), .out5(decoder_1_out5), .out6(decoder_1_out6), .out7(decoder_1_out7),
    .out8(decoder_1_out8), .out9(decoder_1_out9), .out10(decoder_1_out10), .out11(decoder_1_out11),
    .out12(decoder_1_out12), .out13(decoder_1_out13), .out14(decoder_1_out14), .out15(decoder_1_out15),
    .out16(decoder_1_out16), .out17(decoder_1_out17), .out18(decoder_1_out18), .out19(decoder_1_out19),
    .out20(decoder_1_out20), .out21(decoder_1_out21), .out22(decoder_1_out22), .out23(decoder_1_out23),
    .out24(decoder_1_out24), .out25(decoder_1_out25), .out26(decoder_1_out26), .out27(decoder_1_out27),
    .out28(decoder_1_out28), .out29(decoder_1_out29), .out30(decoder_1_out30), .out31(SP_sel), .sel(dir_dest));
  Register #(.width(32)) register_1 (.D({32{1'b0}}), .en(and_1_out), .Q(register_1_q), .clk(CLK), .clr(RST));
  and and_1 (and_1_out, decoder_1_out0, R_W);
  Register #(.width(32)) register_2 (.D(Data), .en(and_2_out), .Q(register_2_q), .clk(CLK), .clr(RST));
  and and_2 (and_2_out, decoder_1_out1, R_W);
  Register #(.width(32)) register_3 (.D(Data), .en(and_3_out), .Q(register_3_q), .clk(CLK), .clr(RST));
  and and_3 (and_3_out, decoder_1_out2, R_W);
  Register #(.width(32)) register_4 (.D(Data), .en(and_4_out), .Q(register_4_q), .clk(CLK), .clr(RST));
  and and_4 (and_4_out, decoder_1_out3, R_W);
  Register #(.width(32)) register_5 (.D(Data), .en(and_5_out), .Q(register_5_q), .clk(CLK), .clr(RST));
  and and_5 (and_5_out, decoder_1_out4, R_W);
  Register #(.width(32)) register_6 (.D(Data), .en(and_6_out), .Q(register_6_q), .clk(CLK), .clr(RST));
  and and_6 (and_6_out, decoder_1_out5, R_W);
  Register #(.width(32)) register_7 (.D(Data), .en(and_7_out), .Q(register_7_q), .clk(CLK), .clr(RST));
  and and_7 (and_7_out, decoder_1_out6, R_W);
  Register #(.width(32)) register_8 (.D(Data), .en(and_8_out), .Q(register_8_q), .clk(CLK), .clr(RST));
  and and_8 (and_8_out, decoder_1_out7, R_W);
  or or_1 (EnSp, SP_sel, in_8);
  or or_2 (mod, in_10, in_9);
  and and_9 (and_9_out, decoder_1_out8, R_W);
  and and_10 (and_10_out, decoder_1_out9, R_W);
  and and_11 (and_11_out, decoder_1_out10, R_W);
  and and_12 (and_12_out, decoder_1_out11, R_W);
  and and_13 (and_13_out, decoder_1_out12, R_W);
  and and_14 (and_14_out, decoder_1_out13, R_W);
  and and_15 (and_15_out, decoder_1_out14, R_W);
  and and_16 (and_16_out, decoder_1_out15, R_W);
  Register #(.width(32)) register_9 (.D(Data), .en(and_9_out), .Q(register_9_q), .clk(CLK), .clr(RST));
  Register #(.width(32)) register_10 (.D(Data), .en(and_10_out), .Q(register_10_q), .clk(CLK), .clr(RST));
  Register #(.width(32)) register_11 (.D(Data), .en(and_11_out), .Q(register_11_q), .clk(CLK), .clr(RST));
  Register #(.width(32)) register_12 (.D(Data), .en(and_12_out), .Q(register_12_q), .clk(CLK), .clr(RST));
  Register #(.width(32)) register_13 (.D(Data), .en(and_13_out), .Q(register_13_q), .clk(CLK), .clr(RST));
  Register #(.width(32)) register_14 (.D(Data), .en(and_14_out), .Q(register_14_q), .clk(CLK), .clr(RST));
  Register #(.width(32)) register_15 (.D(Data), .en(and_15_out), .Q(register_15_q), .clk(CLK), .clr(RST));
  Register #(.width(32)) register_16 (.D(Data), .en(and_16_out), .Q(register_16_q), .clk(CLK), .clr(RST));
  Adder #(.width(32)) adder_1 (.a(out_13), .b(32'h4), .out(adder_1_out));  // open: cin, cout
  Subtractor #(.width(32)) subtractor_1 (.a(out_13), .b(32'h4), .out(subtractor_1_out));  // open: bin, bout
  Multiplexer #(.width(32), .enable("false")) multiplexer_1 (
    .in0(adder_1_out), .in1(subtractor_1_out), .out(multiplexer_1_out), .sel(in_9));
  and and_17 (and_17_out, decoder_1_out16, R_W);
  and and_18 (and_18_out, decoder_1_out17, R_W);
  and and_19 (and_19_out, decoder_1_out18, R_W);
  and and_20 (and_20_out, decoder_1_out19, R_W);
  and and_21 (and_21_out, decoder_1_out20, R_W);
  and and_22 (and_22_out, decoder_1_out21, R_W);
  and and_23 (and_23_out, decoder_1_out22, R_W);
  and and_24 (and_24_out, decoder_1_out23, R_W);
  Multiplexer #(.width(32), .enable("false")) multiplexer_2 (
    .in0(out_13), .in1(multiplexer_1_out), .out(SP_load), .sel(mod));
  Register #(.width(32)) register_17 (.D(Data), .en(and_17_out), .Q(register_17_q), .clk(CLK), .clr(RST));
  Register #(.width(32)) register_18 (.D(Data), .en(and_18_out), .Q(register_18_q), .clk(CLK), .clr(RST));
  Register #(.width(32)) register_19 (.D(Data), .en(and_19_out), .Q(register_19_q), .clk(CLK), .clr(RST));
  Register #(.width(32)) register_20 (.D(Data), .en(and_20_out), .Q(register_20_q), .clk(CLK), .clr(RST));
  Register #(.width(32)) register_21 (.D(Data), .en(and_21_out), .Q(register_21_q), .clk(CLK), .clr(RST));
  Register #(.width(32)) register_22 (.D(Data), .en(and_22_out), .Q(register_22_q), .clk(CLK), .clr(RST));
  Register #(.width(32)) register_23 (.D(Data), .en(and_23_out), .Q(register_23_q), .clk(CLK), .clr(RST));
  Register #(.width(32)) register_24 (.D(Data), .en(and_24_out), .Q(register_24_q), .clk(CLK), .clr(RST));
  and and_25 (and_25_out, decoder_1_out24, R_W);
  and and_26 (and_26_out, decoder_1_out25, R_W);
  and and_27 (and_27_out, decoder_1_out26, R_W);
  and and_28 (and_28_out, decoder_1_out27, R_W);
  and and_29 (and_29_out, decoder_1_out28, R_W);
  and and_30 (and_30_out, decoder_1_out29, R_W);
  and and_31 (and_31_out, decoder_1_out30, R_W);
  Register #(.width(32)) register_25 (.D(Data), .en(and_25_out), .Q(register_25_q), .clk(CLK), .clr(RST));
  Register #(.width(32)) register_26 (.D(Data), .en(and_26_out), .Q(register_26_q), .clk(CLK), .clr(RST));
  Register #(.width(32)) register_27 (.D(Data), .en(and_27_out), .Q(register_27_q), .clk(CLK), .clr(RST));
  Register #(.width(32)) register_28 (.D(Data), .en(and_28_out), .Q(register_28_q), .clk(CLK), .clr(RST));
  Register #(.width(32)) register_29 (.D(Data), .en(and_29_out), .Q(register_29_q), .clk(CLK), .clr(RST));
  Register #(.width(32)) register_30 (.D(Data), .en(and_30_out), .Q(register_30_q), .clk(CLK), .clr(RST));
  Register #(.width(32)) register_31 (.D(Data), .en(and_31_out), .Q(register_31_q), .clk(CLK), .clr(RST));
  Register #(.width(32)) register_32 (.D(SP_load), .en(EnSp), .Q(out_13), .clk(CLK), .clr(RST));
  Multiplexer #(.select(5), .width(32)) multiplexer_3 (
    .in0(register_1_q), .in1(register_2_q), .in2(register_3_q), .in3(register_4_q), .in4(register_5_q),
    .in5(register_6_q), .in6(register_7_q), .in7(register_8_q), .in8(register_9_q), .in9(register_10_q),
    .in10(register_11_q), .in11(register_12_q), .in12(register_13_q), .in13(register_14_q),
    .in14(register_15_q), .in15(register_16_q), .in16(register_17_q), .in17(register_18_q),
    .in18(register_19_q), .in19(register_20_q), .in20(register_21_q), .in21(register_22_q),
    .in22(register_23_q), .in23(register_24_q), .in24(register_25_q), .in25(register_26_q),
    .in26(register_27_q), .in27(register_28_q), .in28(register_29_q), .in29(register_30_q),
    .in30(register_31_q), .in31(out_13), .out(out_11), .sel(dir_a));  // open: en
  Multiplexer #(.select(5), .width(32)) multiplexer_4 (
    .in0(register_1_q), .in1(register_2_q), .in2(register_3_q), .in3(register_4_q), .in4(register_5_q),
    .in5(register_6_q), .in6(register_7_q), .in7(register_8_q), .in8(register_9_q), .in9(register_10_q),
    .in10(register_11_q), .in11(register_12_q), .in12(register_13_q), .in13(register_14_q),
    .in14(register_15_q), .in15(register_16_q), .in16(register_17_q), .in17(register_18_q),
    .in18(register_19_q), .in19(register_20_q), .in20(register_21_q), .in21(register_22_q),
    .in22(register_23_q), .in23(register_24_q), .in24(register_25_q), .in25(register_26_q),
    .in26(register_27_q), .in27(register_28_q), .in28(register_29_q), .in29(register_30_q),
    .in30(register_31_q), .in31(out_13), .out(out_12), .sel(dir_b));  // open: en

  // Other names for the same wires on the sheet: enSP_t = in_8; pop = in_10; push = in_9; SP[31:0] = out_13
endmodule

module PC (
  input  RST,
  input  CLK,
  input  En,
  input  [31:0] PC_Inp,
  output [31:0] out_5
);

  Register #(.width(32)) register_1 (.D(PC_Inp), .en(En), .Q(out_5), .clk(CLK), .clr(RST));

  // Other names for the same wires on the sheet: PC_in[31:0] = PC_Inp
endmodule

module ALU (
  input  [31:0] in_1,
  input  [31:0] in_2,
  input  CLK,
  input  RST,
  input  Sign,
  input  [2:0] Op,
  output [31:0] out_7,
  output [31:0] out_8,
  output [31:0] out_9,
  output out_10,
  output out_11,
  output out_12,
  output out_13
);

  wire adder_3_cout, and_3_out, and_4_out, En, NotEven, Odds, tunnel, u, xor_2_out;
  wire [31:0] A_comp, add, adder_2_out, \and , B_comp, Div, div_t, end_div, end_Mul_U, end_Up_Mul_U, Mul,
       mul_t, multiplexer_2_out, multiplexer_3_out, multiplexer_4_out, multiplexer_5_out, multiplexer_6_out,
       multiplexer_7_out, multiplexer_8_out, multiplexer_9_out, Mulu_Hi, Mulu_Hi_end, Mulu_Lo, Mulu_Lo_end,
       negator_3_out, \nor , \or , rem, sub, subtractor_2_out, Up_Mul, \xor ;

  multiplexer_8input multiplexer_8input_1 (
    .in_1(add), .in_2(sub), .in_3(\and ), .in_4(\nor ), .in_5(\or ), .in_7(\xor ), .in_8(mul_t),
    .in_9(div_t), .out_10(out_7), .in_6(Op));
  Adder #(.width(32)) adder_1 (.a(in_1), .b(in_2), .out(add));  // open: cin, cout
  Subtractor #(.width(32)) subtractor_1 (.a(in_1), .b(in_2), .out(sub));  // open: bin, bout
  assign \and  = in_1 & in_2;  // AND_Gate and_1, 32 bits wide
  Comparator #(.width(32)) comparator_1 (.a(in_1), .b(in_2), .eq(out_13), .lt(tunnel));  // open: gt
  Multiplexer #(.enable("false")) multiplexer_1 (.in0(u), .in1(tunnel), .out(out_12), .sel(Sign));
  and and_2 (Odds, in_1[0], in_2[0]);
  or or_1 (NotEven, in_1[0], in_2[0]);
  nor nor_1 (out_10, out_7[0], out_7[1], out_7[2], out_7[3], out_7[4], out_7[5], out_7[6], out_7[7], out_7[8], out_7[9], out_7[10], out_7[11], out_7[12], out_7[13], out_7[14], out_7[15], out_7[17], out_7[18], out_7[19], out_7[20], out_7[21], out_7[22], out_7[23], out_7[24], out_7[25], out_7[26], out_7[27], out_7[28], out_7[29], out_7[30], out_7[16], out_7[31]);
  assign \or  = in_1 | in_2;  // OR_Gate or_2, 32 bits wide
  and and_3 (and_3_out, Sign, in_1[31]);
  and and_4 (and_4_out, in_2[31], Sign);
  assign \xor  = in_1 ^ in_2;  // XOR_Gate xor_1, 32 bits wide
  assign \nor  = ~(in_1 | in_2);  // NOR_Gate nor_2, 32 bits wide
  Comparator #(.width(32), .mode("unsigned")) comparator_2 (.a(in_1), .b(in_2), .lt(u));  // open: gt, eq
  Multiplexer #(.width(32), .enable("false")) multiplexer_2 (
    .in0(in_1), .in1(A_comp), .out(multiplexer_2_out), .sel(and_3_out));
  Multiplexer #(.width(32), .enable("false")) multiplexer_3 (
    .in0(in_2), .in1(B_comp), .out(multiplexer_3_out), .sel(and_4_out));
  Divider #(.width(32)) divider_1 (.a(multiplexer_2_out), .b(multiplexer_3_out), .out(Div), .rem(rem));  // open: upper
  Multiplexer #(.width(32), .enable("false")) multiplexer_4 (
    .in0({1'b0, in_1[31:1]}), .in1(in_1), .out(multiplexer_4_out), .sel(Sign));
  Multiplexer #(.width(32), .enable("false")) multiplexer_5 (
    .in0({1'b0, in_2[31:1]}), .in1(in_2), .out(multiplexer_5_out), .sel(Sign));
  Negator #(.width(32)) negator_1 (.in(in_1), .out(A_comp));
  Negator #(.width(32)) negator_2 (.in(in_2), .out(B_comp));
  and and_5 (En, Op[1], Op[2]);
  Subtractor #(.width(32)) subtractor_2 (.a(in_1), .b(32'h1), .out(subtractor_2_out));  // open: bin, bout
  Multiplier #(.width(32)) multiplier_1 (
    .a(multiplexer_4_out), .b(multiplexer_5_out), .out(Mul), .cout(Up_Mul));  // open: cin
  Multiplexer #(.width(32), .enable("false")) multiplexer_6 (
    .in0(in_1), .in1(in_2), .out(multiplexer_6_out), .sel(in_1[0]));
  Adder #(.width(32)) adder_2 (.a(subtractor_2_out), .b(in_2), .out(adder_2_out));  // open: cin, cout
  Negator #(.width(32)) negator_3 (.in(Div), .out(negator_3_out));
  Multiplexer #(.width(32), .enable("false")) multiplexer_7 (
    .in0(multiplexer_6_out), .in1(adder_2_out), .out(multiplexer_7_out), .sel(Odds));
  Multiplexer #(.width(32), .enable("false")) multiplexer_8 (
    .in0(Mulu_Hi_end), .in1(rem), .out(multiplexer_8_out), .sel(Op[0]));
  Multiplexer #(.width(32), .enable("false")) multiplexer_9 (
    .in0(Mulu_Lo_end), .in1(end_div), .out(multiplexer_9_out), .sel(Op[0]));
  xor xor_2 (xor_2_out, in_1[31], in_2[31]);
  Adder #(.width(32)) adder_3 (
    .a(multiplexer_7_out), .b({Mul[29:0], 2'b00}), .out(end_Mul_U), .cout(adder_3_cout));  // open: cin
  Adder #(.width(32)) adder_4 (
    .a({Up_Mul[29:0], Mul[31:30]}), .b({32{1'b0}}), .out(end_Up_Mul_U), .cin(adder_3_cout));  // open: cout
  Register #(.width(32)) Hi (.D(multiplexer_8_out), .en(En), .Q(out_8), .clk(CLK), .clr(RST));
  Register #(.width(32)) Lo (.D(multiplexer_9_out), .en(En), .Q(out_9), .clk(CLK), .clr(RST));
  Multiplexer #(.width(32), .enable("false")) multiplexer_10 (
    .in0(Div), .in1(negator_3_out), .out(end_div), .sel(xor_2_out));
  Multiplexer #(.width(32), .enable("false")) multiplexer_11 (
    .in0({Mul[29:0], 2'b00}), .in1(end_Mul_U), .out(Mulu_Lo), .sel(NotEven));
  Multiplexer #(.width(32), .enable("false")) multiplexer_12 (
    .in0({Up_Mul[29:0], Mul[31:30]}), .in1(end_Up_Mul_U), .out(Mulu_Hi), .sel(NotEven));
  Multiplexer #(.width(32), .enable("false")) multiplexer_13 (.in0(Mulu_Lo), .in1(Mul), .out(Mulu_Lo_end), .sel(Sign));
  Multiplexer #(.width(32), .enable("false")) multiplexer_14 (
    .in0(Mulu_Hi), .in1(Up_Mul), .out(Mulu_Hi_end), .sel(Sign));

  assign out_11 = out_7[31];

  // Other names for the same wires on the sheet: _1A = in_1[0]; A[31:0] = in_1; A1[30:0] = in_1[31:1];
  //   Sign_a = in_1[31]; _1B = in_2[0]; B[31:0] = in_2; B1[30:0] = in_2[31:1]; Sign_b = in_2[31]; Hi[31:0] = out_8;
  //   Lo[31:0] = out_9; Up_Mul_U[31:0] = {Up_Mul[29:0], Mul[31:30]}; Mul_U[31:2] = Mul[29:0]; div_mul = Op[0];
  //   Res[31:0] = out_7; Sign_t = out_7[31]; SGN = Sign; slt = out_12; tunnel_t = out_13; Zero = out_10

  // Notes on the sheet:
  //   DIVISION
  //   OUTPUTS
endmodule

module multiplexer_8input (
  input  [31:0] in_1,
  input  [31:0] in_2,
  input  [31:0] in_3,
  input  [31:0] in_4,
  input  [31:0] in_5,
  input  [2:0] in_6,
  input  [31:0] in_7,
  input  [31:0] in_8,
  input  [31:0] in_9,
  output [31:0] out_10
);

  wire a00, a01, a02, a03, a04, a05, a06, a07;

  assign out_10 = a00 ? in_1 : 32'bz;  // Controlled_Buffer controlled_buffer_1
  assign out_10 = a01 ? in_2 : 32'bz;  // Controlled_Buffer controlled_buffer_2
  assign out_10 = a02 ? in_3 : 32'bz;  // Controlled_Buffer controlled_buffer_3
  assign out_10 = a03 ? in_4 : 32'bz;  // Controlled_Buffer controlled_buffer_4
  assign out_10 = a04 ? in_5 : 32'bz;  // Controlled_Buffer controlled_buffer_5
  assign out_10 = a05 ? in_7 : 32'bz;  // Controlled_Buffer controlled_buffer_6
  assign out_10 = a06 ? in_8 : 32'bz;  // Controlled_Buffer controlled_buffer_7
  assign out_10 = a07 ? in_9 : 32'bz;  // Controlled_Buffer controlled_buffer_8
  Decoder #(.select(3)) decoder_1 (
    .out0(a00), .out1(a01), .out2(a02), .out3(a03), .out4(a04), .out5(a05), .out6(a06), .out7(a07), .sel(in_6));  // open: en

  // Other names for the same wires on the sheet: out[31:0] = out_10
endmodule

module ID (
  input  [31:0] Instruction,
  output [25:0] Dest,
  output add,
  output mul,
  output nop,
  output out_6,
  output out_7,
  output out_8,
  output out_9,
  output out_10,
  output out_11,
  output out_12,
  output out_13,
  output out_14,
  output out_15,
  output out_16,
  output out_17,
  output out_18,
  output out_19,
  output out_20,
  output out_21,
  output out_22,
  output out_23,
  output out_24,
  output out_25,
  output out_26,
  output out_27,
  output out_28,
  output out_29,
  output out_30,
  output out_31,
  output out_32,
  output out_33,
  output out_34,
  output out_35,
  output out_36,
  output out_37,
  output out_38,
  output [31:0] \const ,
  output [4:0] out_40,
  output [4:0] out_41,
  output [4:0] out_42
);

  wire _000000, _111000, _111111, \and , and_2_out, and_11_out, and_16_out, div, divu, halt, jr, kbd, mfhi,
       mflo, mulu, \nor , \or , or_1_out, pop, push, R_en, rnd, slt, sltu, sub, tty, \xor ;

  and and_1 (_000000, ~Instruction[31], ~Instruction[30], ~Instruction[29], ~Instruction[28], ~Instruction[27], ~Instruction[26]);  // AND_Gate
  and and_2 (and_2_out, Instruction[5], ~Instruction[4], ~Instruction[3], ~Instruction[2], ~Instruction[1], ~Instruction[0]);  // AND_Gate
  and and_3 (add, and_2_out, _000000);
  and and_4 (out_25, ~Instruction[31], ~Instruction[30], Instruction[29], ~Instruction[28], ~Instruction[27], ~Instruction[26]);  // AND_Gate
  and and_5 (out_35, Instruction[31], ~Instruction[30], Instruction[29], ~Instruction[28], Instruction[27], Instruction[26]);  // AND_Gate
  and and_6 (out_38, ~Instruction[31], ~Instruction[30], ~Instruction[29], ~Instruction[28], Instruction[27], ~Instruction[26]);  // AND_Gate
  and and_7 (R_en, _000000, ~add, ~mul, ~nop);  // AND_Gate
  and and_8 (out_26, ~Instruction[31], ~Instruction[30], Instruction[29], ~Instruction[28], Instruction[27], ~Instruction[26]);  // AND_Gate
  and and_9 (out_36, ~Instruction[31], ~Instruction[30], ~Instruction[29], Instruction[28], ~Instruction[27], ~Instruction[26]);  // AND_Gate
  and and_10 (_111000, Instruction[31], Instruction[30], Instruction[29], ~Instruction[28], ~Instruction[27], ~Instruction[26]);  // AND_Gate
  and and_11 (and_11_out, ~Instruction[5], Instruction[4], Instruction[3], ~Instruction[2], ~Instruction[1], ~Instruction[0]);  // AND_Gate
  and and_12 (mul, and_11_out, _000000);
  Decoder #(.select(4)) decoder_1 (
    .out0(mfhi), .out2(mflo), .out4(jr), .out5(mulu), .out6(div), .out7(divu), .out8(\and ), .out9(\or ),
    .out10(sub), .out11(\nor ), .out12(\xor ), .out14(slt), .out15(sltu),
    .sel({Instruction[5], Instruction[3], Instruction[1:0]}), .en(R_en));  // open: out1, out3, out13
  and and_13 (out_27, ~Instruction[31], ~Instruction[30], Instruction[29], ~Instruction[28], Instruction[27], Instruction[26]);  // AND_Gate
  and and_14 (out_37, ~Instruction[31], ~Instruction[30], ~Instruction[29], Instruction[28], ~Instruction[27], Instruction[26]);  // AND_Gate
  and and_15 (_111111, Instruction[31], Instruction[30], Instruction[29], Instruction[28], Instruction[27], Instruction[26]);
  and and_16 (and_16_out, ~Instruction[5], ~Instruction[4], ~Instruction[3], ~Instruction[2], ~Instruction[1], ~Instruction[0]);  // AND_Gate
  and and_17 (nop, and_16_out, _000000);
  and and_18 (out_28, ~Instruction[31], ~Instruction[30], Instruction[29], Instruction[28], ~Instruction[27], ~Instruction[26]);  // AND_Gate
  and and_19 (out_32, ~Instruction[31], ~Instruction[30], ~Instruction[29], Instruction[28], Instruction[27], ~Instruction[26]);  // AND_Gate
  Multiplexer #(.enable("false")) multiplexer_1 (.in0(1'b0), .in1(pop), .out(out_6), .sel(_111000));
  Multiplexer #(.enable("false")) multiplexer_2 (.in0(1'b0), .in1(push), .out(out_10), .sel(_111000));
  Multiplexer #(.enable("false")) multiplexer_3 (.in0(1'b0), .in1(kbd), .out(out_13), .sel(_111111));
  Multiplexer #(.enable("false")) multiplexer_4 (.in0(1'b0), .in1(tty), .out(out_16), .sel(_111111));
  Multiplexer #(.enable("false")) multiplexer_5 (.in0(1'b0), .in1(rnd), .out(out_19), .sel(_111111));
  Multiplexer #(.enable("false")) multiplexer_6 (.in0(1'b0), .in1(halt), .out(out_22), .sel(_111111));
  and and_20 (out_29, ~Instruction[31], ~Instruction[30], Instruction[29], Instruction[28], ~Instruction[27], Instruction[26]);  // AND_Gate
  and and_21 (out_33, ~Instruction[31], ~Instruction[30], ~Instruction[29], Instruction[28], Instruction[27], Instruction[26]);  // AND_Gate
  Decoder decoder_2 (.out0(pop), .out1(push), .sel(Instruction[0]), .en(_111000));
  Multiplexer #(.width(32), .enable("false")) multiplexer_7 (
    .in0({{17{Instruction[15]}}, Instruction[14:0]}), .in1({{16{1'b0}}, Instruction[15:0]}), .out(\const ),
    .sel(or_1_out));
  or or_1 (or_1_out, out_28, out_29, out_30);
  Multiplexer #(.enable("false")) multiplexer_8 (.in0(1'b0), .in1(mfhi), .out(out_7), .sel(R_en));
  Multiplexer #(.enable("false")) multiplexer_9 (.in0(1'b0), .in1(mflo), .out(out_11), .sel(R_en));
  Multiplexer #(.enable("false")) multiplexer_10 (.in0(1'b0), .in1(jr), .out(out_14), .sel(R_en));
  Multiplexer #(.enable("false")) multiplexer_11 (.in0(1'b0), .in1(mulu), .out(out_17), .sel(R_en));
  Multiplexer #(.enable("false")) multiplexer_12 (.in0(1'b0), .in1(div), .out(out_20), .sel(R_en));
  Multiplexer #(.enable("false")) multiplexer_13 (.in0(1'b0), .in1(divu), .out(out_23), .sel(R_en));
  and and_22 (out_30, ~Instruction[31], ~Instruction[30], Instruction[29], Instruction[28], Instruction[27], ~Instruction[26]);  // AND_Gate
  and and_23 (out_34, ~Instruction[31], ~Instruction[30], ~Instruction[29], ~Instruction[28], ~Instruction[27], Instruction[26]);  // AND_Gate
  Decoder #(.select(2)) decoder_3 (
    .out0(kbd), .out1(tty), .out2(rnd), .out3(halt), .sel(Instruction[1:0]), .en(_111111));
  and and_24 (out_31, Instruction[31], ~Instruction[30], ~Instruction[29], ~Instruction[28], Instruction[27], Instruction[26]);  // AND_Gate
  Multiplexer #(.enable("false")) multiplexer_14 (.in0(1'b0), .in1(\and ), .out(out_8), .sel(R_en));
  Multiplexer #(.enable("false")) multiplexer_15 (.in0(1'b0), .in1(\or ), .out(out_12), .sel(R_en));
  Multiplexer #(.enable("false")) multiplexer_16 (.in0(1'b0), .in1(sub), .out(out_15), .sel(R_en));
  Multiplexer #(.enable("false")) multiplexer_17 (.in0(1'b0), .in1(\nor ), .out(out_18), .sel(R_en));
  Multiplexer #(.enable("false")) multiplexer_18 (.in0(1'b0), .in1(\xor ), .out(out_21), .sel(R_en));
  Multiplexer #(.enable("false")) multiplexer_19 (.in0(1'b0), .in1(slt), .out(out_24), .sel(R_en));
  Multiplexer #(.enable("false")) multiplexer_20 (.in0(1'b0), .in1(sltu), .out(out_9), .sel(R_en));

  assign Dest = Instruction[25:0];
  assign out_40 = Instruction[25:21];
  assign out_41 = Instruction[15:11];
  assign out_42 = Instruction[20:16];

  // Other names for the same wires on the sheet: _0 = Instruction[0]; Const_t[15:0] = Instruction[15:0];
  //   _1 = Instruction[1]; addi = out_25; andi = out_28; beq = out_36; bgtz = out_33; blez = out_32; bltz = out_34;
  //   bne = out_37; _2 = Instruction[2]; _3 = Instruction[3]; _4 = Instruction[4]; _5 = Instruction[5];
  //   _6 = Instruction[6]; _7 = Instruction[7]; _8 = Instruction[8]; _9 = Instruction[9]; _10 = Instruction[10];
  //   _11 = Instruction[11]; Rd[4:0] = Instruction[15:11]; _12 = Instruction[12]; _13 = Instruction[13];
  //   _14 = Instruction[14]; _15 = Instruction[15]; _16 = Instruction[16]; Rt[4:0] = Instruction[20:16];
  //   _17 = Instruction[17]; _18 = Instruction[18]; _19 = Instruction[19]; _20 = Instruction[20];
  //   _21 = Instruction[21]; Rs[4:0] = Instruction[25:21]; _22 = Instruction[22]; _23 = Instruction[23];
  //   _24 = Instruction[24]; _25 = Instruction[25]; _26 = Instruction[26]; _27 = Instruction[27];
  //   _28 = Instruction[28]; _29 = Instruction[29]; _30 = Instruction[30]; _31 = Instruction[31]; j = out_38;
  //   lw = out_31; ori = out_29; slti = out_26; sltiu = out_27; sw = out_35; xori = out_30

  // Notes on the sheet:
  //   I Instructions
  //   J Instructions
  //   R Instructions
  //   Pop/Push Ops
  //   Special Ops
endmodule

module Random (
  input  CLK,
  input  En,
  output [31:0] out_3
);

  Random_part #(.width(32)) random_1 (.clk(CLK), .next(En), .out(out_3));  // open: clr
endmodule

module \wait  (
  input  Start,
  input  Clear,
  input  CLK,
  input  [3:0] \time ,
  output out_5,
  output out_6
);

  wire comparator_1_eq, CS1, d_ff_1_q, load;
  wire [3:0] counter_1_q, multiplexer_1_out;

  or or_1 (out_6, CS1, out_5);
  or or_2 (load, CS1, Start);
  Multiplexer #(.width(4), .enable("false")) multiplexer_1 (
    .in0(4'b0001), .in1(\time ), .out(multiplexer_1_out), .sel(Start));
  D_Flip_Flop d_ff_1 (.clk(CLK), .D(load), .Q(d_ff_1_q));  // open: Qn, preset, en, reset
  Counter #(.width(4), .max('hf)) counter_1 (
    .load(load), .D(multiplexer_1_out), .count(CS1), .Q(counter_1_q), .clk(CLK));  // open: carry, clr
  Demultiplexer #(.enable("false")) demultiplexer_1 (.out0(CS1), .out1(out_5), .in(d_ff_1_q), .sel(comparator_1_eq));
  Comparator #(.width(4), .mode("unsigned")) comparator_1 (
    .a(counter_1_q), .b(4'b0000), .eq(comparator_1_eq));  // open: gt, lt

  // Other names for the same wires on the sheet: dec = CS1; CS2 = out_5; ready = out_5
endmodule

module Branch_Control (
  input  in_1,
  input  in_2,
  input  in_3,
  input  in_4,
  input  in_5,
  input  in_6,
  input  in_7,
  input  in_8,
  input  in_9,
  input  in_10,
  input  in_11,
  input  in_12,
  input  [25:0] in_13,
  input  [31:0] in_14,
  input  [31:0] in_15,
  input  [31:0] in_16,
  output [31:0] PC_Out
);

  wire and_1_out, and_2_out, and_3_out, and_4_out, and_5_out, and_6_out, branch, jmp, or_1_out;
  wire [31:0] Branch_Address, multiplexer_1_out, multiplexer_2_out, PC_4;

  or or_1 (or_1_out, in_3, in_7);
  and and_1 (and_1_out, in_7, ~in_3);  // AND_Gate
  Adder #(.width(32)) adder_1 (.a(in_16), .b(32'h4), .out(PC_4));  // open: cin, cout
  and and_2 (and_2_out, in_1, in_4);
  and and_3 (and_3_out, ~in_4, in_2);  // AND_Gate
  and and_4 (and_4_out, in_5, or_1_out);
  and and_5 (and_5_out, in_6, ~or_1_out);  // AND_Gate
  and and_6 (and_6_out, and_1_out, in_8);
  or or_2 (branch, and_2_out, and_3_out, and_4_out, and_5_out, and_6_out);
  or or_3 (jmp, branch, in_9, in_10);
  Adder #(.width(32)) adder_2 (.a(PC_4), .b({in_15[29:0], 2'b00}), .out(Branch_Address));  // open: cin, cout
  Multiplexer #(.select(2), .width(32), .enable("false")) multiplexer_1 (
    .in0(Branch_Address), .in1(in_14), .in2({in_16[31:28], in_13, 2'b00}), .out(multiplexer_1_out),
    .sel({in_9, in_10}));  // open: in3
  Multiplexer #(.width(32), .enable("false")) multiplexer_2 (
    .in0(PC_4), .in1(multiplexer_1_out), .out(multiplexer_2_out), .sel(jmp));
  Multiplexer #(.width(32), .enable("false")) multiplexer_3 (
    .in0(in_16), .in1(multiplexer_2_out), .out(PC_Out), .sel(in_12));

  // Other names for the same wires on the sheet: jr = in_10; j = in_9; _0 = in_7; beq = in_1; bgtz = in_6;
  //   blez = in_5; bltz = in_8; bne = in_2; CLK = in_11; Dest[25:0] = in_13;
  //   Destination[31:2] = {in_16[31:28], in_13}; PC_In[31:0] = in_16; next = in_12; Offset[31:0] = in_15;
  //   Rs[31:0] = in_14; S_Offset[31:2] = in_15[29:0]; tunnel = in_4; ZF = in_3
endmodule

module Instruction_Fetch (
  input  in_1,
  input  in_2,
  input  in_3,
  input  [31:0] in_4,
  input  [31:0] in_5,
  input  [31:0] in_6,
  input  [31:0] in_7,
  input  [31:0] in_8,
  output [31:0] out_9,
  output out_10
);

  wire [31:0] out;

  // Probe on in_4[3:2]
  Multiplexer #(.select(2), .width(32), .enable("false")) multiplexer_1 (
    .in0(in_5), .in1(in_6), .in2(in_7), .in3(in_8), .out({out[7:0], out[15:8], out[23:16], out[31:24]}),
    .sel(in_4[3:2]));
  Register #(.width(32)) register_1 (.D(out), .en(in_3), .Q(out_9), .clk(in_1), .clr(in_2));
  D_Flip_Flop d_ff_1 (.clk(in_1), .D(in_3), .Q(out_10));  // open: Qn, preset, en, reset

  // Other names for the same wires on the sheet: CLK = in_1; Bank[1:0] = in_4[3:2]; address[15:0] = in_4[19:4];
  //   Ready = in_3; RST = in_2
endmodule

module ReadMem (
  input  in_1,
  input  in_2,
  input  in_3,
  input  [31:0] in_4,
  input  [31:0] in_5,
  input  [31:0] in_6,
  input  [31:0] in_7,
  input  [31:0] in_8,
  output [31:0] out_9,
  output out_10
);

  wire [31:0] out;

  Multiplexer #(.select(2), .width(32), .enable("false")) multiplexer_1 (
    .in0(in_5), .in1(in_6), .in2(in_7), .in3(in_8), .out({out[7:0], out[15:8], out[23:16], out[31:24]}),
    .sel(in_4[3:2]));
  Register #(.width(32)) register_1 (.D(out), .en(in_3), .Q(out_9), .clk(in_1), .clr(in_2));
  D_Flip_Flop d_ff_1 (.clk(in_1), .D(in_3), .Q(out_10));  // open: Qn, preset, en, reset

  // Other names for the same wires on the sheet: CLK = in_1; Bank[1:0] = in_4[3:2]; address[15:0] = in_4[19:4];
  //   Ready = in_3; RST = in_2
endmodule

module WriteMem (
  input  in_1,
  input  in_2,
  input  in_3,
  input  [3:0] in_4,
  input  [31:0] in_5,
  input  [31:0] in_6,
  output [3:0] out_7,
  output [15:0] out_8,
  output [31:0] out_9,
  output [31:0] out_10,
  output [31:0] out_11,
  output out_12,
  output out_13,
  output [31:0] out_14
);

  wire [31:0] register_1_q;

  Decoder #(.select(2)) decoder_1 (
    .out0(out_7[0]), .out1(out_7[1]), .out2(out_7[2]), .out3(out_7[3]), .sel(in_6[3:2]));  // open: en
  Register #(.width(32)) register_1 (
    .D({in_5[7:0], in_5[15:8], in_5[23:16], in_5[31:24]}), .en(in_2), .Q(register_1_q), .clk(in_1), .clr(in_3));
  \wait  wait_1 (.Start(in_2), .Clear(in_3), .CLK(in_1), .\time (in_4), .out_5(out_12), .out_6(out_13));
  Demultiplexer #(.select(2), .width(32), .enable("false")) demultiplexer_1 (
    .out0(out_9), .out1(out_10), .out2(out_11), .out3(out_14), .in(register_1_q), .sel(in_6[3:2]));

  assign out_8 = in_6[19:4];

  // Other names for the same wires on the sheet: Data[31:0] = in_5; Bank_1[31:0] = out_9; Bank_2[31:0] = out_10;
  //   Bank_3[31:0] = out_11; Bank_4[31:0] = out_14; CLK = in_1; En = in_2; Bank[1:0] = in_6[3:2];
  //   address[15:0] = in_6[19:4]; Mask[3:0] = out_7; Reset = in_3; WT[3:0] = in_4
endmodule

module CacheInst (
  input  in_1,
  input  in_2,
  input  in_3,
  input  [31:0] RAM_Out_0,
  input  [31:0] RAM_Out_1,
  input  [31:0] RAM_Out_2,
  input  [31:0] RAM_Out_3,
  input  [31:0] Address,
  input  [3:0] ReadTime,
  output [31:0] CacheOut0,
  output [31:0] CacheOut1,
  output [31:0] CacheOut2,
  output [31:0] CacheOut3,
  output [15:0] AddressOut,
  output Finish,
  output out_16
);

  wire and_1_out, controlled_buffer_1_out, controlled_buffer_2_out, controlled_buffer_3_out,
       controlled_buffer_4_out, controlled_buffer_5_out, controlled_buffer_6_out, controlled_buffer_7_out,
       controlled_buffer_8_out, decoder_1_out0, decoder_1_out1, decoder_1_out2, decoder_1_out3,
       decoder_1_out4, decoder_1_out5, decoder_1_out6, decoder_1_out7, demultiplexer_1_out0,
       demultiplexer_2_out0, demultiplexer_2_out1, Finish_t, hit, miss, not_2_out, not_3_out, not_4_out,
       not_5_out, not_6_out, not_7_out, not_8_out, not_9_out, or_1_out, Ready, start, start_q, v0, v1, v2,
       v3, v4, v5, v6, v7, Val, wait_2_q;
  wire [12:0] tagOut, xnor_1_out;

  Demultiplexer #(.enable("false")) demultiplexer_1 (
    .out0(demultiplexer_1_out0), .out1(start), .in(start_q), .sel(miss));
  D_Flip_Flop u_start (.clk(in_3), .D(in_1), .Q(start_q));  // open: Qn, preset, en, reset
  RAM_part #(.addrWidth(3), .dataWidth(32), .bus("separate")) ram_1 (
    .addr(Address[6:4]), .din(RAM_Out_0), .data(CacheOut0), .str(Finish_t), .clk(in_3), .ld(1'b1), .clr(in_2));  // open: sel
  RAM_part #(.addrWidth(3), .dataWidth(32), .bus("separate")) ram_2 (
    .addr(Address[6:4]), .din(RAM_Out_1), .data(CacheOut1), .str(Finish_t), .clk(in_3), .ld(1'b1), .clr(in_2));  // open: sel
  RAM_part #(.addrWidth(3), .dataWidth(32), .bus("separate")) ram_3 (
    .addr(Address[6:4]), .din(RAM_Out_2), .data(CacheOut2), .str(Finish_t), .clk(in_3), .ld(1'b1), .clr(in_2));  // open: sel
  RAM_part #(.addrWidth(3), .dataWidth(32), .bus("separate")) ram_4 (
    .addr(Address[6:4]), .din(RAM_Out_3), .data(CacheOut3), .str(Finish_t), .clk(in_3), .ld(1'b1), .clr(in_2));  // open: sel
  or or_1 (or_1_out, demultiplexer_2_out0, start);
  \wait  wait_1 (.Start(start), .Clear(in_2), .CLK(in_3), .\time (ReadTime), .out_5(Finish_t), .out_6(out_16));
  D_Flip_Flop wait_2 (.clk(in_3), .D(or_1_out), .Q(wait_2_q));  // open: Qn, preset, en, reset
  Demultiplexer #(.enable("false")) demultiplexer_2 (
    .out0(demultiplexer_2_out0), .out1(demultiplexer_2_out1), .in(wait_2_q), .sel(Finish_t));
  or or_2 (Ready, demultiplexer_1_out0, demultiplexer_2_out1);
  assign xnor_1_out = ~(tagOut ^ Address[19:7]);  // XNOR_Gate xnor_1, 13 bits wide
  RAM_part #(.addrWidth(3), .dataWidth(13), .bus("separate")) ram_5 (
    .addr(Address[6:4]), .din(Address[19:7]), .data(tagOut), .str(Finish_t), .clk(in_3), .ld(1'b1), .clr(in_2));  // open: sel
  Multiplexer #(.select(3)) multiplexer_1 (
    .in0(v0), .in1(v1), .in2(v2), .in3(v3), .in4(v4), .in5(v5), .in6(v6), .in7(v7), .out(Val),
    .sel(Address[6:4]));  // open: en
  and and_1 (and_1_out, xnor_1_out[12], xnor_1_out[11], xnor_1_out[10], xnor_1_out[9], xnor_1_out[8], xnor_1_out[7], xnor_1_out[6], xnor_1_out[5], xnor_1_out[4], xnor_1_out[3], xnor_1_out[2], xnor_1_out[1], xnor_1_out[0]);
  and and_2 (hit, Val, and_1_out);
  Decoder #(.select(3)) decoder_1 (
    .out0(decoder_1_out0), .out1(decoder_1_out1), .out2(decoder_1_out2), .out3(decoder_1_out3),
    .out4(decoder_1_out4), .out5(decoder_1_out5), .out6(decoder_1_out6), .out7(decoder_1_out7),
    .sel(Address[6:4]));  // open: en
  not not_1 (miss, hit);
  not not_2 (not_2_out, v0);
  assign controlled_buffer_1_out = not_2_out ? decoder_1_out0 : 1'bz;  // Controlled_Buffer controlled_buffer_1
  not not_3 (not_3_out, v1);
  assign controlled_buffer_2_out = not_3_out ? decoder_1_out1 : 1'bz;  // Controlled_Buffer controlled_buffer_2
  not not_4 (not_4_out, v2);
  assign controlled_buffer_3_out = not_4_out ? decoder_1_out2 : 1'bz;  // Controlled_Buffer controlled_buffer_3
  not not_5 (not_5_out, v3);
  assign controlled_buffer_4_out = not_5_out ? decoder_1_out3 : 1'bz;  // Controlled_Buffer controlled_buffer_4
  not not_6 (not_6_out, v4);
  assign controlled_buffer_5_out = not_6_out ? decoder_1_out4 : 1'bz;  // Controlled_Buffer controlled_buffer_5
  not not_7 (not_7_out, v5);
  assign controlled_buffer_6_out = not_7_out ? decoder_1_out5 : 1'bz;  // Controlled_Buffer controlled_buffer_6
  not not_8 (not_8_out, v6);
  assign controlled_buffer_7_out = not_8_out ? decoder_1_out6 : 1'bz;  // Controlled_Buffer controlled_buffer_7
  not not_9 (not_9_out, v7);
  assign controlled_buffer_8_out = not_9_out ? decoder_1_out7 : 1'bz;  // Controlled_Buffer controlled_buffer_8
  D_Flip_Flop d_ff_1 (.clk(in_3), .D(controlled_buffer_1_out), .Q(v0), .reset(in_2));  // open: Qn, preset, en
  D_Flip_Flop d_ff_2 (.clk(in_3), .D(controlled_buffer_2_out), .Q(v1), .reset(in_2));  // open: Qn, preset, en
  D_Flip_Flop d_ff_3 (.clk(in_3), .D(controlled_buffer_3_out), .Q(v2), .reset(in_2));  // open: Qn, preset, en
  D_Flip_Flop d_ff_4 (.clk(in_3), .D(controlled_buffer_4_out), .Q(v3), .reset(in_2));  // open: Qn, preset, en
  D_Flip_Flop d_ff_5 (.clk(in_3), .D(controlled_buffer_5_out), .Q(v4), .reset(in_2));  // open: Qn, preset, en
  D_Flip_Flop d_ff_6 (.clk(in_3), .D(controlled_buffer_6_out), .Q(v5), .reset(in_2));  // open: Qn, preset, en
  D_Flip_Flop d_ff_7 (.clk(in_3), .D(controlled_buffer_7_out), .Q(v6), .reset(in_2));  // open: Qn, preset, en
  D_Flip_Flop d_ff_8 (.clk(in_3), .D(controlled_buffer_8_out), .Q(v7), .reset(in_2));  // open: Qn, preset, en
  D_Flip_Flop d_ff_9 (.clk(in_3), .D(Ready), .Q(Finish));  // open: Qn, preset, en, reset

  assign AddressOut = Address[19:4];

  // Other names for the same wires on the sheet: offset[1:0] = Address[3:2]; Address_t[15:0] = Address[19:4];
  //   tag[12:0] = Address[19:7]; Clear = in_2; CLK = in_3; Enable = in_1; idx[2:0] = Address[6:4];
  //   RAM_OUTPUT_0[31:0] = RAM_Out_0; RAM_OUTPUT_1[31:0] = RAM_Out_1; RAM_OUTPUT_2[31:0] = RAM_Out_2;
  //   RAM_OUTPUT_3[31:0] = RAM_Out_3; Read_Time[3:0] = ReadTime
endmodule

module CacheData (
  input  [31:0] Address,
  input  in_2,
  input  in_3,
  input  in_4,
  input  in_5,
  input  [31:0] RAM_Out_0,
  input  [31:0] RAM_Out_1,
  input  [31:0] RAM_Out_2,
  input  [31:0] RAM_Out_3,
  input  [31:0] Value,
  input  [3:0] ReadTime,
  input  [3:0] WriteTime,
  output CS,
  output [15:0] AddressOut,
  output FinishRead,
  output RAM_R_W,
  output FinishWrt,
  output [3:0] Mask,
  output [31:0] CacheOut0,
  output [31:0] CacheOut1,
  output [31:0] CacheOut2,
  output [31:0] CacheOut3
);

  wire and_1_out, and_2_out, and_3_out, and_5_out, and_7_out, and_9_out, and_16_out, and_18_out, and_20_out,
       and_22_out, btag, btag_0, btag_1, controlled_buffer_1_out, controlled_buffer_2_out,
       controlled_buffer_3_out, controlled_buffer_4_out, controlled_buffer_5_out, controlled_buffer_6_out,
       controlled_buffer_7_out, controlled_buffer_8_out, d, d0, d1, d2, d3, d4, d5, d6, d7, d_ff_1_q,
       decoder_1_out0, decoder_1_out1, decoder_1_out2, decoder_1_out3, decoder_2_out0, decoder_2_out1,
       decoder_2_out2, decoder_2_out3, decoder_2_out4, decoder_2_out5, decoder_2_out6, decoder_2_out7,
       decoder_3_out0, decoder_3_out1, decoder_3_out2, decoder_3_out3, decoder_3_out4, decoder_3_out5,
       decoder_3_out6, decoder_3_out7, decoder_4_out0, decoder_4_out1, decoder_4_out2, decoder_4_out3,
       decoder_4_out4, decoder_4_out5, decoder_4_out6, decoder_4_out7, demultiplexer_1_out0,
       demultiplexer_1_out1, demultiplexer_2_out0, demultiplexer_2_out1, demultiplexer_3_out0,
       demultiplexer_3_out1, demultiplexer_4_out0, demultiplexer_4_out1, demultiplexer_5_out0,
       demultiplexer_6_out0, demultiplexer_7_out0, demultiplexer_8_out0, demultiplexer_9_out1,
       demultiplexer_10_out0, dirty, empty, en0, en1, en2, en3, en4, en5, en6, en7, enDirty0, enDirty1,
       enDirty2, enDirty3, enDirty4, enDirty5, enDirty6, enDirty7, enRnd, enRnd_0, enRnd_1, enV, enV_0,
       Finish, Finish_1, Finish_3, full, hit, hit0, hit1, hit2, hit3, hit4, hit5, hit6, hit7, LdDirty,
       LdDirty_0, miss, not_3_out, not_4_out, not_5_out, not_6_out, not_7_out, not_8_out, not_9_out,
       not_10_out, or_8_out, or_9_out, or_10_out, or_11_out, or_12_out, or_17_out, or_18_out, R, R_0, R_1,
       read_2_q, read_q, Ready, start, str0, str1, str2, str3, v0, v1, v2, v3, v4, v5, v6, v7, wrt_2_q;
  wire [2:0] adder_1_out, idx, idx0, idx1, idxHit, multiplexer_8_out, priority_encoder_1_out;
  wire [3:0] multiplexer_10_out;
  wire [15:0] tag0, tag1, tag2, tag3, tag4, tag5, tag6, tag7, tagAddr, xnor_1_out, xnor_2_out, xnor_3_out,
       xnor_4_out, xnor_5_out, xnor_6_out, xnor_7_out, xnor_8_out;
  wire [31:0] multiplexer_2_out, multiplexer_3_out, multiplexer_4_out, multiplexer_5_out;

  Register #(.width(16)) register_1 (.D(Address[19:4]), .en(en0), .Q(tag0), .clk(in_4), .clr(in_3));
  Register #(.width(16)) register_2 (.D(Address[19:4]), .en(en1), .Q(tag1), .clk(in_4), .clr(in_3));
  Register #(.width(16)) register_3 (.D(Address[19:4]), .en(en2), .Q(tag2), .clk(in_4), .clr(in_3));
  Register #(.width(16)) register_4 (.D(Address[19:4]), .en(en3), .Q(tag3), .clk(in_4), .clr(in_3));
  Multiplexer #(.width(16)) multiplexer_1 (
    .in0(Address[19:4]), .in1(tagAddr), .out(AddressOut), .sel(btag));  // open: en
  or or_1 (RAM_R_W, btag_0, btag_1);
  Register #(.width(16)) register_5 (.D(Address[19:4]), .en(en4), .Q(tag4), .clk(in_4), .clr(in_3));
  Register #(.width(16)) register_6 (.D(Address[19:4]), .en(en5), .Q(tag5), .clk(in_4), .clr(in_3));
  Register #(.width(16)) register_7 (.D(Address[19:4]), .en(en6), .Q(tag6), .clk(in_4), .clr(in_3));
  Register #(.width(16)) register_8 (.D(Address[19:4]), .en(en7), .Q(tag7), .clk(in_4), .clr(in_3));
  Multiplexer #(.width(32)) multiplexer_2 (
    .in0(RAM_Out_0), .in1({Value[7:0], Value[15:8], Value[23:16], Value[31:24]}), .out(multiplexer_2_out),
    .sel(dirty));  // open: en
  Multiplexer #(.width(32)) multiplexer_3 (
    .in0(RAM_Out_1), .in1({Value[7:0], Value[15:8], Value[23:16], Value[31:24]}), .out(multiplexer_3_out),
    .sel(dirty));  // open: en
  Multiplexer #(.width(32)) multiplexer_4 (
    .in0(RAM_Out_2), .in1({Value[7:0], Value[15:8], Value[23:16], Value[31:24]}), .out(multiplexer_4_out),
    .sel(dirty));  // open: en
  Multiplexer #(.width(32)) multiplexer_5 (
    .in0(RAM_Out_3), .in1({Value[7:0], Value[15:8], Value[23:16], Value[31:24]}), .out(multiplexer_5_out),
    .sel(dirty));  // open: en
  or or_2 (btag, btag_0, btag_1);
  or or_3 (start, R_0, enRnd_1, R_1, enRnd_0);
  or or_4 (LdDirty, LdDirty_0, dirty);
  or or_5 (R, R_0, R_1);
  or or_6 (enV, enV_0, dirty);
  or or_7 (enRnd, enRnd_0, enRnd_1);
  or or_8 (or_8_out, Finish, str0);
  or or_9 (or_9_out, Finish, str1);
  or or_10 (or_10_out, Finish, str2);
  or or_11 (or_11_out, Finish, str3);
  Multiplexer #(.select(3)) multiplexer_6 (
    .in0(d0), .in1(d1), .in2(d2), .in3(d3), .in4(d4), .in5(d5), .in6(d6), .in7(d7), .out(d), .sel(idx));  // open: en
  RAM_part #(.addrWidth(3), .dataWidth(32), .bus("separate")) ram_1 (
    .addr(idx), .din(multiplexer_2_out), .data(CacheOut0), .str(or_8_out), .clk(in_4), .ld(1'b1), .clr(in_3));  // open: sel
  RAM_part #(.addrWidth(3), .dataWidth(32), .bus("separate")) ram_2 (
    .addr(idx), .din(multiplexer_3_out), .data(CacheOut1), .str(or_9_out), .clk(in_4), .ld(1'b1), .clr(in_3));  // open: sel
  RAM_part #(.addrWidth(3), .dataWidth(32), .bus("separate")) ram_3 (
    .addr(idx), .din(multiplexer_4_out), .data(CacheOut2), .str(or_10_out), .clk(in_4), .ld(1'b1), .clr(in_3));  // open: sel
  RAM_part #(.addrWidth(3), .dataWidth(32), .bus("separate")) ram_4 (
    .addr(idx), .din(multiplexer_5_out), .data(CacheOut3), .str(or_11_out), .clk(in_4), .ld(1'b1), .clr(in_3));  // open: sel
  and and_1 (and_1_out, ~in_5, in_2);  // AND_Gate
  assign xnor_1_out = ~(tag0 ^ Address[19:4]);  // XNOR_Gate xnor_1, 16 bits wide
  assign xnor_2_out = ~(tag2 ^ Address[19:4]);  // XNOR_Gate xnor_2, 16 bits wide
  assign xnor_3_out = ~(tag4 ^ Address[19:4]);  // XNOR_Gate xnor_3, 16 bits wide
  assign xnor_4_out = ~(tag6 ^ Address[19:4]);  // XNOR_Gate xnor_4, 16 bits wide
  Demultiplexer #(.enable("false")) demultiplexer_1 (
    .out0(demultiplexer_1_out0), .out1(demultiplexer_1_out1), .in(and_1_out), .sel(miss));
  Demultiplexer #(.enable("false")) demultiplexer_2 (
    .out0(demultiplexer_2_out0), .out1(demultiplexer_2_out1), .in(and_2_out), .sel(miss));
  and and_2 (and_2_out, in_5, in_2);
  and and_3 (and_3_out, xnor_1_out[15], xnor_1_out[14], xnor_1_out[13], xnor_1_out[12], xnor_1_out[11], xnor_1_out[10], xnor_1_out[9], xnor_1_out[8], xnor_1_out[7], xnor_1_out[6], xnor_1_out[5], xnor_1_out[4], xnor_1_out[3], xnor_1_out[2], xnor_1_out[1], xnor_1_out[0]);
  and and_4 (hit0, v0, and_3_out);
  and and_5 (and_5_out, xnor_2_out[15], xnor_2_out[14], xnor_2_out[13], xnor_2_out[12], xnor_2_out[11], xnor_2_out[10], xnor_2_out[9], xnor_2_out[8], xnor_2_out[7], xnor_2_out[6], xnor_2_out[5], xnor_2_out[4], xnor_2_out[3], xnor_2_out[2], xnor_2_out[1], xnor_2_out[0]);
  and and_6 (hit2, v2, and_5_out);
  and and_7 (and_7_out, xnor_3_out[15], xnor_3_out[14], xnor_3_out[13], xnor_3_out[12], xnor_3_out[11], xnor_3_out[10], xnor_3_out[9], xnor_3_out[8], xnor_3_out[7], xnor_3_out[6], xnor_3_out[5], xnor_3_out[4], xnor_3_out[3], xnor_3_out[2], xnor_3_out[1], xnor_3_out[0]);
  and and_8 (hit4, v4, and_7_out);
  and and_9 (and_9_out, xnor_4_out[15], xnor_4_out[14], xnor_4_out[13], xnor_4_out[12], xnor_4_out[11], xnor_4_out[10], xnor_4_out[9], xnor_4_out[8], xnor_4_out[7], xnor_4_out[6], xnor_4_out[5], xnor_4_out[4], xnor_4_out[3], xnor_4_out[2], xnor_4_out[1], xnor_4_out[0]);
  and and_10 (hit6, v6, and_9_out);
  Demultiplexer #(.enable("false")) demultiplexer_3 (
    .out0(demultiplexer_3_out0), .out1(demultiplexer_3_out1), .in(demultiplexer_1_out1), .sel(full));
  or or_12 (or_12_out, v0, v1, v2, v3, v4, v5, v6, v7);
  Priority_Encoder priority_encoder_1 (
    .in0(v0), .in1(v1), .in2(v2), .in3(v3), .in4(v4), .in5(v5), .in6(v6), .in7(v7),
    .out(priority_encoder_1_out), .en_in(1'b1));  // open: gs, en_out
  Priority_Encoder priority_encoder_2 (
    .in0(hit0), .in1(hit1), .in2(hit2), .in3(hit3), .in4(hit4), .in5(hit5), .in6(hit6), .in7(hit7),
    .out(idxHit), .en_in(1'b1));  // open: gs, en_out
  or or_13 (R_0, demultiplexer_5_out0, demultiplexer_7_out0, demultiplexer_3_out0, LdDirty_0);
  Demultiplexer #(.enable("false")) demultiplexer_4 (
    .out0(demultiplexer_4_out0), .out1(demultiplexer_4_out1), .in(demultiplexer_2_out1), .sel(full));
  and and_11 (full, v0, v1, v2, v3, v4, v5, v6, v7);
  not not_1 (empty, or_12_out);
  or or_14 (hit, hit0, hit1, hit2, hit3, hit4, hit5, hit6, hit7);
  not not_2 (miss, hit);
  Adder #(.width(3)) adder_1 (.a(priority_encoder_1_out), .b(3'b001), .out(adder_1_out));  // open: cin, cout
  D_Flip_Flop read (.clk(in_4), .D(R_0), .Q(read_q), .reset(in_3));  // open: Qn, preset, en
  Demultiplexer #(.enable("false")) demultiplexer_5 (
    .out0(demultiplexer_5_out0), .out1(Finish_3), .in(read_q), .sel(Ready));
  Demultiplexer #(.enable("false")) demultiplexer_6 (
    .out0(demultiplexer_6_out0), .out1(enRnd_0), .in(demultiplexer_4_out1), .sel(d));
  Decoder #(.select(2)) decoder_1 (
    .out0(decoder_1_out0), .out1(decoder_1_out1), .out2(decoder_1_out2), .out3(decoder_1_out3),
    .sel(Address[3:2]));  // open: en
  Multiplexer #(.width(3)) multiplexer_7 (.in0(adder_1_out), .in1(3'b000), .out(idx0), .sel(empty));  // open: en
  assign xnor_5_out = ~(tag3 ^ Address[19:4]);  // XNOR_Gate xnor_5, 16 bits wide
  assign xnor_6_out = ~(tag7 ^ Address[19:4]);  // XNOR_Gate xnor_6, 16 bits wide
  Demultiplexer #(.enable("false")) demultiplexer_7 (
    .out0(demultiplexer_7_out0), .out1(enRnd_1), .in(demultiplexer_3_out1), .sel(d));
  or or_15 (R_1, demultiplexer_8_out0, demultiplexer_4_out0, demultiplexer_6_out0, demultiplexer_9_out1);
  Random_part #(.width(3)) random_1 (.clk(in_4), .next(enRnd), .out(idx1));  // open: clr
  Multiplexer #(.width(3)) multiplexer_8 (.in0(idx0), .in1(idx1), .out(multiplexer_8_out), .sel(full));  // open: en
  assign xnor_7_out = ~(tag1 ^ Address[19:4]);  // XNOR_Gate xnor_7, 16 bits wide
  assign xnor_8_out = ~(tag5 ^ Address[19:4]);  // XNOR_Gate xnor_8, 16 bits wide
  or or_16 (enV_0, demultiplexer_1_out0, Finish_3);
  or or_17 (or_17_out, demultiplexer_10_out0, enRnd_1);
  D_Flip_Flop read_2 (.clk(in_4), .D(R_1), .Q(read_2_q), .reset(in_3));  // open: Qn, preset, en
  or or_18 (or_18_out, btag_1, enRnd_0);
  and and_12 (str0, decoder_1_out0, dirty);
  and and_13 (str1, decoder_1_out1, dirty);
  and and_14 (str2, dirty, decoder_1_out2);
  and and_15 (str3, dirty, decoder_1_out3);
  Multiplexer #(.width(3)) multiplexer_9 (.in0(multiplexer_8_out), .in1(idxHit), .out(idx), .sel(hit));  // open: en
  and and_16 (and_16_out, xnor_7_out[15], xnor_7_out[14], xnor_7_out[13], xnor_7_out[12], xnor_7_out[11], xnor_7_out[10], xnor_7_out[9], xnor_7_out[8], xnor_7_out[7], xnor_7_out[6], xnor_7_out[5], xnor_7_out[4], xnor_7_out[3], xnor_7_out[2], xnor_7_out[1], xnor_7_out[0]);
  and and_17 (hit1, v1, and_16_out);
  and and_18 (and_18_out, xnor_5_out[15], xnor_5_out[14], xnor_5_out[13], xnor_5_out[12], xnor_5_out[11], xnor_5_out[10], xnor_5_out[9], xnor_5_out[8], xnor_5_out[7], xnor_5_out[6], xnor_5_out[5], xnor_5_out[4], xnor_5_out[3], xnor_5_out[2], xnor_5_out[1], xnor_5_out[0]);
  and and_19 (hit3, v3, and_18_out);
  and and_20 (and_20_out, xnor_8_out[15], xnor_8_out[14], xnor_8_out[13], xnor_8_out[12], xnor_8_out[11], xnor_8_out[10], xnor_8_out[9], xnor_8_out[8], xnor_8_out[7], xnor_8_out[6], xnor_8_out[5], xnor_8_out[4], xnor_8_out[3], xnor_8_out[2], xnor_8_out[1], xnor_8_out[0]);
  and and_21 (hit5, v5, and_20_out);
  and and_22 (and_22_out, xnor_6_out[15], xnor_6_out[14], xnor_6_out[13], xnor_6_out[12], xnor_6_out[11], xnor_6_out[10], xnor_6_out[9], xnor_6_out[8], xnor_6_out[7], xnor_6_out[6], xnor_6_out[5], xnor_6_out[4], xnor_6_out[3], xnor_6_out[2], xnor_6_out[1], xnor_6_out[0]);
  and and_23 (hit7, v7, and_22_out);
  D_Flip_Flop wrt (.clk(in_4), .D(or_17_out), .Q(btag_0), .reset(in_3));  // open: Qn, preset, en
  Demultiplexer #(.enable("false")) demultiplexer_8 (
    .out0(demultiplexer_8_out0), .out1(Finish_1), .in(read_2_q), .sel(Ready));
  D_Flip_Flop wrt_2 (.clk(in_4), .D(or_18_out), .Q(wrt_2_q), .reset(in_3));  // open: Qn, preset, en
  Demultiplexer #(.enable("false")) demultiplexer_9 (
    .out0(btag_1), .out1(demultiplexer_9_out1), .in(wrt_2_q), .sel(Ready));
  Decoder #(.select(3)) decoder_2 (
    .out0(decoder_2_out0), .out1(decoder_2_out1), .out2(decoder_2_out2), .out3(decoder_2_out3),
    .out4(decoder_2_out4), .out5(decoder_2_out5), .out6(decoder_2_out6), .out7(decoder_2_out7), .sel(idx),
    .en(enV));
  Demultiplexer #(.enable("false")) demultiplexer_10 (
    .out0(demultiplexer_10_out0), .out1(LdDirty_0), .in(btag_0), .sel(Ready));
  not not_3 (not_3_out, v0);
  assign controlled_buffer_1_out = not_3_out ? decoder_2_out0 : 1'bz;  // Controlled_Buffer controlled_buffer_1
  not not_4 (not_4_out, v1);
  assign controlled_buffer_2_out = not_4_out ? decoder_2_out1 : 1'bz;  // Controlled_Buffer controlled_buffer_2
  not not_5 (not_5_out, v2);
  assign controlled_buffer_3_out = not_5_out ? decoder_2_out2 : 1'bz;  // Controlled_Buffer controlled_buffer_3
  not not_6 (not_6_out, v3);
  assign controlled_buffer_4_out = not_6_out ? decoder_2_out3 : 1'bz;  // Controlled_Buffer controlled_buffer_4
  not not_7 (not_7_out, v4);
  assign controlled_buffer_5_out = not_7_out ? decoder_2_out4 : 1'bz;  // Controlled_Buffer controlled_buffer_5
  not not_8 (not_8_out, v5);
  assign controlled_buffer_6_out = not_8_out ? decoder_2_out5 : 1'bz;  // Controlled_Buffer controlled_buffer_6
  not not_9 (not_9_out, v6);
  assign controlled_buffer_7_out = not_9_out ? decoder_2_out6 : 1'bz;  // Controlled_Buffer controlled_buffer_7
  not not_10 (not_10_out, v7);
  assign controlled_buffer_8_out = not_10_out ? decoder_2_out7 : 1'bz;  // Controlled_Buffer controlled_buffer_8
  Decoder #(.select(3)) decoder_3 (
    .out0(decoder_3_out0), .out1(decoder_3_out1), .out2(decoder_3_out2), .out3(decoder_3_out3),
    .out4(decoder_3_out4), .out5(decoder_3_out5), .out6(decoder_3_out6), .out7(decoder_3_out7), .sel(idx));  // open: en
  D_Flip_Flop d_ff_1 (.clk(in_4), .D(Finish_1), .Q(d_ff_1_q), .reset(in_3));  // open: Qn, preset, en
  D_Flip_Flop d_ff_2 (.clk(in_4), .D(controlled_buffer_1_out), .Q(v0), .reset(in_3));  // open: Qn, preset, en
  D_Flip_Flop d_ff_3 (.clk(in_4), .D(controlled_buffer_2_out), .Q(v1), .reset(in_3));  // open: Qn, preset, en
  D_Flip_Flop d_ff_4 (.clk(in_4), .D(controlled_buffer_3_out), .Q(v2), .reset(in_3));  // open: Qn, preset, en
  D_Flip_Flop d_ff_5 (.clk(in_4), .D(controlled_buffer_4_out), .Q(v3), .reset(in_3));  // open: Qn, preset, en
  D_Flip_Flop d_ff_6 (.clk(in_4), .D(controlled_buffer_5_out), .Q(v4), .reset(in_3));  // open: Qn, preset, en
  D_Flip_Flop d_ff_7 (.clk(in_4), .D(controlled_buffer_6_out), .Q(v5), .reset(in_3));  // open: Qn, preset, en
  D_Flip_Flop d_ff_8 (.clk(in_4), .D(controlled_buffer_7_out), .Q(v6), .reset(in_3));  // open: Qn, preset, en
  D_Flip_Flop d_ff_9 (.clk(in_4), .D(controlled_buffer_8_out), .Q(v7), .reset(in_3));  // open: Qn, preset, en
  and and_24 (en0, decoder_3_out0, Finish);
  and and_25 (en1, decoder_3_out1, Finish);
  and and_26 (en2, decoder_3_out2, Finish);
  and and_27 (en3, decoder_3_out3, Finish);
  and and_28 (en4, Finish, decoder_3_out4);
  and and_29 (en5, Finish, decoder_3_out5);
  and and_30 (en6, Finish, decoder_3_out6);
  and and_31 (en7, Finish, decoder_3_out7);
  or or_19 (dirty, demultiplexer_2_out0, d_ff_1_q);
  Multiplexer #(.width(4)) multiplexer_10 (
    .in0(WriteTime), .in1(ReadTime), .out(multiplexer_10_out), .sel(R));  // open: en
  Decoder #(.select(3)) decoder_4 (
    .out0(decoder_4_out0), .out1(decoder_4_out1), .out2(decoder_4_out2), .out3(decoder_4_out3),
    .out4(decoder_4_out4), .out5(decoder_4_out5), .out6(decoder_4_out6), .out7(decoder_4_out7), .sel(idx));  // open: en
  D_Flip_Flop d_ff_10 (.clk(in_4), .D(enV_0), .Q(FinishRead));  // open: Qn, preset, en, reset
  D_Flip_Flop d_ff_11 (.clk(in_4), .D(dirty), .Q(FinishWrt));  // open: Qn, preset, en, reset
  or or_20 (Finish, Finish_3, Finish_1);
  Register #(.width(1)) register_9 (.D(dirty), .en(enDirty0), .Q(d0), .clk(in_4), .clr(in_3));
  Register #(.width(1)) register_10 (.D(dirty), .en(enDirty1), .Q(d1), .clk(in_4), .clr(in_3));
  Register #(.width(1)) register_11 (.D(dirty), .en(enDirty2), .Q(d2), .clk(in_4), .clr(in_3));
  Register #(.width(1)) register_12 (.D(dirty), .en(enDirty3), .Q(d3), .clk(in_4), .clr(in_3));
  Multiplexer #(.select(3), .width(16)) multiplexer_11 (
    .in0(tag0), .in1(tag1), .in2(tag2), .in3(tag3), .in4(tag4), .in5(tag5), .in6(tag6), .in7(tag7),
    .out(tagAddr), .sel(idx));  // open: en
  \wait  wait_1 (.Start(start), .Clear(in_3), .CLK(in_4), .\time (multiplexer_10_out), .out_5(Ready), .out_6(CS));
  and and_32 (enDirty0, decoder_4_out0, LdDirty);
  and and_33 (enDirty1, decoder_4_out1, LdDirty);
  and and_34 (enDirty2, decoder_4_out2, LdDirty);
  and and_35 (enDirty3, decoder_4_out3, LdDirty);
  and and_36 (enDirty4, LdDirty, decoder_4_out4);
  and and_37 (enDirty5, LdDirty, decoder_4_out5);
  and and_38 (enDirty6, LdDirty, decoder_4_out6);
  and and_39 (enDirty7, LdDirty, decoder_4_out7);
  Register #(.width(1)) register_13 (.D(dirty), .en(enDirty4), .Q(d4), .clk(in_4), .clr(in_3));
  Register #(.width(1)) register_14 (.D(dirty), .en(enDirty5), .Q(d5), .clk(in_4), .clr(in_3));
  Register #(.width(1)) register_15 (.D(dirty), .en(enDirty6), .Q(d6), .clk(in_4), .clr(in_3));
  Register #(.width(1)) register_16 (.D(dirty), .en(enDirty7), .Q(d7), .clk(in_4), .clr(in_3));

  assign Mask = 4'b1111;

  // Other names for the same wires on the sheet: offset[1:0] = Address[3:2]; Address_t[15:0] = Address[19:4];
  //   tag[15:0] = Address[19:4]; Clear = in_3; CLK = in_4; Enable = in_2; Finish_0 = enV_0; R_W = in_5;
  //   r_w_0 = btag_0; r_w_1 = btag_1; RAM_OUTPUT_0[31:0] = RAM_Out_0; RAM_OUTPUT_1[31:0] = RAM_Out_1;
  //   RAM_OUTPUT_2[31:0] = RAM_Out_2; RAM_OUTPUT_3[31:0] = RAM_Out_3; Read_Time[3:0] = ReadTime; enV_1 = dirty;
  //   Finish_2 = dirty; LdDirty_1 = dirty; selVal = dirty; start_0 = R_0; start_1 = enRnd_1; start_2 = R_1;
  //   start_3 = enRnd_0; Value_t[31:0] = {Value[7:0], Value[15:8], Value[23:16], Value[31:24]};
  //   Write_Time[3:0] = WriteTime

  // Notes on the sheet:
  //   DATA FROM RAM
  //   RAM TIMING
  //   RAM CONTROL
  //   Bank 0
  //   Bank 1
  //   Bank 2
  //   Bank 3
  //   Reading
  //   Writing
endmodule
