// Logisim project cp2.circ as structural Verilog
module semisumador (
  input  in_1,
  input  in_2,
  output out_3,
  output out_4
);

  xor xor_1 (out_3, in_1, in_2);
  and and_1 (out_4, in_1, in_2);

  // Other names for the same wires on the sheet: bit_a = in_1; bit_b = in_2
endmodule

module sumador (
  input  in_1,
  input  in_2,
  input  in_3,
  output out_4,
  output out_5
);

  wire semisumador_1_out_3, semisumador_1_out_4, semisumador_2_out_4;

  semisumador semisumador_1 (.in_1(in_1), .in_2(in_2), .out_3(semisumador_1_out_3), .out_4(semisumador_1_out_4));
  semisumador semisumador_2 (.in_1(semisumador_1_out_3), .in_2(in_3), .out_3(out_4), .out_4(semisumador_2_out_4));
  or or_1 (out_5, semisumador_2_out_4, semisumador_1_out_4);

  // Other names for the same wires on the sheet: bit_a = in_1; bit_b = in_2; Carry = in_3
endmodule

module sumador_8bits (
  input  [7:0] in_1,
  input  [7:0] in_2,
  output [7:0] out_3,
  output out_4
);

  wire sumador_1_out_5, sumador_2_out_5, sumador_3_out_5, sumador_4_out_5, sumador_5_out_5, sumador_6_out_5,
       sumador_7_out_5;

  // Probe on in_1
  // Probe on in_2
  sumador sumador_1 (.in_1(in_1[0]), .in_2(in_2[0]), .in_3(1'b0), .out_4(out_3[0]), .out_5(sumador_1_out_5));
  sumador sumador_2 (.in_1(in_1[1]), .in_2(in_2[1]), .in_3(sumador_1_out_5), .out_4(out_3[1]), .out_5(sumador_2_out_5));
  sumador sumador_3 (.in_1(in_1[2]), .in_2(in_2[2]), .in_3(sumador_2_out_5), .out_4(out_3[2]), .out_5(sumador_3_out_5));
  sumador sumador_4 (.in_1(in_1[3]), .in_2(in_2[3]), .in_3(sumador_3_out_5), .out_4(out_3[3]), .out_5(sumador_4_out_5));
  sumador sumador_5 (.in_1(in_1[4]), .in_2(in_2[4]), .in_3(sumador_4_out_5), .out_4(out_3[4]), .out_5(sumador_5_out_5));
  sumador sumador_6 (.in_1(in_1[5]), .in_2(in_2[5]), .in_3(sumador_5_out_5), .out_4(out_3[5]), .out_5(sumador_6_out_5));
  sumador sumador_7 (.in_1(in_1[6]), .in_2(in_2[6]), .in_3(sumador_6_out_5), .out_4(out_3[6]), .out_5(sumador_7_out_5));
  sumador sumador_8 (.in_1(in_1[7]), .in_2(in_2[7]), .in_3(sumador_7_out_5), .out_4(out_3[7]), .out_5(out_4));
  // Probe on out_3
endmodule

module sumador_4bits (
  input  [3:0] in_1,
  input  [3:0] in_2,
  output [3:0] out_3,
  output out_4
);

  wire sumador_1_out_5, sumador_2_out_5, sumador_3_out_5;

  // Probe on in_1
  // Probe on in_2
  sumador sumador_1 (.in_1(in_1[0]), .in_2(in_2[0]), .in_3(1'b0), .out_4(out_3[0]), .out_5(sumador_1_out_5));
  sumador sumador_2 (.in_1(in_1[1]), .in_2(in_2[1]), .in_3(sumador_1_out_5), .out_4(out_3[1]), .out_5(sumador_2_out_5));
  sumador sumador_3 (.in_1(in_1[2]), .in_2(in_2[2]), .in_3(sumador_2_out_5), .out_4(out_3[2]), .out_5(sumador_3_out_5));
  sumador sumador_4 (.in_1(in_1[3]), .in_2(in_2[3]), .in_3(sumador_3_out_5), .out_4(out_3[3]), .out_5(out_4));
  // Probe on out_3
endmodule

module restador_4bits (
  input  [3:0] in_1,
  input  [3:0] in_2,
  output [3:0] out_3,
  output out_4
);

  wire sumador_1_out_5, sumador_2_out_5, sumador_3_out_5, sumador_4_out_5;
  wire [3:0] not_1_out;

  // Probe on in_1
  // Probe on not_1_out
  assign not_1_out = ~in_2;  // NOT_Gate not_1, 4 bits wide
  sumador sumador_1 (.in_1(in_1[0]), .in_2(not_1_out[0]), .in_3(1'b1), .out_4(out_3[0]), .out_5(sumador_1_out_5));
  sumador sumador_2 (
    .in_1(in_1[1]), .in_2(not_1_out[1]), .in_3(sumador_1_out_5), .out_4(out_3[1]), .out_5(sumador_2_out_5));
  sumador sumador_3 (
    .in_1(in_1[2]), .in_2(not_1_out[2]), .in_3(sumador_2_out_5), .out_4(out_3[2]), .out_5(sumador_3_out_5));
  sumador sumador_4 (
    .in_1(in_1[3]), .in_2(not_1_out[3]), .in_3(sumador_3_out_5), .out_4(out_3[3]), .out_5(sumador_4_out_5));
  // Probe on out_3
  not not_2 (out_4, sumador_4_out_5);
endmodule

module ALU (
  input  [3:0] in_1,
  input  [3:0] in_2,
  input  in_3,
  input  in_4,
  output [3:0] out_5
);

  wire And, Or, Resta, Suma;
  wire [3:0] and_1_out, and_2_out, and_6_out, and_10_out, and_14_out, or_1_out, restador_4bits_1_out_3,
       sumador_4bits_1_out_3;

  decoder decoder_1 (.in_1(in_3), .in_2(in_4), .out_3(Or), .out_4(Resta), .out_5(And), .out_6(Suma));
  assign and_1_out = in_2 & in_1;  // AND_Gate and_1, 4 bits wide
  assign or_1_out = in_2 | in_1;  // OR_Gate or_1, 4 bits wide
  restador_4bits restador_4bits_1 (.in_1(in_1), .in_2(in_2), .out_3(restador_4bits_1_out_3));  // open: out_4
  sumador_4bits sumador_4bits_1 (.in_1(in_2), .in_2(in_1), .out_3(sumador_4bits_1_out_3));  // open: out_4
  and and_2 (and_2_out[0], restador_4bits_1_out_3[0], Resta);
  and and_3 (and_2_out[1], restador_4bits_1_out_3[1], Resta);
  and and_4 (and_2_out[2], restador_4bits_1_out_3[2], Resta);
  and and_5 (and_2_out[3], restador_4bits_1_out_3[3], Resta);
  and and_6 (and_6_out[0], sumador_4bits_1_out_3[0], Suma);
  and and_7 (and_6_out[1], sumador_4bits_1_out_3[1], Suma);
  and and_8 (and_6_out[2], sumador_4bits_1_out_3[2], Suma);
  and and_9 (and_6_out[3], sumador_4bits_1_out_3[3], Suma);
  and and_10 (and_10_out[0], and_1_out[0], And);
  and and_11 (and_10_out[1], and_1_out[1], And);
  and and_12 (and_10_out[2], and_1_out[2], And);
  and and_13 (and_10_out[3], and_1_out[3], And);
  and and_14 (and_14_out[0], or_1_out[0], Or);
  and and_15 (and_14_out[1], or_1_out[1], Or);
  and and_16 (and_14_out[2], or_1_out[2], Or);
  and and_17 (and_14_out[3], or_1_out[3], Or);
  assign out_5 = and_2_out | and_6_out | and_10_out | and_14_out;  // OR_Gate or_2, 4 bits wide
  // Probe on out_5
endmodule

module decoder (
  input  in_1,
  input  in_2,
  output out_3,
  output out_4,
  output out_5,
  output out_6
);

  wire not_1_out, not_2_out;

  not not_1 (not_1_out, in_1);
  not not_2 (not_2_out, in_2);
  and and_1 (out_3, in_1, in_2);
  and and_2 (out_4, not_1_out, in_2);
  and and_3 (out_5, in_1, not_2_out);
  and and_4 (out_6, not_1_out, not_2_out);
endmodule
