// Logisim project cp2_javier_oramas.circ as structural Verilog: 17 circuits, main circuit main
module main (
  input  [3:0] in_1,
  input  [3:0] in_2,
  input  in_3,
  output [3:0] out_4,
  output [3:0] out_5,
  output [3:0] out_6,
  output [3:0] out_7,
  output [3:0] out_8,
  output [3:0] out_9,
  output [3:0] out_10,
  output [3:0] out_11,
  output [3:0] out_12,
  output [3:0] out_13,
  output [3:0] out_14,
  output [3:0] out_15,
  output [3:0] out_16,
  output [3:0] out_17,
  output [3:0] out_18,
  output [3:0] out_19
);

  wire [3:0] and_1_out, demultiplexer_1_out0, demultiplexer_1_out1, demultiplexer_1_out2,
       demultiplexer_1_out3, demultiplexer_1_out4, demultiplexer_1_out5, demultiplexer_1_out6,
       demultiplexer_1_out7, demultiplexer_1_out8, demultiplexer_1_out9, demultiplexer_1_out10,
       demultiplexer_1_out11, demultiplexer_1_out12, demultiplexer_1_out13, demultiplexer_1_out14,
       demultiplexer_1_out15, demultiplexer_16num_4bits_1_out_4, demultiplexer_16num_4bits_1_out_5,
       demultiplexer_16num_4bits_1_out_6, demultiplexer_16num_4bits_1_out_7,
       demultiplexer_16num_4bits_1_out_8, demultiplexer_16num_4bits_1_out_9,
       demultiplexer_16num_4bits_1_out_10, demultiplexer_16num_4bits_1_out_11,
       demultiplexer_16num_4bits_1_out_12, demultiplexer_16num_4bits_1_out_13,
       demultiplexer_16num_4bits_1_out_14, demultiplexer_16num_4bits_1_out_15,
       demultiplexer_16num_4bits_1_out_16, demultiplexer_16num_4bits_1_out_17,
       demultiplexer_16num_4bits_1_out_18, demultiplexer_16num_4bits_1_out_19;

  assign and_1_out = in_1 & {4{in_3}};  // AND_Gate and_1, 4 bits wide
  Demultiplexer #(.select(4), .width(4), .enable("false")) demultiplexer_1 (
    .out0(demultiplexer_1_out0), .out1(demultiplexer_1_out1), .out2(demultiplexer_1_out2),
    .out3(demultiplexer_1_out3), .out4(demultiplexer_1_out4), .out5(demultiplexer_1_out5),
    .out6(demultiplexer_1_out6), .out7(demultiplexer_1_out7), .out8(demultiplexer_1_out8),
    .out9(demultiplexer_1_out9), .out10(demultiplexer_1_out10), .out11(demultiplexer_1_out11),
    .out12(demultiplexer_1_out12), .out13(demultiplexer_1_out13), .out14(demultiplexer_1_out14),
    .out15(demultiplexer_1_out15), .in(and_1_out), .sel(in_2));
  demultiplexer_16num_4bits demultiplexer_16num_4bits_1 (
    .in_1(and_1_out), .out_4(demultiplexer_16num_4bits_1_out_4), .out_5(demultiplexer_16num_4bits_1_out_5),
    .out_6(demultiplexer_16num_4bits_1_out_6), .out_7(demultiplexer_16num_4bits_1_out_7),
    .out_8(demultiplexer_16num_4bits_1_out_8), .out_9(demultiplexer_16num_4bits_1_out_9),
    .out_10(demultiplexer_16num_4bits_1_out_10), .out_11(demultiplexer_16num_4bits_1_out_11),
    .out_12(demultiplexer_16num_4bits_1_out_12), .out_13(demultiplexer_16num_4bits_1_out_13),
    .out_14(demultiplexer_16num_4bits_1_out_14), .out_15(demultiplexer_16num_4bits_1_out_15),
    .out_16(demultiplexer_16num_4bits_1_out_16), .out_17(demultiplexer_16num_4bits_1_out_17),
    .out_18(demultiplexer_16num_4bits_1_out_18), .out_19(demultiplexer_16num_4bits_1_out_19), .in_3(in_2));  // open: in_2
  assign out_4 = demultiplexer_1_out0 & demultiplexer_16num_4bits_1_out_4;  // AND_Gate and_2, 4 bits wide
  assign out_5 = demultiplexer_1_out1 & demultiplexer_16num_4bits_1_out_5;  // AND_Gate and_3, 4 bits wide
  assign out_6 = demultiplexer_1_out2 & demultiplexer_16num_4bits_1_out_6;  // AND_Gate and_4, 4 bits wide
  assign out_7 = demultiplexer_16num_4bits_1_out_7 & demultiplexer_1_out3;  // AND_Gate and_5, 4 bits wide
  assign out_8 = demultiplexer_16num_4bits_1_out_8 & demultiplexer_1_out4;  // AND_Gate and_6, 4 bits wide
  assign out_9 = demultiplexer_16num_4bits_1_out_9 & demultiplexer_1_out5;  // AND_Gate and_7, 4 bits wide
  assign out_10 = demultiplexer_16num_4bits_1_out_10 & demultiplexer_1_out6;  // AND_Gate and_8, 4 bits wide
  assign out_11 = demultiplexer_16num_4bits_1_out_11 & demultiplexer_1_out7;  // AND_Gate and_9, 4 bits wide
  assign out_12 = demultiplexer_16num_4bits_1_out_12 & demultiplexer_1_out8;  // AND_Gate and_10, 4 bits wide
  assign out_13 = demultiplexer_16num_4bits_1_out_13 & demultiplexer_1_out9;  // AND_Gate and_11, 4 bits wide
  assign out_14 = demultiplexer_16num_4bits_1_out_14 & demultiplexer_1_out10;  // AND_Gate and_12, 4 bits wide
  assign out_15 = demultiplexer_16num_4bits_1_out_15 & demultiplexer_1_out11;  // AND_Gate and_13, 4 bits wide
  assign out_16 = demultiplexer_16num_4bits_1_out_16 & demultiplexer_1_out12;  // AND_Gate and_14, 4 bits wide
  assign out_17 = demultiplexer_16num_4bits_1_out_17 & demultiplexer_1_out13;  // AND_Gate and_15, 4 bits wide
  assign out_18 = demultiplexer_16num_4bits_1_out_18 & demultiplexer_1_out14;  // AND_Gate and_16, 4 bits wide
  assign out_19 = demultiplexer_16num_4bits_1_out_19 & demultiplexer_1_out15;  // AND_Gate and_17, 4 bits wide
endmodule

module semisumador (
  input  in_1,
  input  in_2,
  output out_3,
  output out_4
);

  xor xor_1 (out_3, in_1, in_2);
  and and_1 (out_4, in_1, in_2);

  // Other names for the same wires on the sheet: bit_a = in_1; bit_b = in_2
endmodule

module sumador (
  input  in_1,
  input  in_2,
  input  in_3,
  output out_4,
  output out_5
);

  wire semisumador_1_out_3, semisumador_1_out_4, semisumador_2_out_4;

  semisumador semisumador_1 (.in_1(in_1), .in_2(in_2), .out_3(semisumador_1_out_3), .out_4(semisumador_1_out_4));
  semisumador semisumador_2 (.in_1(semisumador_1_out_3), .in_2(in_3), .out_3(out_4), .out_4(semisumador_2_out_4));
  or or_1 (out_5, semisumador_2_out_4, semisumador_1_out_4);

  // Other names for the same wires on the sheet: bit_a = in_1; bit_b = in_2; Carry = in_3
endmodule

module sumador_8bits (
  input  [7:0] in_1,
  input  [7:0] in_2,
  output [7:0] out_3,
  output out_4
);

  wire sumador_1_out_5, sumador_2_out_5, sumador_3_out_5, sumador_4_out_5, sumador_5_out_5, sumador_6_out_5,
       sumador_7_out_5;

  // Probe on in_1
  // Probe on in_2
  sumador sumador_1 (.in_1(in_1[0]), .in_2(in_2[0]), .in_3(1'b0), .out_4(out_3[0]), .out_5(sumador_1_out_5));
  sumador sumador_2 (.in_1(in_1[1]), .in_2(in_2[1]), .in_3(sumador_1_out_5), .out_4(out_3[1]), .out_5(sumador_2_out_5));
  sumador sumador_3 (.in_1(in_1[2]), .in_2(in_2[2]), .in_3(sumador_2_out_5), .out_4(out_3[2]), .out_5(sumador_3_out_5));
  sumador sumador_4 (.in_1(in_1[3]), .in_2(in_2[3]), .in_3(sumador_3_out_5), .out_4(out_3[3]), .out_5(sumador_4_out_5));
  sumador sumador_5 (.in_1(in_1[4]), .in_2(in_2[4]), .in_3(sumador_4_out_5), .out_4(out_3[4]), .out_5(sumador_5_out_5));
  sumador sumador_6 (.in_1(in_1[5]), .in_2(in_2[5]), .in_3(sumador_5_out_5), .out_4(out_3[5]), .out_5(sumador_6_out_5));
  sumador sumador_7 (.in_1(in_1[6]), .in_2(in_2[6]), .in_3(sumador_6_out_5), .out_4(out_3[6]), .out_5(sumador_7_out_5));
  sumador sumador_8 (.in_1(in_1[7]), .in_2(in_2[7]), .in_3(sumador_7_out_5), .out_4(out_3[7]), .out_5(out_4));
  // Probe on out_3
endmodule

module sumador_4bits (
  input  [3:0] in_1,
  input  [3:0] in_2,
  output [3:0] out_3,
  output out_4
);

  wire sumador_1_out_5, sumador_2_out_5, sumador_3_out_5;

  // Probe on in_1
  // Probe on in_2
  sumador sumador_1 (.in_1(in_1[0]), .in_2(in_2[0]), .in_3(1'b0), .out_4(out_3[0]), .out_5(sumador_1_out_5));
  sumador sumador_2 (.in_1(in_1[1]), .in_2(in_2[1]), .in_3(sumador_1_out_5), .out_4(out_3[1]), .out_5(sumador_2_out_5));
  sumador sumador_3 (.in_1(in_1[2]), .in_2(in_2[2]), .in_3(sumador_2_out_5), .out_4(out_3[2]), .out_5(sumador_3_out_5));
  sumador sumador_4 (.in_1(in_1[3]), .in_2(in_2[3]), .in_3(sumador_3_out_5), .out_4(out_3[3]), .out_5(out_4));
  // Probe on out_3
endmodule

module restador_4bits (
  input  [3:0] in_1,
  input  [3:0] in_2,
  output [3:0] out_3,
  output out_4
);

  wire sumador_1_out_5, sumador_2_out_5, sumador_3_out_5, sumador_4_out_5;
  wire [3:0] not_1_out;

  // Probe on in_1
  // Probe on not_1_out
  assign not_1_out = ~in_2;  // NOT_Gate not_1, 4 bits wide
  sumador sumador_1 (.in_1(in_1[0]), .in_2(not_1_out[0]), .in_3(1'b1), .out_4(out_3[0]), .out_5(sumador_1_out_5));
  sumador sumador_2 (
    .in_1(in_1[1]), .in_2(not_1_out[1]), .in_3(sumador_1_out_5), .out_4(out_3[1]), .out_5(sumador_2_out_5));
  sumador sumador_3 (
    .in_1(in_1[2]), .in_2(not_1_out[2]), .in_3(sumador_2_out_5), .out_4(out_3[2]), .out_5(sumador_3_out_5));
  sumador sumador_4 (
    .in_1(in_1[3]), .in_2(not_1_out[3]), .in_3(sumador_3_out_5), .out_4(out_3[3]), .out_5(sumador_4_out_5));
  // Probe on out_3
  not not_2 (out_4, sumador_4_out_5);
endmodule

module ALU (
  input  [3:0] in_1,
  input  [3:0] in_2,
  input  [1:0] in_3,
  output [3:0] out_4
);

  wire [3:0] and_1_out, or_1_out, restador_4bits_1_out_3, sumador_4bits_1_out_3;

  assign and_1_out = in_2 & in_1;  // AND_Gate and_1, 4 bits wide
  assign or_1_out = in_2 | in_1;  // OR_Gate or_1, 4 bits wide
  sumador_4bits sumador_4bits_1 (.in_1(in_1), .in_2(in_2), .out_3(sumador_4bits_1_out_3));  // open: out_4
  restador_4bits restador_4bits_1 (.in_1(in_1), .in_2(in_2), .out_3(restador_4bits_1_out_3));  // open: out_4
  multiplexer_4num_4bits multiplexer_4num_4bits_1 (
    .in_1(sumador_4bits_1_out_3), .in_2(restador_4bits_1_out_3), .in_3(and_1_out), .in_4(or_1_out),
    .out_7(out_4), .in_6(in_3));  // open: in_5
  // Probe on out_4
endmodule

module decoder (
  input  in_1,
  input  in_2,
  output out_3,
  output out_4,
  output out_5,
  output out_6
);

  wire not_1_out, not_2_out;

  not not_1 (not_1_out, in_1);
  not not_2 (not_2_out, in_2);
  and and_1 (out_3, in_1, in_2);
  and and_2 (out_4, not_1_out, in_2);
  and and_3 (out_5, in_1, not_2_out);
  and and_4 (out_6, not_1_out, not_2_out);
endmodule

module multiplexer_2num_4bits (
  input  [3:0] in_1,
  input  [3:0] in_2,
  input  in_3,
  input  in_4,
  output [3:0] out_5
);

  wire not_1_out, not_2_out, not_3_out, not_4_out;
  wire [3:0] and_1_out, and_5_out, or_1_out;

  not not_1 (not_1_out, in_4);
  not not_2 (not_2_out, in_4);
  not not_3 (not_3_out, in_4);
  not not_4 (not_4_out, in_4);
  and and_1 (and_1_out[0], in_1[0], not_1_out);
  and and_2 (and_1_out[1], in_1[1], not_2_out);
  and and_3 (and_1_out[2], in_1[2], not_3_out);
  and and_4 (and_1_out[3], in_1[3], not_4_out);
  and and_5 (and_5_out[0], in_2[0], in_4);
  and and_6 (and_5_out[1], in_2[1], in_4);
  and and_7 (and_5_out[2], in_2[2], in_4);
  and and_8 (and_5_out[3], in_2[3], in_4);
  assign or_1_out = and_1_out | and_5_out;  // OR_Gate or_1, 4 bits wide
  assign out_5 = or_1_out & {4{in_3}};  // AND_Gate and_9, 4 bits wide
endmodule

module multiplexer_4num_4bits (
  input  [3:0] in_1,
  input  [3:0] in_2,
  input  [3:0] in_3,
  input  [3:0] in_4,
  input  in_5,
  input  [1:0] in_6,
  output [3:0] out_7
);

  wire selector_2;
  wire [3:0] multiplexer_2num_4bits_1_out_5, multiplexer_2num_4bits_2_out_5, multiplexer_2num_4bits_3_out_5;

  multiplexer_2num_4bits multiplexer_2num_4bits_1 (
    .in_1(in_1), .in_2(in_2), .out_5(multiplexer_2num_4bits_1_out_5), .in_4(in_6[0]));  // open: in_3
  multiplexer_2num_4bits multiplexer_2num_4bits_2 (
    .in_1(in_3), .in_2(in_4), .out_5(multiplexer_2num_4bits_2_out_5), .in_4(selector_2));  // open: in_3
  multiplexer_2num_4bits multiplexer_2num_4bits_3 (
    .in_1(multiplexer_2num_4bits_1_out_5), .in_2(multiplexer_2num_4bits_2_out_5),
    .out_5(multiplexer_2num_4bits_3_out_5), .in_4(in_6[1]));  // open: in_3
  and and_1 (selector_2, in_6[0], in_6[1]);
  assign out_7 = multiplexer_2num_4bits_3_out_5 & {4{in_5}};  // AND_Gate and_2, 4 bits wide

  // Other names for the same wires on the sheet: selector_1 = in_6[0]; selector_3 = in_6[1]
endmodule

module multiplexer_16num_4_bits (
  input  [3:0] in_1,
  input  [3:0] in_2,
  input  [3:0] in_3,
  input  [3:0] in_4,
  input  [3:0] in_5,
  input  [3:0] in_6,
  input  [3:0] in_7,
  input  [3:0] in_8,
  input  [3:0] in_9,
  input  [3:0] in_10,
  input  [3:0] in_11,
  input  [3:0] in_12,
  input  [3:0] in_13,
  input  [3:0] in_14,
  input  [3:0] in_15,
  input  [3:0] in_16,
  input  in_17,
  input  [3:0] in_18,
  output [3:0] out_19
);

  wire [3:0] multiplexer_2num_4bits_1_out_5, multiplexer_8num_4bits_1_out_11, multiplexer_8num_4bits_2_out_11;

  multiplexer_8num_4bits multiplexer_8num_4bits_1 (
    .in_1(in_1), .in_2(in_2), .in_3(in_3), .in_4(in_4), .in_5(in_5), .in_6(in_6), .in_7(in_7), .in_8(in_8),
    .out_11(multiplexer_8num_4bits_1_out_11), .in_10(in_18[2:0]));  // open: in_9
  multiplexer_8num_4bits multiplexer_8num_4bits_2 (
    .in_1(in_9), .in_2(in_10), .in_3(in_11), .in_4(in_12), .in_5(in_13), .in_6(in_14), .in_7(in_15),
    .in_8(in_16), .out_11(multiplexer_8num_4bits_2_out_11), .in_10(in_18[2:0]));  // open: in_9
  multiplexer_2num_4bits multiplexer_2num_4bits_1 (
    .in_1(multiplexer_8num_4bits_1_out_11), .in_2(multiplexer_8num_4bits_2_out_11),
    .out_5(multiplexer_2num_4bits_1_out_5), .in_4(in_18[3]));  // open: in_3
  assign out_19 = multiplexer_2num_4bits_1_out_5 & {4{in_17}};  // AND_Gate and_1, 4 bits wide

  // Other names for the same wires on the sheet: selector_2 = in_18[3]; selector_1[2:0] = in_18[2:0]
endmodule

module multiplexer_8num_4bits (
  input  [3:0] in_1,
  input  [3:0] in_2,
  input  [3:0] in_3,
  input  [3:0] in_4,
  input  [3:0] in_5,
  input  [3:0] in_6,
  input  [3:0] in_7,
  input  [3:0] in_8,
  input  in_9,
  input  [2:0] in_10,
  output [3:0] out_11
);

  wire [3:0] multiplexer_2num_4bits_1_out_5, multiplexer_4num_4bits_1_out_7, multiplexer_4num_4bits_2_out_7;

  multiplexer_4num_4bits multiplexer_4num_4bits_1 (
    .in_1(in_1), .in_2(in_2), .in_3(in_3), .in_4(in_4), .out_7(multiplexer_4num_4bits_1_out_7),
    .in_6(in_10[1:0]));  // open: in_5
  multiplexer_4num_4bits multiplexer_4num_4bits_2 (
    .in_1(in_5), .in_2(in_6), .in_3(in_7), .in_4(in_8), .out_7(multiplexer_4num_4bits_2_out_7),
    .in_6(in_10[1:0]));  // open: in_5
  multiplexer_2num_4bits multiplexer_2num_4bits_1 (
    .in_1(multiplexer_4num_4bits_1_out_7), .in_2(multiplexer_4num_4bits_2_out_7),
    .out_5(multiplexer_2num_4bits_1_out_5), .in_4(in_10[2]));  // open: in_3
  assign out_11 = multiplexer_2num_4bits_1_out_5 & {4{in_9}};  // AND_Gate and_1, 4 bits wide

  // Other names for the same wires on the sheet: selector_1[1:0] = in_10[1:0]
endmodule

module demultiplexer_2num_4bits (
  input  [3:0] in_1,
  input  in_2,
  input  in_3,
  output [3:0] out_4,
  output [3:0] out_5
);

  wire not_1_out, not_2_out, not_3_out, not_4_out;
  wire [3:0] and_1_out;

  assign and_1_out = in_1 & {4{in_2}};  // AND_Gate and_1, 4 bits wide
  not not_1 (not_1_out, in_3);
  not not_2 (not_2_out, in_3);
  not not_3 (not_3_out, in_3);
  not not_4 (not_4_out, in_3);
  and and_2 (out_4[0], and_1_out[0], not_1_out);
  and and_3 (out_4[1], and_1_out[1], not_2_out);
  and and_4 (out_4[2], and_1_out[2], not_3_out);
  and and_5 (out_4[3], and_1_out[3], not_4_out);
  and and_6 (out_5[0], and_1_out[0], in_3);
  and and_7 (out_5[1], and_1_out[1], in_3);
  and and_8 (out_5[2], and_1_out[2], in_3);
  and and_9 (out_5[3], and_1_out[3], in_3);
endmodule

module demultiplexer_4num_4bits (
  input  [3:0] in_1,
  input  in_2,
  input  [1:0] in_3,
  output [3:0] out_4,
  output [3:0] out_5,
  output [3:0] out_6,
  output [3:0] out_7
);

  wire and_3_out, and_5_out, and_7_out, and_9_out, s1_n, s2_n;
  wire [3:0] and_1_out, and_2_out, and_4_out, and_6_out, and_8_out;
  wire [3:3] not_3_out, not_4_out, not_5_out, not_6_out;

  assign and_1_out = in_1 & {4{in_2}};  // AND_Gate and_1, 4 bits wide
  not not_1 (s2_n, in_3[1]);
  not not_2 (s1_n, in_3[0]);
  assign and_2_out = and_1_out & {4{not_3_out[3]}};  // AND_Gate and_2, 4 bits wide
  not not_3 (not_3_out[3], and_3_out);
  and and_3 (and_3_out, in_3[1], in_3[0]);
  assign out_7 = and_1_out ^ and_2_out;  // XOR_Gate xor_1, 4 bits wide
  assign out_6 = and_1_out ^ and_4_out;  // XOR_Gate xor_2, 4 bits wide
  assign and_4_out = and_1_out & {4{not_4_out[3]}};  // AND_Gate and_4, 4 bits wide
  not not_4 (not_4_out[3], and_5_out);
  and and_5 (and_5_out, in_3[1], s1_n);
  assign and_6_out = and_1_out & {4{not_5_out[3]}};  // AND_Gate and_6, 4 bits wide
  not not_5 (not_5_out[3], and_7_out);
  and and_7 (and_7_out, s2_n, in_3[0]);
  assign out_5 = and_1_out ^ and_6_out;  // XOR_Gate xor_3, 4 bits wide
  assign and_8_out = and_1_out & {4{not_6_out[3]}};  // AND_Gate and_8, 4 bits wide
  not not_6 (not_6_out[3], and_9_out);
  and and_9 (and_9_out, s2_n, s1_n);
  assign out_4 = and_1_out ^ and_8_out;  // XOR_Gate xor_4, 4 bits wide

  // Other names for the same wires on the sheet: s1 = in_3[0]; s2 = in_3[1]
endmodule

module demultiplexer_8num_4bits (
  input  [3:0] in_1,
  input  in_2,
  input  [2:0] in_3,
  output [3:0] out_4,
  output [3:0] out_5,
  output [3:0] out_6,
  output [3:0] out_7,
  output [3:0] out_8,
  output [3:0] out_9,
  output [3:0] out_10,
  output [3:0] out_11
);

  wire and_3_out, and_5_out, and_7_out, and_9_out, and_11_out, and_13_out, and_15_out, and_17_out, s1_n,
       s2_n, s3_n;
  wire [3:0] and_1_out, and_2_out, and_4_out, and_6_out, and_8_out, and_10_out, and_12_out, and_14_out,
       and_16_out;
  wire [3:3] not_1_out, not_3_out, not_6_out, not_7_out, not_8_out, not_9_out, not_10_out, not_11_out;

  assign and_1_out = in_1 & {4{in_2}};  // AND_Gate and_1, 4 bits wide
  assign and_2_out = and_1_out & {4{not_1_out[3]}};  // AND_Gate and_2, 4 bits wide
  not not_1 (not_1_out[3], and_3_out);
  and and_3 (and_3_out, in_3[2], in_3[1], in_3[0]);
  assign out_11 = and_1_out ^ and_2_out;  // XOR_Gate xor_1, 4 bits wide
  not not_2 (s3_n, in_3[2]);
  assign and_4_out = and_1_out & {4{not_3_out[3]}};  // AND_Gate and_4, 4 bits wide
  not not_3 (not_3_out[3], and_5_out);
  and and_5 (and_5_out, in_3[2], in_3[1], s1_n);
  not not_4 (s2_n, in_3[1]);
  assign out_10 = and_1_out ^ and_4_out;  // XOR_Gate xor_2, 4 bits wide
  not not_5 (s1_n, in_3[0]);
  assign out_9 = and_1_out ^ and_6_out;  // XOR_Gate xor_3, 4 bits wide
  assign and_6_out = and_1_out & {4{not_6_out[3]}};  // AND_Gate and_6, 4 bits wide
  not not_6 (not_6_out[3], and_7_out);
  and and_7 (and_7_out, in_3[2], s2_n, in_3[0]);
  assign and_8_out = and_1_out & {4{not_7_out[3]}};  // AND_Gate and_8, 4 bits wide
  not not_7 (not_7_out[3], and_9_out);
  and and_9 (and_9_out, in_3[2], s2_n, s1_n);
  assign out_8 = and_1_out ^ and_8_out;  // XOR_Gate xor_4, 4 bits wide
  assign out_7 = and_1_out ^ and_10_out;  // XOR_Gate xor_5, 4 bits wide
  assign and_10_out = and_1_out & {4{not_8_out[3]}};  // AND_Gate and_10, 4 bits wide
  not not_8 (not_8_out[3], and_11_out);
  and and_11 (and_11_out, s3_n, in_3[1], in_3[0]);
  assign and_12_out = and_1_out & {4{not_9_out[3]}};  // AND_Gate and_12, 4 bits wide
  not not_9 (not_9_out[3], and_13_out);
  and and_13 (and_13_out, s3_n, in_3[1], s1_n);
  assign out_6 = and_1_out ^ and_12_out;  // XOR_Gate xor_6, 4 bits wide
  assign out_5 = and_1_out ^ and_14_out;  // XOR_Gate xor_7, 4 bits wide
  assign and_14_out = and_1_out & {4{not_10_out[3]}};  // AND_Gate and_14, 4 bits wide
  not not_10 (not_10_out[3], and_15_out);
  and and_15 (and_15_out, s3_n, s2_n, in_3[0]);
  assign out_4 = and_1_out ^ and_16_out;  // XOR_Gate xor_8, 4 bits wide
  assign and_16_out = and_1_out & {4{not_11_out[3]}};  // AND_Gate and_16, 4 bits wide
  not not_11 (not_11_out[3], and_17_out);
  and and_17 (and_17_out, s3_n, s2_n, s1_n);

  // Other names for the same wires on the sheet: s1 = in_3[0]; s2 = in_3[1]; s3 = in_3[2]
endmodule

module demultiplexer_16num_4bits (
  input  [3:0] in_1,
  input  in_2,
  input  [3:0] in_3,
  output [3:0] out_4,
  output [3:0] out_5,
  output [3:0] out_6,
  output [3:0] out_7,
  output [3:0] out_8,
  output [3:0] out_9,
  output [3:0] out_10,
  output [3:0] out_11,
  output [3:0] out_12,
  output [3:0] out_13,
  output [3:0] out_14,
  output [3:0] out_15,
  output [3:0] out_16,
  output [3:0] out_17,
  output [3:0] out_18,
  output [3:0] out_19
);

  wire and_3_out, and_5_out, and_7_out, and_9_out, and_11_out, and_13_out, and_15_out, and_17_out,
       and_19_out, and_21_out, and_23_out, and_25_out, and_27_out, and_29_out, and_31_out, and_33_out, s1_n,
       s2_n, s3_n, s4_n;
  wire [3:0] and_1_out, and_2_out, and_4_out, and_6_out, and_8_out, and_10_out, and_12_out, and_14_out,
       and_16_out, and_18_out, and_20_out, and_22_out, and_24_out, and_26_out, and_28_out, and_30_out,
       and_32_out;
  wire [3:3] not_1_out, not_2_out, not_3_out, not_7_out, not_9_out, not_10_out, not_11_out, not_12_out,
       not_13_out, not_14_out, not_15_out, not_16_out, not_17_out, not_18_out, not_19_out, not_20_out;

  assign and_1_out = in_1 & {4{in_2}};  // AND_Gate and_1, 4 bits wide
  assign out_19 = and_1_out ^ and_2_out;  // XOR_Gate xor_1, 4 bits wide
  assign and_2_out = and_1_out & {4{not_1_out[3]}};  // AND_Gate and_2, 4 bits wide
  not not_1 (not_1_out[3], and_3_out);
  and and_3 (and_3_out, in_3[3], in_3[2], in_3[1], in_3[0]);
  assign and_4_out = and_1_out & {4{not_2_out[3]}};  // AND_Gate and_4, 4 bits wide
  assign out_18 = and_1_out ^ and_4_out;  // XOR_Gate xor_2, 4 bits wide
  not not_2 (not_2_out[3], and_5_out);
  and and_5 (and_5_out, in_3[3], in_3[2], in_3[1], s1_n);
  assign and_6_out = and_1_out & {4{not_3_out[3]}};  // AND_Gate and_6, 4 bits wide
  not not_3 (not_3_out[3], and_7_out);
  and and_7 (and_7_out, in_3[3], in_3[2], s2_n, in_3[0]);
  not not_4 (s4_n, in_3[3]);
  assign out_17 = and_1_out ^ and_6_out;  // XOR_Gate xor_3, 4 bits wide
  not not_5 (s3_n, in_3[2]);
  not not_6 (s2_n, in_3[1]);
  assign out_16 = and_1_out ^ and_8_out;  // XOR_Gate xor_4, 4 bits wide
  assign and_8_out = and_1_out & {4{not_7_out[3]}};  // AND_Gate and_8, 4 bits wide
  not not_7 (not_7_out[3], and_9_out);
  and and_9 (and_9_out, in_3[3], in_3[2], s2_n, s1_n);
  not not_8 (s1_n, in_3[0]);
  assign and_10_out = and_1_out & {4{not_9_out[3]}};  // AND_Gate and_10, 4 bits wide
  not not_9 (not_9_out[3], and_11_out);
  and and_11 (and_11_out, in_3[3], s3_n, in_3[1], in_3[0]);
  assign out_15 = and_1_out ^ and_10_out;  // XOR_Gate xor_5, 4 bits wide
  assign out_14 = and_1_out ^ and_12_out;  // XOR_Gate xor_6, 4 bits wide
  assign and_12_out = and_1_out & {4{not_10_out[3]}};  // AND_Gate and_12, 4 bits wide
  not not_10 (not_10_out[3], and_13_out);
  and and_13 (and_13_out, in_3[3], s3_n, in_3[1], s1_n);
  assign and_14_out = and_1_out & {4{not_11_out[3]}};  // AND_Gate and_14, 4 bits wide
  not not_11 (not_11_out[3], and_15_out);
  and and_15 (and_15_out, in_3[3], s3_n, s2_n, in_3[0]);
  assign out_13 = and_1_out ^ and_14_out;  // XOR_Gate xor_7, 4 bits wide
  assign and_16_out = and_1_out & {4{not_12_out[3]}};  // AND_Gate and_16, 4 bits wide
  not not_12 (not_12_out[3], and_17_out);
  and and_17 (and_17_out, in_3[3], s3_n, s2_n, s1_n);
  assign out_12 = and_1_out ^ and_16_out;  // XOR_Gate xor_8, 4 bits wide
  assign and_18_out = and_1_out & {4{not_13_out[3]}};  // AND_Gate and_18, 4 bits wide
  not not_13 (not_13_out[3], and_19_out);
  and and_19 (and_19_out, s4_n, in_3[2], in_3[1], in_3[0]);
  assign out_11 = and_1_out ^ and_18_out;  // XOR_Gate xor_9, 4 bits wide
  assign out_10 = and_1_out ^ and_20_out;  // XOR_Gate xor_10, 4 bits wide
  assign and_20_out = and_1_out & {4{not_14_out[3]}};  // AND_Gate and_20, 4 bits wide
  not not_14 (not_14_out[3], and_21_out);
  and and_21 (and_21_out, s4_n, in_3[2], in_3[1], s1_n);
  assign and_22_out = and_1_out & {4{not_15_out[3]}};  // AND_Gate and_22, 4 bits wide
  assign out_9 = and_1_out ^ and_22_out;  // XOR_Gate xor_11, 4 bits wide
  not not_15 (not_15_out[3], and_23_out);
  and and_23 (and_23_out, s4_n, in_3[2], s2_n, in_3[0]);
  assign and_24_out = and_1_out & {4{not_16_out[3]}};  // AND_Gate and_24, 4 bits wide
  not not_16 (not_16_out[3], and_25_out);
  and and_25 (and_25_out, s4_n, in_3[2], s2_n, s1_n);
  assign out_8 = and_1_out ^ and_24_out;  // XOR_Gate xor_12, 4 bits wide
  assign and_26_out = and_1_out & {4{not_17_out[3]}};  // AND_Gate and_26, 4 bits wide
  assign out_7 = and_1_out ^ and_26_out;  // XOR_Gate xor_13, 4 bits wide
  not not_17 (not_17_out[3], and_27_out);
  and and_27 (and_27_out, s4_n, s3_n, in_3[1], in_3[0]);
  assign and_28_out = and_1_out & {4{not_18_out[3]}};  // AND_Gate and_28, 4 bits wide
  not not_18 (not_18_out[3], and_29_out);
  and and_29 (and_29_out, s4_n, s3_n, in_3[1], s1_n);
  assign out_6 = and_1_out ^ and_28_out;  // XOR_Gate xor_14, 4 bits wide
  assign out_5 = and_1_out ^ and_30_out;  // XOR_Gate xor_15, 4 bits wide
  assign and_30_out = and_1_out & {4{not_19_out[3]}};  // AND_Gate and_30, 4 bits wide
  not not_19 (not_19_out[3], and_31_out);
  and and_31 (and_31_out, s4_n, s3_n, s2_n, in_3[0]);
  assign and_32_out = and_1_out & {4{not_20_out[3]}};  // AND_Gate and_32, 4 bits wide
  assign out_4 = and_1_out ^ and_32_out;  // XOR_Gate xor_16, 4 bits wide
  not not_20 (not_20_out[3], and_33_out);
  and and_33 (and_33_out, s4_n, s3_n, s2_n, s1_n);

  // Other names for the same wires on the sheet: s1 = in_3[0]; s2 = in_3[1]; s3 = in_3[2]; s4 = in_3[3]
endmodule

module decoder_8bits (
  input  [2:0] in_1,
  output out_2,
  output out_3,
  output out_4,
  output out_5,
  output out_6,
  output out_7,
  output out_8,
  output out_9
);

  wire s1_n, s2_n, s3_n;

  not not_1 (s1_n, in_1[0]);
  not not_2 (s2_n, in_1[1]);
  not not_3 (s3_n, in_1[2]);
  and and_1 (out_2, s1_n, s2_n, s3_n);
  and and_2 (out_4, in_1[0], s2_n, s3_n);
  and and_3 (out_6, s1_n, in_1[1], s3_n);
  and and_4 (out_8, in_1[0], in_1[1], s3_n);
  and and_5 (out_3, s1_n, s2_n, in_1[2]);
  and and_6 (out_5, in_1[0], s2_n, in_1[2]);
  and and_7 (out_7, s1_n, in_1[1], in_1[2]);
  and and_8 (out_9, in_1[0], in_1[1], in_1[2]);

  // Other names for the same wires on the sheet: s1 = in_1[0]; s2 = in_1[1]; s3 = in_1[2]
endmodule
