// Logisim project multiplexer_2num_4bits.circ as structural Verilog
module multiplexer_2num_4bits (
  input  [3:0] in_1,
  input  [3:0] in_2,
  input  in_3,
  input  in_4,
  output [3:0] out_5
);

  wire not_1_out, not_2_out, not_3_out, not_4_out;
  wire [3:0] and_1_out, and_5_out, or_1_out;

  not not_1 (not_1_out, in_4);
  not not_2 (not_2_out, in_4);
  not not_3 (not_3_out, in_4);
  not not_4 (not_4_out, in_4);
  and and_1 (and_1_out[0], in_1[0], not_1_out);
  and and_2 (and_1_out[1], in_1[1], not_2_out);
  and and_3 (and_1_out[2], in_1[2], not_3_out);
  and and_4 (and_1_out[3], in_1[3], not_4_out);
  and and_5 (and_5_out[0], in_2[0], in_4);
  and and_6 (and_5_out[1], in_2[1], in_4);
  and and_7 (and_5_out[2], in_2[2], in_4);
  and and_8 (and_5_out[3], in_2[3], in_4);
  assign or_1_out = and_1_out | and_5_out;  // OR_Gate or_1, 4 bits wide
  assign out_5 = or_1_out & {4{in_3}};  // AND_Gate and_9, 4 bits wide
endmodule
