// Logisim project ALU.circ as structural Verilog
module ALU (
  input  [3:0] in_1,
  input  [3:0] in_2,
  input  [1:0] in_3,
  output [3:0] out_4
);

  wire [3:0] and_1_out, or_1_out, restador_4bits_1_out_3, sumador_4bits_1_out_3;

  assign and_1_out = in_2 & in_1;  // AND_Gate and_1, 4 bits wide
  assign or_1_out = in_2 | in_1;  // OR_Gate or_1, 4 bits wide
  sumador_4bits sumador_4bits_1 (.in_1(in_1), .in_2(in_2), .out_3(sumador_4bits_1_out_3));  // open: out_4
  restador_4bits restador_4bits_1 (.in_1(in_1), .in_2(in_2), .out_3(restador_4bits_1_out_3));  // open: out_4
  Multiplexer #(.select(2), .width(4), .enable("false")) multiplexer_1 (
    .in0(sumador_4bits_1_out_3), .in1(restador_4bits_1_out_3), .in2(and_1_out), .in3(or_1_out), .out(out_4),
    .sel(in_3));
  // Probe on out_4
endmodule
