// Logisim project decoder_8bits.circ as structural Verilog
module decoder_8bits (
  input  [2:0] in_1,
  output out_2,
  output out_3,
  output out_4,
  output out_5,
  output out_6,
  output out_7,
  output out_8,
  output out_9
);

  wire s1_n, s2_n, s3_n;

  not not_1 (s1_n, in_1[0]);
  not not_2 (s2_n, in_1[1]);
  not not_3 (s3_n, in_1[2]);
  and and_1 (out_2, s1_n, s2_n, s3_n);
  and and_2 (out_4, in_1[0], s2_n, s3_n);
  and and_3 (out_6, s1_n, in_1[1], s3_n);
  and and_4 (out_8, in_1[0], in_1[1], s3_n);
  and and_5 (out_3, s1_n, s2_n, in_1[2]);
  and and_6 (out_5, in_1[0], s2_n, in_1[2]);
  and and_7 (out_7, s1_n, in_1[1], in_1[2]);
  and and_8 (out_9, in_1[0], in_1[1], in_1[2]);

  // Other names for the same wires on the sheet: s1 = in_1[0]; s2 = in_1[1]; s3 = in_1[2]
endmodule
