// Logisim project restador_4bits.circ as structural Verilog
module restador_4bits (
  input  [3:0] in_1,
  input  [3:0] in_2,
  output [3:0] out_3,
  output out_4
);

  wire sumador_1_out_5, sumador_2_out_5, sumador_3_out_5;
  wire [3:0] not_1_out;

  // Probe on in_1
  // Probe on not_1_out
  assign not_1_out = ~in_2;  // NOT_Gate not_1, 4 bits wide
  sumador sumador_1 (.in_1(in_1[0]), .in_2(not_1_out[0]), .in_3(1'b1), .out_4(out_3[0]), .out_5(sumador_1_out_5));
  sumador sumador_2 (
    .in_1(in_1[1]), .in_2(not_1_out[1]), .in_3(sumador_1_out_5), .out_4(out_3[1]), .out_5(sumador_2_out_5));
  sumador sumador_3 (
    .in_1(in_1[2]), .in_2(not_1_out[2]), .in_3(sumador_2_out_5), .out_4(out_3[2]), .out_5(sumador_3_out_5));
  sumador sumador_4 (.in_1(in_1[3]), .in_2(not_1_out[3]), .in_3(sumador_3_out_5), .out_4(out_3[3]), .out_5(out_4));
  // Probe on out_3
endmodule
