// Logisim project semisumador.circ as structural Verilog
module semisumador (
  input  in_1,
  input  in_2,
  output out_3,
  output out_4
);

  xor xor_1 (out_3, in_1, in_2);
  and and_1 (out_4, in_1, in_2);

  // Other names for the same wires on the sheet: bit_a = in_1; bit_b = in_2
endmodule
