// Logisim project sumador.circ as structural Verilog
module sumador (
  input  in_1,
  input  in_2,
  input  in_3,
  output out_4,
  output out_5
);

  wire semisumador_1_out_3, semisumador_1_out_4, semisumador_2_out_4;

  semisumador semisumador_1 (.in_1(in_1), .in_2(in_2), .out_3(semisumador_1_out_3), .out_4(semisumador_1_out_4));
  semisumador semisumador_2 (.in_1(semisumador_1_out_3), .in_2(in_3), .out_3(out_4), .out_4(semisumador_2_out_4));
  or or_1 (out_5, semisumador_2_out_4, semisumador_1_out_4);

  // Other names for the same wires on the sheet: bit_a = in_1; bit_b = in_2; Carry = in_3
endmodule
