// Logisim project sumador_4bits.circ as structural Verilog
module sumador_4bits (
  input  [3:0] in_1,
  input  [3:0] in_2,
  output [3:0] out_3,
  output out_4
);

  wire sumador_1_out_5, sumador_2_out_5, sumador_3_out_5;

  // Probe on in_1
  // Probe on in_2
  sumador sumador_1 (.in_1(in_1[0]), .in_2(in_2[0]), .in_3(1'b0), .out_4(out_3[0]), .out_5(sumador_1_out_5));
  sumador sumador_2 (.in_1(in_1[1]), .in_2(in_2[1]), .in_3(sumador_1_out_5), .out_4(out_3[1]), .out_5(sumador_2_out_5));
  sumador sumador_3 (.in_1(in_1[2]), .in_2(in_2[2]), .in_3(sumador_2_out_5), .out_4(out_3[2]), .out_5(sumador_3_out_5));
  sumador sumador_4 (.in_1(in_1[3]), .in_2(in_2[3]), .in_3(sumador_3_out_5), .out_4(out_3[3]), .out_5(out_4));
  // Probe on out_3
endmodule
