// Logisim project 8bit_registry.circ as structural Verilog: 1 circuit, main circuit main
module main (
  input  IN,
  input  CLK,
  input  EN,
  input  Reset,
  output [7:0] out_5
);

  wire and_1_out;

  and and_1 (and_1_out, CLK, EN);
  D_Flip_Flop d_ff_1 (.clk(and_1_out), .D(IN), .Q(out_5[7]), .reset(Reset));  // open: Qn, preset, en
  D_Flip_Flop d_ff_2 (.clk(and_1_out), .D(out_5[7]), .Q(out_5[6]), .reset(Reset));  // open: Qn, preset, en
  D_Flip_Flop d_ff_3 (.clk(and_1_out), .D(out_5[6]), .Q(out_5[5]), .reset(Reset));  // open: Qn, preset, en
  D_Flip_Flop d_ff_4 (.clk(and_1_out), .D(out_5[5]), .Q(out_5[4]), .reset(Reset));  // open: Qn, preset, en
  D_Flip_Flop d_ff_5 (.clk(and_1_out), .D(out_5[4]), .Q(out_5[3]), .reset(Reset));  // open: Qn, preset, en
  D_Flip_Flop d_ff_6 (.clk(and_1_out), .D(out_5[3]), .Q(out_5[2]), .reset(Reset));  // open: Qn, preset, en
  D_Flip_Flop d_ff_7 (.clk(and_1_out), .D(out_5[2]), .Q(out_5[1]), .reset(Reset));  // open: Qn, preset, en
  D_Flip_Flop d_ff_8 (.clk(and_1_out), .D(out_5[1]), .Q(out_5[0]), .reset(Reset));  // open: Qn, preset, en
endmodule
