// Logisim project Counter.circ as structural Verilog: 1 circuit, main circuit main
module main (
  input  CLK,
  input  Reset,
  output [1:0] out_3
);

  wire and_1_out, nand_1_out;

  nand nand_1 (nand_1_out, out_3[1], out_3[0]);
  and and_1 (and_1_out, nand_1_out, CLK);
  J_K_Flip_Flop j_k_ff_1 (
    .J(out_3[0]), .clk(and_1_out), .K(out_3[0]), .Q(out_3[1]), .reset(Reset));  // open: Qn, preset, en
  J_K_Flip_Flop j_k_ff_2 (
    .J(and_1_out), .clk(and_1_out), .K(and_1_out), .Q(out_3[0]), .reset(Reset));  // open: Qn, preset, en

  // Other names for the same wires on the sheet: Q0 = out_3[0]; Q1 = out_3[1]
endmodule
