// Logisim project D_flip_flop.circ as structural Verilog: 1 circuit, main circuit main
module main (
  input  in_1,
  output out_2,
  output out_3
);

  wire clock_1_out, nand_1_out, nand_2_out, not_1_out;

  not not_1 (not_1_out, in_1);
  Clock clock_1 (.out(clock_1_out));
  nand nand_1 (nand_1_out, in_1, clock_1_out);
  nand nand_2 (nand_2_out, clock_1_out, not_1_out);
  SR_flip_flop_main main_1 (.in_1(nand_1_out), .in_2(nand_2_out), .in_3(clock_1_out), .out_4(out_2), .out_5(out_3));
endmodule
