// Logisim project T_flip_flop.circ as structural Verilog: 1 circuit, main circuit main
module main (
  input  in_1,
  output out_2,
  output out_3
);

  wire and_1_out, and_2_out, clock_1_out;

  Clock clock_1 (.out(clock_1_out));
  and and_1 (and_1_out, out_2, in_1, clock_1_out);
  and and_2 (and_2_out, clock_1_out, in_1, out_3);
  nor nor_1 (out_2, and_1_out, out_3);
  nor nor_2 (out_3, out_2, and_2_out);
endmodule
