// Logisim project datapath.circ as structural Verilog: 1 circuit, main circuit main
module main (
  input  [31:0] in_1,
  input  in_2,
  input  [4:0] in_3,
  input  [4:0] in_4,
  input  [4:0] in_5,
  input  [2:0] in_6,
  input  in_7,
  input  in_8
);

  wire clock_1_out;
  wire [31:0] main_1_out_7, main_1_out_8, main_2_p5, multiplexer_1_out;

  Multiplexer #(.width(32)) multiplexer_1 (
    .in0(main_2_p5), .in1(in_1), .out(multiplexer_1_out), .sel(in_2));  // open: en
  RF_main main_1 (
    .out_7(main_1_out_7), .out_8(main_1_out_8), .Data(multiplexer_1_out), .dir_dest(in_3), .dir_a(in_5),
    .dir_b(in_4), .CLK(clock_1_out), .R_W(in_7));
  Clock clock_1 (.out(clock_1_out));
  // ALU_32_main main_2: pin names not known; wires that end beside it: main_1_out_7, main_1_out_8, in_6, in_8, main_2_p5
endmodule
