// Logisim project registro_bidireccional.circ as structural Verilog: 1 circuit, main circuit main
module main (
  input  CLK,
  input  R_L,
  input  I0,
  input  LOAD,
  input  RST,
  output O0,
  output O1,
  output O2,
  output O3
);

  wire multiplexer_1_out, multiplexer_2_out, multiplexer_3_out, multiplexer_4_out, multiplexer_5_out,
       multiplexer_6_out;

  Multiplexer #(.enable("false")) multiplexer_1 (.in0(multiplexer_2_out), .in1(O1), .out(multiplexer_1_out), .sel(R_L));
  Multiplexer #(.enable("false")) multiplexer_2 (.in0(O3), .in1(I0), .out(multiplexer_2_out), .sel(LOAD));
  D_Flip_Flop d_ff_1 (.clk(CLK), .D(multiplexer_1_out), .Q(O0), .reset(RST));  // open: Qn, preset, en
  Multiplexer #(.enable("false")) multiplexer_3 (.in0(O0), .in1(O2), .out(multiplexer_3_out), .sel(R_L));
  D_Flip_Flop d_ff_2 (.clk(CLK), .D(multiplexer_3_out), .Q(O1), .reset(RST));  // open: Qn, preset, en
  Multiplexer #(.enable("false")) multiplexer_4 (.in0(O1), .in1(O3), .out(multiplexer_4_out), .sel(R_L));
  D_Flip_Flop d_ff_3 (.clk(CLK), .D(multiplexer_4_out), .Q(O2), .reset(RST));  // open: Qn, preset, en
  Multiplexer #(.enable("false")) multiplexer_5 (.in0(O2), .in1(multiplexer_6_out), .out(multiplexer_5_out), .sel(R_L));
  Multiplexer #(.enable("false")) multiplexer_6 (.in0(O0), .in1(I0), .out(multiplexer_6_out), .sel(LOAD));
  D_Flip_Flop d_ff_4 (.clk(CLK), .D(multiplexer_5_out), .Q(O3), .reset(RST));  // open: Qn, preset, en

  // Other names for the same wires on the sheet: RL = R_L
endmodule
