// Logisim project registro_contador.circ as structural Verilog: 1 circuit, main circuit main
module main (
  input  CLK,
  input  EN,
  input  I0,
  input  I1,
  input  I2,
  input  I3,
  input  RST,
  output O0,
  output O1,
  output O2,
  output O3
);

  wire and_1_out, and_2_out, and_3_out, and_4_out, and_5_out, and_6_out, and_7_out, and_8_out, d_ff_1_qn,
       d_ff_2_qn, d_ff_3_qn, d_ff_4_qn, not_1_out, not_2_out, not_3_out, not_4_out, or_1_out, or_2_out,
       or_3_out, or_4_out;

  and and_1 (and_1_out, I0, EN);
  or or_1 (or_1_out, and_1_out, and_2_out);
  and and_2 (and_2_out, not_1_out, d_ff_1_qn);
  not not_1 (not_1_out, EN);
  D_Flip_Flop d_ff_1 (.clk(CLK), .D(or_1_out), .Q(O0), .Qn(d_ff_1_qn), .reset(RST));  // open: preset, en
  or or_2 (or_2_out, and_3_out, and_4_out);
  and and_3 (and_3_out, I1, EN);
  D_Flip_Flop d_ff_2 (.clk(CLK), .D(or_2_out), .Q(O1), .Qn(d_ff_2_qn), .en(d_ff_1_qn), .reset(RST));  // open: preset
  and and_4 (and_4_out, not_2_out, d_ff_2_qn);
  not not_2 (not_2_out, EN);
  or or_3 (or_3_out, and_5_out, and_7_out);
  and and_5 (and_5_out, I2, EN);
  not not_3 (not_3_out, EN);
  D_Flip_Flop d_ff_3 (.clk(CLK), .D(or_3_out), .Q(O2), .Qn(d_ff_3_qn), .en(d_ff_2_qn), .reset(RST));  // open: preset
  and and_6 (and_6_out, I3, EN);
  and and_7 (and_7_out, not_3_out, d_ff_3_qn);
  or or_4 (or_4_out, and_6_out, and_8_out);
  and and_8 (and_8_out, not_4_out, d_ff_4_qn);
  not not_4 (not_4_out, EN);
  D_Flip_Flop d_ff_4 (.clk(CLK), .D(or_4_out), .Q(O3), .Qn(d_ff_4_qn), .en(d_ff_3_qn), .reset(RST));  // open: preset
endmodule
