// Logisim project Pares_Impares.circ as structural Verilog: 1 circuit, main circuit main
module main (
  output out_1
);

  wire clock_1_out, comparator_1_eq, comparator_2_eq, d_ff_1_q, d_ff_2_q, keyboard_1_avail, not_1_out,
       not_2_out;
  wire [6:0] keyboard_1_data;

  Clock clock_1 (.out(clock_1_out));
  Keyboard keyboard_1 (.clk(clock_1_out), .avail(keyboard_1_avail), .data(keyboard_1_data));  // open: re, clr
  Comparator #(.width(7)) comparator_1 (.a(7'b1000001), .b(keyboard_1_data), .eq(comparator_1_eq));  // open: gt, lt
  Comparator #(.width(7)) comparator_2 (.a(7'b1000010), .b(keyboard_1_data), .eq(comparator_2_eq));  // open: gt, lt
  D_Flip_Flop d_ff_1 (
    .clk(clock_1_out), .D(comparator_1_eq), .Q(d_ff_1_q), .en(keyboard_1_avail));  // open: Qn, preset, reset
  D_Flip_Flop d_ff_2 (
    .clk(clock_1_out), .D(comparator_2_eq), .Q(d_ff_2_q), .en(keyboard_1_avail));  // open: Qn, preset, reset
  not not_1 (not_1_out, keyboard_1_avail);
  not not_2 (not_2_out, d_ff_1_q);
  and and_1 (out_1, not_2_out, d_ff_2_q, not_1_out);

  // Notes on the sheet:
  //   Paridad B
  //   Paridad A
endmodule
