// Logisim project Pattern-gen.circ as structural Verilog: 2 circuits, main circuit main
module main (
  input  in_1,
  input  in_2,
  output out_3
);

  wire and_1_out, not_1_out;
  wire [1:0] count_1_out_3;

  count count_1 (.in_1(in_1), .in_2(in_2), .out_3(count_1_out_3));
  not not_1 (not_1_out, count_1_out_3[0]);
  not not_2 (out_3, and_1_out);
  and and_1 (and_1_out, not_1_out, count_1_out_3[1]);
endmodule

module count (
  input  in_1,
  input  in_2,
  output [1:0] out_3
);

  J_K_Flip_Flop j_k_ff_1 (.J(out_3[0]), .clk(in_1), .K(out_3[0]), .Q(out_3[1]), .reset(in_2));  // open: Qn, preset, en
  J_K_Flip_Flop j_k_ff_2 (.J(in_1), .clk(in_1), .K(in_1), .Q(out_3[0]), .reset(in_2));  // open: Qn, preset, en
endmodule
