// Logisim project Pattern-rec.circ as structural Verilog: 1 circuit, main circuit main
module main (
  input  in_1,
  input  in_2,
  output out_3
);

  wire d_ff_1_q, d_ff_2_q, d_ff_3_q, not_1_out;

  D_Flip_Flop d_ff_1 (.clk(in_2), .D(in_1), .Q(d_ff_1_q));  // open: Qn, preset, en, reset
  D_Flip_Flop d_ff_2 (.clk(in_2), .D(d_ff_1_q), .Q(d_ff_2_q));  // open: Qn, preset, en, reset
  D_Flip_Flop d_ff_3 (.clk(in_2), .D(d_ff_2_q), .Q(d_ff_3_q));  // open: Qn, preset, en, reset
  not not_1 (not_1_out, d_ff_2_q);
  and and_1 (out_3, d_ff_3_q, not_1_out, d_ff_1_q, in_1);
endmodule
