// Logisim project expendedora.circ as structural Verilog: 1 circuit, main circuit main
module main (
);

  wire _5c_out, _10c_out, and_1_out, and_4_out, and_5_out, and_6_out, and_7_out, button_1_out, button_2_out,
       CLK, Cola, comparator_1_gt, comparator_2_gt, comparator_3_gt, drink, not_1_out, not_2_out, not_3_out,
       not_4_out, not_5_out, or_1_out, or_2_out, or_3_out, reset, select, selection_done, Soda, sumar_5,
       sumar_10;
  wire [2:0] adder_1_out, adder_2_out, multiplexer_1_out, multiplexer_2_out, multiplexer_3_out,
       multiplexer_4_out, subtractor_1_out, subtractor_2_out, value;

  Clock clock_1 (.out(CLK));
  Button button_1 (.out(button_1_out));
  Button button_2 (.out(button_2_out));
  Button button_3 (.out(reset));
  Button _5c (.out(_5c_out));
  Button _10c (.out(_10c_out));
  not not_1 (not_1_out, button_1_out);
  Comparator #(.width(3), .mode("unsigned")) comparator_1 (
    .a(value), .b(3'b100), .gt(comparator_1_gt));  // open: eq, lt
  not not_2 (not_2_out, comparator_1_gt);
  Adder #(.width(3)) adder_1 (.a(value), .b(3'b001), .out(adder_1_out));  // open: cin, cout
  Adder #(.width(3)) adder_2 (.a(value), .b(3'b010), .out(adder_2_out));  // open: cin, cout
  or or_1 (or_1_out, button_1_out, button_2_out);
  and and_1 (and_1_out, not_1_out, button_2_out);
  and and_2 (sumar_5, not_2_out, _5c_out);
  and and_3 (sumar_10, not_2_out, _10c_out);
  Multiplexer #(.width(3), .enable("false")) multiplexer_1 (
    .in0(value), .in1(adder_1_out), .out(multiplexer_1_out), .sel(sumar_5));
  Multiplexer #(.width(3), .enable("false")) multiplexer_2 (
    .in0(value), .in1(adder_2_out), .out(multiplexer_2_out), .sel(sumar_10));
  and and_4 (and_4_out, or_1_out, CLK);
  and and_5 (and_5_out, not_3_out, CLK);
  D_Flip_Flop d_ff_1 (.clk(CLK), .D(multiplexer_3_out[0]), .Q(value[0]), .reset(reset));  // open: Qn, preset, en
  not not_3 (not_3_out, selection_done);
  D_Flip_Flop d_ff_2 (.clk(and_5_out), .D(and_4_out), .Q(selection_done), .reset(reset));  // open: Qn, preset, en
  D_Flip_Flop d_ff_3 (.clk(and_4_out), .D(and_1_out), .Q(drink), .reset(reset));  // open: Qn, preset, en
  D_Flip_Flop d_ff_4 (.clk(CLK), .D(multiplexer_3_out[1]), .Q(value[1]), .reset(reset));  // open: Qn, preset, en
  Multiplexer #(.width(3), .enable("false")) multiplexer_3 (
    .in0(multiplexer_1_out), .in1(multiplexer_2_out), .out(multiplexer_3_out), .sel(select));
  D_Flip_Flop d_ff_5 (.clk(CLK), .D(multiplexer_3_out[2]), .Q(value[2]), .reset(reset));  // open: Qn, preset, en
  or or_2 (or_2_out, sumar_5, sumar_10);
  not not_4 (not_4_out, sumar_5);
  and and_6 (and_6_out, not_4_out, sumar_10);
  and and_7 (and_7_out, or_2_out, CLK);
  D_Flip_Flop d_ff_6 (.clk(and_7_out), .D(and_6_out), .Q(select));  // open: Qn, preset, en, reset
  Comparator #(.width(3), .mode("unsigned")) comparator_2 (
    .a(value), .b(3'b100), .gt(comparator_2_gt));  // open: eq, lt
  not not_5 (not_5_out, drink);
  Comparator #(.width(3), .mode("unsigned")) comparator_3 (
    .a(value), .b(3'b011), .gt(comparator_3_gt));  // open: eq, lt
  Subtractor #(.width(3)) subtractor_1 (.a(value), .b(3'b100), .out(subtractor_1_out));  // open: bin, bout
  Subtractor #(.width(3)) subtractor_2 (.a(value), .b(3'b011), .out(subtractor_2_out));  // open: bin, bout
  Multiplexer #(.width(3)) multiplexer_4 (
    .in0(subtractor_1_out), .in1(subtractor_2_out), .out(multiplexer_4_out), .sel(Soda), .en(or_3_out));
  or or_3 (or_3_out, Soda, Cola);
  and and_8 (Cola, comparator_2_gt, selection_done, not_5_out);
  and and_9 (Soda, comparator_3_gt, selection_done, drink);
  LED led_1 (.in(Cola));
  LED led_2 (.in(Soda));
  LED led_3 (.in(multiplexer_4_out[0]));
  LED led_4 (.in(multiplexer_4_out[1]));

  // Notes on the sheet:
  //   Cola
  //   Soda
  //   Reset
  //   5c
  //   10c
  //   Seleccionar Bebida
  //   Ingresar Dinero
  //   Agregar dinero
  //   Dispensar Bebida
  //   Devolver Vuelto
  //   Cola
  //   Soda
  //   5c
  //   10c
endmodule
