// Logisim project semaforo.circ as structural Verilog: 2 circuits, main circuit main
module main (
  input  in_1
);

  wire and_2_out, and_3_out, and_4_out, and_5_out, and_6_out, and_7_out, and_8_out, and_9_out, and_10_out,
       and_11_out, and_12_out, and_13_out, clock_1_out, count, not_1_out, not_2_out, not_3_out, not_4_out,
       not_5_out, not_6_out, not_7_out, not_8_out, not_9_out, not_10_out, not_11_out, not_12_out, not_13_out,
       not_14_out, not_15_out, or_1_out, or_2_out, or_3_out, S0, S1;
  wire [1:0] counter_1_out_3;

  Clock clock_1 (.out(clock_1_out));
  and and_1 (count, counter_1_out_3[0], counter_1_out_3[1]);
  counter counter_1 (.CLK(clock_1_out), .out_3(counter_1_out_3));  // open: Reset
  not not_1 (not_1_out, S0);
  not not_2 (not_2_out, S1);
  and and_2 (and_2_out, not_1_out, not_2_out, in_1);
  not not_3 (not_3_out, in_1);
  and and_3 (and_3_out, not_3_out, not_4_out, S0);
  not not_4 (not_4_out, S1);
  not not_5 (not_5_out, S0);
  and and_4 (and_4_out, not_5_out, S1, in_1);
  not not_6 (not_6_out, in_1);
  and and_5 (and_5_out, not_6_out, S1, S0);
  and and_6 (and_6_out, S0, not_7_out, in_1);
  not not_7 (not_7_out, S1);
  not not_8 (not_8_out, in_1);
  not not_9 (not_9_out, S0);
  and and_7 (and_7_out, not_8_out, not_9_out, S1);
  not not_10 (not_10_out, S0);
  and and_8 (and_8_out, not_10_out, S1, in_1);
  not not_11 (not_11_out, in_1);
  and and_9 (and_9_out, not_11_out, S1, S0);
  or or_1 (or_1_out, and_2_out, and_3_out, and_4_out, and_5_out);
  or or_2 (or_2_out, and_6_out, and_7_out, and_8_out, and_9_out);
  D_Flip_Flop d_ff_1 (.clk(count), .D(or_1_out), .Q(S0));  // open: Qn, preset, en, reset
  D_Flip_Flop d_ff_2 (.clk(count), .D(or_2_out), .Q(S1));  // open: Qn, preset, en, reset
  and and_10 (and_10_out, S0, not_12_out);
  not not_12 (not_12_out, S1);
  and and_11 (and_11_out, S0, S1);
  not not_13 (not_13_out, S0);
  LED led_1 (.in(and_12_out));
  and and_12 (and_12_out, not_13_out, not_14_out);
  not not_14 (not_14_out, S1);
  or or_3 (or_3_out, and_10_out, and_11_out);
  LED led_2 (.in(or_3_out));
  not not_15 (not_15_out, S0);
  LED led_3 (.in(and_13_out));
  and and_13 (and_13_out, not_15_out, S1);

  // Other names for the same wires on the sheet: I = in_1
endmodule

module counter (
  input  CLK,
  input  Reset,
  output [1:0] out_3
);

  J_K_Flip_Flop j_k_ff_1 (.J(out_3[0]), .clk(CLK), .K(out_3[0]), .Q(out_3[1]), .reset(Reset));  // open: Qn, preset, en
  J_K_Flip_Flop j_k_ff_2 (.J(CLK), .clk(CLK), .K(CLK), .Q(out_3[0]), .reset(Reset));  // open: Qn, preset, en

  // Other names for the same wires on the sheet: Q0 = out_3[0]; Q1 = out_3[1]
endmodule
