// Logisim project verif_pattern.circ as structural Verilog: 1 circuit, main circuit main
module main (
  output out_1
);

  wire clock_1_out, main_1_out_3;

  Clock clock_1 (.out(clock_1_out));
  Pattern_gen_main main_1 (.in_1(clock_1_out), .out_3(main_1_out_3));  // open: in_2
  Pattern_rec_main main_2 (.in_1(main_1_out_3), .out_3(out_1), .in_2(clock_1_out));

  // Notes on the sheet:
  //   Generador
  //   Reconocedor
endmodule
