// Logisim project Perfecto.circ as structural Verilog: 2 circuits, main circuit main
module main (
  input  in_1,
  input  [31:0] in_2,
  output out_3
);

  wire and_1_out, and_2_out, CLK, comparator_1_lt, comparator_2_eq, counter_1_q, Done, End,
       multiplexer_1_out, multiplexer_6_out, not_2_out, not_3_out, On, or_1_out, S_N;
  wire [31:0] adder_1_out, adder_2_out, C, c_t, multiplexer_2_out, multiplexer_5_out, resto_1_out_6, S, s_t;

  Clock clock_1 (.out(CLK));
  Counter #(.width(1), .max('h1), .trigger("falling")) counter_1 (
    .Q(counter_1_q), .clk(and_1_out));  // open: load, D, count, carry, clr
  and and_1 (and_1_out, Done, CLK);
  Multiplexer #(.enable("false")) multiplexer_1 (.in0(1'b0), .in1(Done), .out(multiplexer_1_out), .sel(counter_1_q));
  resto resto_1 (.in_1(CLK), .in_2(or_1_out), .in_3(in_2), .in_4(C), .out_6(resto_1_out_6), .out_5(Done));
  or or_1 (or_1_out, in_1, multiplexer_1_out);
  Multiplexer #(.width(32), .enable("false")) multiplexer_2 (.in0(32'h1), .in1(c_t), .out(multiplexer_2_out), .sel(On));
  Comparator #(.width(32)) comparator_1 (.a(C), .b(in_2), .lt(comparator_1_lt));  // open: gt, eq
  not not_1 (End, comparator_1_lt);
  Adder #(.width(32)) adder_1 (.a(S), .b(C), .out(adder_1_out));  // open: cin, cout
  Register #(.width(32)) u_C (.D(multiplexer_2_out), .Q(C), .clk(CLK));  // open: en, clr
  Comparator #(.width(32)) comparator_2 (.a(resto_1_out_6), .b({32{1'b0}}), .eq(comparator_2_eq));  // open: gt, lt
  Adder #(.width(32)) adder_2 (.a(32'h1), .b(C), .out(adder_2_out));  // open: cin, cout
  and and_2 (and_2_out, Done, comparator_2_eq);
  Multiplexer #(.width(32), .enable("false")) multiplexer_3 (
    .in1(adder_1_out), .out(s_t), .sel(and_2_out));  // open: in0
  Multiplexer #(.width(32), .enable("false")) multiplexer_4 (.in1(adder_2_out), .out(c_t), .sel(Done));  // open: in0
  Multiplexer #(.width(32), .enable("false")) multiplexer_5 (
    .in0({32{1'b0}}), .in1(s_t), .out(multiplexer_5_out), .sel(On));
  Comparator #(.width(32)) comparator_3 (.a(S), .b(in_2), .eq(S_N));  // open: gt, lt
  Register #(.width(32)) u_S (.D(multiplexer_5_out), .Q(S), .clk(CLK));  // open: en, clr
  not not_2 (not_2_out, End);
  Multiplexer #(.enable("false")) multiplexer_6 (.in0(not_2_out), .in1(in_1), .out(multiplexer_6_out), .sel(not_3_out));
  not not_3 (not_3_out, On);
  D_Flip_Flop d_ff_1 (.clk(CLK), .D(multiplexer_6_out), .Q(On));  // open: Qn, preset, en, reset
  Multiplexer #(.enable("false")) multiplexer_7 (.in0(1'b0), .in1(S_N), .out(out_3), .sel(End));

  // Other names for the same wires on the sheet: N[31:0] = in_2; RST = in_1

  // Notes on the sheet:
  //   Salida
endmodule

module resto (
  input  in_1,
  input  in_2,
  input  [31:0] in_3,
  input  [31:0] in_4,
  output out_5,
  output [31:0] out_6
);

  wire End, not_1_out, not_2_out, On;
  wire [31:0] A, a_t, multiplexer_1_out, resta;

  Multiplexer #(.width(32), .enable("false")) multiplexer_1 (.in0(in_3), .in1(a_t), .out(multiplexer_1_out), .sel(On));
  Subtractor #(.width(32)) subtractor_1 (.a(A), .b(in_4), .out(resta));  // open: bin, bout
  Register #(.width(32)) register_1 (.D(multiplexer_1_out), .Q(A), .clk(in_1));  // open: en, clr
  Multiplexer #(.width(32), .enable("false")) multiplexer_2 (.in0(resta), .in1(in_3), .out(a_t), .sel(in_2));
  not not_1 (not_1_out, End);
  not not_2 (not_2_out, On);
  Comparator #(.width(32), .mode("unsigned")) comparator_1 (.a(resta), .b(in_4), .lt(End));  // open: gt, eq
  D_Flip_Flop #(.trigger("high")) d_ff_1 (.clk(in_1), .D(out_5), .Q(On));  // open: Qn, preset, en, reset
  Multiplexer #(.enable("false")) multiplexer_3 (.in0(not_1_out), .in1(in_2), .out(out_5), .sel(not_2_out));
  Multiplexer #(.width(32), .enable("false")) multiplexer_4 (.in0({32{1'b0}}), .in1(a_t), .out(out_6), .sel(End));

  // Other names for the same wires on the sheet: CLK_prime = in_1; Ia[31:0] = in_3; Ib[31:0] = in_4; RST = in_2

  // Notes on the sheet:
  //   Memoria
  //   Salida
endmodule
