// Logisim project Primo.circ as structural Verilog: 1 circuit, main circuit main
module main (
  input  [31:0] in_1,
  output Salida
);

  wire and_1_out, CLK, comparator_1_eq, comparator_2_eq, End, multiplexer_2_out, not_1_out, not_2_out, On,
       RST;
  wire [31:0] C, c_t, divider_1_rem, multiplexer_1_out;

  Clock clock_1 (.out(CLK));
  Button button_1 (.out(RST));
  Multiplexer #(.width(32), .enable("false")) multiplexer_1 (.in0(32'h2), .in1(c_t), .out(multiplexer_1_out), .sel(On));
  Register #(.width(32)) u_c (.D(multiplexer_1_out), .Q(C), .clk(CLK));  // open: en, clr
  Divider #(.width(32)) divider_1 (.a(in_1), .b(C), .rem(divider_1_rem));  // open: out, upper
  Comparator #(.width(32), .mode("unsigned")) comparator_1 (.a(in_1), .b(C), .eq(comparator_1_eq));  // open: gt, lt
  Comparator #(.width(32), .mode("unsigned")) comparator_2 (
    .a(divider_1_rem), .b({32{1'b0}}), .eq(comparator_2_eq));  // open: gt, lt
  Adder #(.width(32)) adder_1 (.a(C), .b(32'h1), .out(c_t));  // open: cin, cout
  or or_1 (End, comparator_1_eq, comparator_2_eq);
  not not_1 (not_1_out, End);
  Multiplexer #(.enable("false")) multiplexer_2 (.in0(not_1_out), .in1(RST), .out(multiplexer_2_out), .sel(not_2_out));
  not not_2 (not_2_out, On);
  and and_1 (and_1_out, End, comparator_2_eq);
  D_Flip_Flop d_ff_1 (.clk(CLK), .D(multiplexer_2_out), .Q(On));  // open: Qn, preset, en, reset
  not not_3 (Salida, and_1_out);

  // Other names for the same wires on the sheet: N[31:0] = in_1

  // Notes on the sheet:
  //   Memoria
endmodule
