// Logisim project fib.circ as structural Verilog: 1 circuit, main circuit main
module main (
  output [31:0] out_1
);

  wire CLk, End, multiplexer_4_out, not_1_out, not_2_out, RST, SF;
  wire [31:0] F1, multiplexer_1_out, multiplexer_2_out, multiplexer_3_out, N, n_t, R1, R2;

  Clock clock_1 (.out(CLk));
  Button button_1 (.out(RST));
  Register #(.width(32)) fib1 (.D(multiplexer_1_out), .Q(R1), .clk(CLk));  // open: en, clr
  Multiplexer #(.width(32), .enable("false")) multiplexer_1 (.in0(32'h1), .in1(F1), .out(multiplexer_1_out), .sel(SF));
  Comparator #(.width(32)) comparator_1 (.a(N), .b({32{1'b0}}), .eq(End));  // open: gt, lt
  // Probe on R2
  // Probe on R1
  Adder #(.width(32)) adder_1 (.a(R1), .b(R2), .out(F1));  // open: cin, cout
  Subtractor #(.width(32)) subtractor_1 (.a(N), .b(32'h1), .out(n_t));  // open: bin, bout
  Register #(.width(32)) fib2 (.D(multiplexer_2_out), .Q(R2), .clk(CLk));  // open: en, clr
  Multiplexer #(.width(32), .enable("false")) multiplexer_2 (.in0(32'h1), .in1(R1), .out(multiplexer_2_out), .sel(SF));
  Multiplexer #(.width(32), .enable("false")) multiplexer_3 (.in0(32'h8), .in1(n_t), .out(multiplexer_3_out), .sel(SF));
  Register #(.width(32)) u_N (.D(multiplexer_3_out), .Q(N), .clk(CLk));  // open: en, clr
  Register #(.width(32)) register_1 (.D(R1), .en(End), .Q(out_1), .clk(CLk), .clr(RST));
  not not_1 (not_1_out, End);
  Multiplexer #(.enable("false")) multiplexer_4 (.in0(not_1_out), .in1(RST), .out(multiplexer_4_out), .sel(not_2_out));
  not not_2 (not_2_out, SF);
  D_Flip_Flop Start (.clk(CLk), .D(multiplexer_4_out), .Q(SF));  // open: Qn, preset, en, reset

  // Notes on the sheet:
  //   Iniciar o reiniciar
  //   Operaciones
  //   N-1
  //   N
  //   Memoria
  //   Salida
endmodule
