// Logisim project resto.circ as structural Verilog: 1 circuit, main circuit main
module main (
  input  in_1,
  input  in_2,
  input  [31:0] in_3,
  input  [31:0] in_4,
  output [31:0] out_5
);

  wire End, multiplexer_3_out, not_1_out, not_2_out, On;
  wire [31:0] A, a_t, multiplexer_1_out, resta;

  Multiplexer #(.width(32), .enable("false")) multiplexer_1 (.in0(in_3), .in1(a_t), .out(multiplexer_1_out), .sel(On));
  Subtractor #(.width(32)) subtractor_1 (.a(A), .b(in_4), .out(resta));  // open: bin, bout
  Register #(.width(32)) register_1 (.D(multiplexer_1_out), .Q(A), .clk(in_1));  // open: en, clr
  Multiplexer #(.width(32), .enable("false")) multiplexer_2 (.in0(resta), .in1(in_3), .out(a_t), .sel(in_2));
  not not_1 (not_1_out, End);
  not not_2 (not_2_out, On);
  Comparator #(.width(32), .mode("unsigned")) comparator_1 (.a(resta), .b(in_4), .lt(End));  // open: gt, eq
  D_Flip_Flop d_ff_1 (.clk(in_1), .D(multiplexer_3_out), .Q(On));  // open: Qn, preset, en, reset
  Multiplexer #(.enable("false")) multiplexer_3 (.in0(not_1_out), .in1(in_2), .out(multiplexer_3_out), .sel(not_2_out));
  Multiplexer #(.width(32), .enable("false")) multiplexer_4 (.in0({32{1'b0}}), .in1(a_t), .out(out_5), .sel(End));

  // Other names for the same wires on the sheet: CLK_prime = in_1; Ia[31:0] = in_3; Ib[31:0] = in_4; RST = in_2

  // Notes on the sheet:
  //   Memoria
  //   Salida
endmodule
