// Logisim project s-mips.circ as structural Verilog: 18 circuits, main circuit S-MIPS Board
module RAM (
  input  [15:0] Address,
  input  [31:0] Data_In_0,
  input  [31:0] Data_In_1,
  input  [31:0] Data_In_2,
  input  [31:0] Data_In_3,
  input  [3:0] Mask,
  input  nRead_Write,
  input  Chip_Select,
  input  Reset,
  output [31:0] Data_Out_0,
  output [31:0] Data_Out_1,
  output [31:0] Data_Out_2,
  output [31:0] Data_Out_3,
  output [3:0] Read_Time,
  output [3:0] Write_Time
);

  wire and_2_out, and_3_out, and_4_out, and_5_out, and_6_out, and_7_out, and_8_out, and_9_out, Changed, CLK,
       comparator_2_eq, comparator_3_eq, comparator_4_eq, comparator_5_eq, comparator_6_eq, Count,
       demultiplexer_3_out0, Idle, Idle_q, Load, Load0, Load1, nand_1_out, or_1_out, or_2_out, or_3_out,
       or_4_out, or_5_out, or_6_out, or_7_out, or_8_out, or_9_out, or_10_out, Proc_q, Update_Mem, Zero_Time;
  wire [3:0] counter_1_q, multiplexer_1_out, subtractor_1_out;
  wire [31:0] register_1_q, register_2_q, register_3_q, register_4_q, register_5_q;

  // Probe on 4'b0011
  // Probe on 4'b0101
  Multiplexer #(.width(4), .enable("false")) multiplexer_1 (
    .in0(4'b0011), .in1(4'b0101), .out(multiplexer_1_out), .sel(nRead_Write));
  or or_1 (or_1_out, Idle, Update_Mem);
  or or_2 (or_2_out, ~Chip_Select, Reset);  // OR_Gate
  Subtractor #(.width(4)) subtractor_1 (.a(multiplexer_1_out), .b(4'b0010), .out(subtractor_1_out));  // open: bin, bout
  Demultiplexer #(.enable("false")) demultiplexer_1 (.out0(Idle), .out1(Load0), .in(Idle_q), .sel(Changed));
  D_Flip_Flop u_Idle (.clk(CLK), .D(or_1_out), .Q(Idle_q), .preset(or_2_out));  // open: Qn, en, reset
  // Probe on counter_1_q
  Counter #(.width(4), .max('hf)) counter_1 (
    .load(Load), .D(subtractor_1_out), .count(Count), .Q(counter_1_q), .clk(CLK), .clr(or_3_out));  // open: carry
  or or_3 (or_3_out, ~Chip_Select, Reset);  // OR_Gate
  Comparator #(.width(4), .mode("unsigned")) comparator_1 (
    .a(4'b0000), .b(counter_1_q), .eq(Zero_Time));  // open: gt, lt
  or or_4 (or_4_out, Count, Load0, Load1);
  Register #(.width(32)) register_1 (.D(Data_In_0), .en(Chip_Select), .Q(register_1_q), .clk(CLK), .clr(or_5_out));
  or or_5 (or_5_out, ~Chip_Select, Reset);  // OR_Gate
  Register #(.width(32)) register_2 (.D(Data_In_1), .en(Chip_Select), .Q(register_2_q), .clk(CLK), .clr(or_6_out));
  or or_6 (or_6_out, ~Chip_Select, Reset);  // OR_Gate
  Register #(.width(32)) register_3 (.D(Data_In_2), .en(Chip_Select), .Q(register_3_q), .clk(CLK), .clr(or_7_out));
  or or_7 (or_7_out, ~Chip_Select, Reset);  // OR_Gate
  Register #(.width(32)) register_4 (.D(Data_In_3), .en(Chip_Select), .Q(register_4_q), .clk(CLK), .clr(or_8_out));
  or or_8 (or_8_out, ~Chip_Select, Reset);  // OR_Gate
  Register #(.width(32)) register_5 (
    .D({{11{1'b1}}, nRead_Write, Mask, Address}), .en(Chip_Select), .Q(register_5_q), .clk(CLK),
    .clr(or_9_out));
  or or_9 (or_9_out, ~Chip_Select, Reset);  // OR_Gate
  D_Flip_Flop Proc (.clk(CLK), .D(or_4_out), .Q(Proc_q), .reset(or_10_out));  // open: Qn, preset, en
  or or_10 (or_10_out, ~Chip_Select, Reset);  // OR_Gate
  Demultiplexer #(.enable("false")) demultiplexer_2 (
    .out0(Count), .out1(Update_Mem), .in(demultiplexer_3_out0), .sel(Zero_Time));
  Demultiplexer #(.enable("false")) demultiplexer_3 (
    .out0(demultiplexer_3_out0), .out1(Load1), .in(Proc_q), .sel(Changed));
  Clock clock_1 (.out(CLK));
  Comparator #(.width(32)) comparator_2 (.a(register_1_q), .b(Data_In_0), .eq(comparator_2_eq));  // open: gt, lt
  Comparator #(.width(32)) comparator_3 (.a(register_2_q), .b(Data_In_1), .eq(comparator_3_eq));  // open: gt, lt
  Comparator #(.width(32)) comparator_4 (.a(register_3_q), .b(Data_In_2), .eq(comparator_4_eq));  // open: gt, lt
  Comparator #(.width(32)) comparator_5 (.a(register_4_q), .b(Data_In_3), .eq(comparator_5_eq));  // open: gt, lt
  Comparator #(.width(32)) comparator_6 (
    .a(register_5_q), .b({{11{1'b1}}, nRead_Write, Mask, Address}), .eq(comparator_6_eq));  // open: gt, lt
  nand nand_1 (nand_1_out, comparator_6_eq, comparator_2_eq, comparator_3_eq, comparator_4_eq, comparator_5_eq);
  and and_1 (Changed, nand_1_out, Chip_Select);
  or or_11 (Load, Count, Load1, Load0);
  and and_2 (and_2_out, Mask[0], Update_Mem, nRead_Write);
  and and_3 (and_3_out, Mask[1], Update_Mem, nRead_Write);
  and and_4 (and_4_out, Mask[2], Update_Mem, nRead_Write);
  and and_5 (and_5_out, Mask[3], Update_Mem, nRead_Write);
  RAM_part #(.addrWidth(16), .dataWidth(32), .bus("separate")) ram_1 (
    .addr(Address), .din(Data_In_0), .data(Data_Out_0), .str(and_2_out), .sel(Chip_Select), .clk(CLK),
    .ld(and_6_out), .clr(Reset));
  and and_6 (and_6_out, ~nRead_Write, Idle);  // AND_Gate
  RAM_part #(.addrWidth(16), .dataWidth(32), .bus("separate")) ram_2 (
    .addr(Address), .din(Data_In_1), .data(Data_Out_1), .str(and_3_out), .sel(Chip_Select), .clk(CLK),
    .ld(and_7_out), .clr(Reset));
  and and_7 (and_7_out, ~nRead_Write, Idle);  // AND_Gate
  RAM_part #(.addrWidth(16), .dataWidth(32), .bus("separate")) ram_3 (
    .addr(Address), .din(Data_In_2), .data(Data_Out_2), .str(and_4_out), .sel(Chip_Select), .clk(CLK),
    .ld(and_8_out), .clr(Reset));
  and and_8 (and_8_out, ~nRead_Write, Idle);  // AND_Gate
  RAM_part #(.addrWidth(16), .dataWidth(32), .bus("separate")) ram_4 (
    .addr(Address), .din(Data_In_3), .data(Data_Out_3), .str(and_5_out), .sel(Chip_Select), .clk(CLK),
    .ld(and_9_out), .clr(Reset));
  and and_9 (and_9_out, ~nRead_Write, Idle);  // AND_Gate

  assign Read_Time = 4'b0011;
  assign Write_Time = 4'b0101;

  // Other names for the same wires on the sheet: M0 = Mask[0]; M1 = Mask[1]; M2 = Mask[2]; M3 = Mask[3];
  //   RW = nRead_Write; CLR = Reset; CS = Chip_Select; Load2 = Count

  // Notes on the sheet:
  //   NO MODIFICAR
  //   excepto quizás los valores RT y WT
  //   BANK0
  //   BANK1
  //   BANK2
  //   BANK3
endmodule

module S_MIPS_Board (
  output halt
);

  wire button_1_out, CLK, CS, d_ff_1_q, R_W, Reset_out, RST, TTY_EN;
  wire [2:0] KDB;
  wire [3:0] Mask, ram_1_read_time, ram_1_write_time;
  wire [6:0] KDB_DATA, TTY_DATA;
  wire [15:0] Addr;
  wire [31:0] ram_1_data_out_0, ram_1_data_out_1, ram_1_data_out_2, ram_1_data_out_3, s_mips_1_ram_in_0,
       s_mips_1_ram_in_1, s_mips_1_ram_in_2, s_mips_1_ram_in_3;

  TTY #(.rows(25), .cols(80)) tty_1 (.data(TTY_DATA), .clk(CLK), .we(TTY_EN), .clr(RST));
  RAM ram_1 (
    .Address(Addr), .Data_Out_0(ram_1_data_out_0), .Data_Out_1(ram_1_data_out_1),
    .Data_Out_2(ram_1_data_out_2), .Data_Out_3(ram_1_data_out_3), .Data_In_0(s_mips_1_ram_in_0),
    .Data_In_1(s_mips_1_ram_in_1), .Data_In_2(s_mips_1_ram_in_2), .Data_In_3(s_mips_1_ram_in_3), .Mask(Mask),
    .nRead_Write(R_W), .Chip_Select(CS), .Read_Time(ram_1_read_time), .Reset(button_1_out),
    .Write_Time(ram_1_write_time));
  Button button_1 (.out(button_1_out));
  Keyboard #(.buflen(64)) keyboard_1 (.clk(CLK), .re(KDB[0]), .avail(KDB[2]), .data(KDB_DATA));  // open: clr
  S_MIPS s_mips_1 (
    .Kbd_Enable(KDB[0]), .Address(Addr), .Kbd_Clear(KDB[1]), .Kbd_Available(KDB[2]),
    .RAM_In_0(s_mips_1_ram_in_0), .Kbd_ASCII_Data(KDB_DATA), .RAM_In_1(s_mips_1_ram_in_1),
    .TTY_Enable(TTY_EN), .RAM_In_2(s_mips_1_ram_in_2), .RAM_In_3(s_mips_1_ram_in_3),
    .TTY_ASCII_Data(TTY_DATA), .Reset(RST), .RAM_Out_0(ram_1_data_out_0), .Clock(CLK),
    .RAM_Out_1(ram_1_data_out_1), .Stop(halt), .RAM_Out_2(ram_1_data_out_2), .RAM_Out_3(ram_1_data_out_3),
    .Mask(Mask), .Read_Time(ram_1_read_time), .Write_Time(ram_1_write_time), .nRead_Write(R_W),
    .Chip_Select(CS));
  D_Flip_Flop d_ff_1 (.clk(CLK), .D(1'b1), .Q(d_ff_1_q), .reset(Reset_out));  // open: Qn, preset, en
  Button Reset (.out(Reset_out));
  Clock clock_1 (.out(CLK));
  D_Flip_Flop d_ff_2 (.clk(CLK), .D(d_ff_1_q), .Qn(RST), .reset(Reset_out));  // open: Q, preset, en

  // Notes on the sheet:
  //   NO MODIFICAR
  //   Keyboard
endmodule

module multiplexer (
  input  [31:0] in_1,
  input  [31:0] in_2,
  input  [31:0] in_3,
  input  [31:0] in_4,
  input  [31:0] in_5,
  input  [31:0] in_6,
  input  [31:0] in_7,
  input  [31:0] in_8,
  input  [31:0] in_9,
  input  [31:0] in_10,
  input  [31:0] in_11,
  input  [31:0] in_12,
  input  [31:0] in_13,
  input  [31:0] in_14,
  input  [31:0] in_15,
  input  [31:0] in_16,
  input  [31:0] in_17,
  input  [31:0] in_18,
  input  [31:0] in_19,
  input  [31:0] in_20,
  input  [31:0] in_21,
  input  [31:0] in_22,
  input  [31:0] in_23,
  input  [31:0] in_24,
  input  [31:0] in_25,
  input  [31:0] in_26,
  input  [31:0] in_27,
  input  [31:0] in_28,
  input  [31:0] in_29,
  input  [31:0] in_30,
  input  [31:0] in_31,
  input  [4:0] in_32,
  input  [31:0] in_33,
  output [31:0] out_34
);

  wire a0, a1, a2, a3, a4, a5, a6, a7, a8, a9, a10, a11, a12, a13, a14, a15, a16, a17, a18, a19, a20, a21,
       a22, a23, a24, a25, a26, a27, a28, a29, a30, a31;

  assign out_34 = a0 ? in_1 : 32'bz;  // Controlled_Buffer controlled_buffer_1
  assign out_34 = a1 ? in_2 : 32'bz;  // Controlled_Buffer controlled_buffer_2
  assign out_34 = a2 ? in_3 : 32'bz;  // Controlled_Buffer controlled_buffer_3
  assign out_34 = a3 ? in_4 : 32'bz;  // Controlled_Buffer controlled_buffer_4
  assign out_34 = a4 ? in_5 : 32'bz;  // Controlled_Buffer controlled_buffer_5
  assign out_34 = a5 ? in_6 : 32'bz;  // Controlled_Buffer controlled_buffer_6
  assign out_34 = a6 ? in_7 : 32'bz;  // Controlled_Buffer controlled_buffer_7
  assign out_34 = a7 ? in_8 : 32'bz;  // Controlled_Buffer controlled_buffer_8
  assign out_34 = a8 ? in_9 : 32'bz;  // Controlled_Buffer controlled_buffer_9
  assign out_34 = a9 ? in_10 : 32'bz;  // Controlled_Buffer controlled_buffer_10
  assign out_34 = a10 ? in_11 : 32'bz;  // Controlled_Buffer controlled_buffer_11
  assign out_34 = a11 ? in_12 : 32'bz;  // Controlled_Buffer controlled_buffer_12
  assign out_34 = a12 ? in_13 : 32'bz;  // Controlled_Buffer controlled_buffer_13
  assign out_34 = a13 ? in_14 : 32'bz;  // Controlled_Buffer controlled_buffer_14
  assign out_34 = a14 ? in_15 : 32'bz;  // Controlled_Buffer controlled_buffer_15
  assign out_34 = a15 ? in_16 : 32'bz;  // Controlled_Buffer controlled_buffer_16
  assign out_34 = a16 ? in_17 : 32'bz;  // Controlled_Buffer controlled_buffer_17
  assign out_34 = a17 ? in_18 : 32'bz;  // Controlled_Buffer controlled_buffer_18
  assign out_34 = a18 ? in_19 : 32'bz;  // Controlled_Buffer controlled_buffer_19
  assign out_34 = a19 ? in_20 : 32'bz;  // Controlled_Buffer controlled_buffer_20
  assign out_34 = a20 ? in_21 : 32'bz;  // Controlled_Buffer controlled_buffer_21
  assign out_34 = a21 ? in_22 : 32'bz;  // Controlled_Buffer controlled_buffer_22
  assign out_34 = a22 ? in_23 : 32'bz;  // Controlled_Buffer controlled_buffer_23
  assign out_34 = a23 ? in_24 : 32'bz;  // Controlled_Buffer controlled_buffer_24
  assign out_34 = a24 ? in_25 : 32'bz;  // Controlled_Buffer controlled_buffer_25
  assign out_34 = a25 ? in_26 : 32'bz;  // Controlled_Buffer controlled_buffer_26
  assign out_34 = a26 ? in_27 : 32'bz;  // Controlled_Buffer controlled_buffer_27
  assign out_34 = a27 ? in_28 : 32'bz;  // Controlled_Buffer controlled_buffer_28
  assign out_34 = a28 ? in_29 : 32'bz;  // Controlled_Buffer controlled_buffer_29
  assign out_34 = a29 ? in_30 : 32'bz;  // Controlled_Buffer controlled_buffer_30
  assign out_34 = a30 ? in_31 : 32'bz;  // Controlled_Buffer controlled_buffer_31
  assign out_34 = a31 ? in_33 : 32'bz;  // Controlled_Buffer controlled_buffer_32
  Decoder #(.select(5)) decoder_1 (
    .out0(a0), .out1(a1), .out2(a2), .out3(a3), .out4(a4), .out5(a5), .out6(a6), .out7(a7), .out8(a8),
    .out9(a9), .out10(a10), .out11(a11), .out12(a12), .out13(a13), .out14(a14), .out15(a15), .out16(a16),
    .out17(a17), .out18(a18), .out19(a19), .out20(a20), .out21(a21), .out22(a22), .out23(a23), .out24(a24),
    .out25(a25), .out26(a26), .out27(a27), .out28(a28), .out29(a29), .out30(a30), .out31(a31), .sel(in_32));  // open: en

  // Other names for the same wires on the sheet: out[31:0] = out_34
endmodule

module S_MIPS (
  input  Kbd_Available,
  input  [6:0] Kbd_ASCII_Data,
  input  [31:0] RAM_Out_0,
  input  [31:0] RAM_Out_1,
  input  Reset,
  input  [31:0] RAM_Out_2,
  input  Clock,
  input  [31:0] RAM_Out_3,
  input  [3:0] Read_Time,
  input  [3:0] Write_Time,
  output Kbd_Enable,
  output [15:0] Address,
  output Kbd_Clear,
  output TTY_Enable,
  output [6:0] TTY_ASCII_Data,
  output Stop,
  output [31:0] RAM_In_0,
  output [31:0] RAM_In_1,
  output [31:0] RAM_In_2,
  output [31:0] RAM_In_3,
  output [3:0] Mask,
  output nRead_Write,
  output Chip_Select
);

  wire _0, add, addi, alu, \and , and_1_out, andi, beq, bgtz, blez, bltz, bne, CLK, CS_1, CS_2, div, divu,
       enRead, enRND, enSP, enWrite, halt, InstEn, InstEnab, j, jr, kbd, lw, mem, mfhi, mflo, minus_1, mul,
       mulu, Next, NextInst, nop, \nor , o_beq, o_bgtz, o_blez, o_bltz, o_bne, o_j, o_jr, \or , or_1_out,
       or_2_out, or_3_out, or_11_out, or_13_out, or_14_out, ori, pop, pop_RF, push, push_RF, R_W, RD, Ready,
       Ready_1, Ready_2, Ready_mem, ReadyR, ReadyW, rnd_t, SelD2, Sign, slt, slt_res, slti, sltiu, sltu, sub,
       sw, tty, tunnel, \xor , xori, zero, ZF;
  wire [2:0] OpCode, SelData;
  wire [4:0] multiplexer_2_out, SelRd, SelRs, SelRt;
  wire [15:0] InstAddr, MemAddr;
  wire [25:0] Dest;
  wire [31:0] adder_1_out, CACHE_INSTOUT_0, CACHE_INSTOUT_1, CACHE_INSTOUT_2, CACHE_INSTOUT_3, Cte, Data,
       Dir, Hi, instfetcher_1_instruction, KBD_Data_end, Lo, MemData, multiplexer_5_out, multiplexer_6_out,
       PC_In, PC_Out, Res, RND, Rt, slt_res_end, SP, Value;
  wire [31:7] Rs;

  and and_1 (and_1_out, enRead, ~Ready_2);  // AND_Gate
  or or_1 (or_1_out, enWrite, push_RF);
  or or_2 (or_2_out, InstEn, Reset);
  or or_3 (or_3_out, and_1_out, or_1_out);
  and and_2 (InstEnab, or_2_out, ~or_3_out);  // AND_Gate
  and and_3 (CLK, Clock, ~Stop);  // AND_Gate
  // Probe on {Rs, TTY_ASCII_Data}
  Multiplexer #(.width(16), .enable("false")) multiplexer_1 (.in0(MemAddr), .in1(InstAddr), .out(Address), .sel(CS_1));
  or or_4 (Chip_Select, CS_1, CS_2);
  CacheInst cacheinst_1 (
    .Address(PC_Out), .in_2(InstEnab), .in_3(Reset), .in_4(CLK), .RAM_Out_0(RAM_Out_0),
    .RAM_Out_1(RAM_Out_1), .RAM_Out_2(RAM_Out_2), .RAM_Out_3(RAM_Out_3), .ReadTime(Read_Time),
    .AddressOut(InstAddr), .CacheOut0(CACHE_INSTOUT_0), .CacheOut1(CACHE_INSTOUT_1),
    .CacheOut2(CACHE_INSTOUT_2), .CacheOut3(CACHE_INSTOUT_3), .CS(CS_1), .Finish(Ready));
  PC pc_1 (.RST(Reset), .CLK(CLK), .En(NextInst), .PC_Input(PC_In), .PC_Output(PC_Out));
  // Probe on PC_Out
  InstFetcher instfetcher_1 (
    .Dir(PC_Out), .in_2(CLK), .in_3(Reset), .RAM_In1(CACHE_INSTOUT_0), .RAM_In2(CACHE_INSTOUT_1),
    .RAM_In3(CACHE_INSTOUT_2), .RAM_In4(CACHE_INSTOUT_3), .Instruction(instfetcher_1_instruction),
    .Finish(Ready_1), .Ready(Ready));
  assign slt_res_end = {{31{1'b0}}, slt_res};  // Bit_Extender bit_extender_1
  assign KBD_Data_end = {{25{1'b0}}, Kbd_ASCII_Data};  // Bit_Extender bit_extender_2
  // Probe on instfetcher_1_instruction
  or or_5 (alu, div, andi, addi, add, sub, mul, mulu, divu, \and , \or , \nor , ori, xori, \xor );
  or or_6 (NextInst, Next, Ready_mem);
  or or_7 (SelData[2], mflo, kbd, mem, minus_1);
  and and_4 (minus_1, ~Kbd_Available, kbd);  // AND_Gate
  or or_8 (mem, pop, lw);
  IDecoder idecoder_1 (
    .Instruction(instfetcher_1_instruction), .pop(pop), .mfhi(mfhi), .\and (\and ), .sltu(sltu), .push(push),
    .mflo(mflo), .\or (\or ), .kbd(kbd), .jr(jr), .sub(sub), .tty(tty), .mulu(mulu), .\nor (\nor ),
    .rnd(rnd_t), .div(div), .\xor (\xor ), .halt(halt), .divu(divu), .slt(slt), .Const(Cte), .Rs(SelRs),
    .addi(addi), .add(add), .Rd(SelRd), .Rt(SelRt), .slti(slti), .mult(mul), .sltiu(sltiu), .nop(nop),
    .andi(andi), .ori(ori), .xori(xori), .lw(lw), .sw(sw), .beq(beq), .bne(bne), .blez(blez), .bgtz(bgtz),
    .bltz(bltz), .dest(Dest), .j(j));
  or or_9 (SelData[1], kbd, minus_1, alu, mfhi);
  or or_10 (SelData[0], mfhi, rnd_t, mem, minus_1);
  // Probe on multiplexer_2_out
  // Probe on SelRs
  BCU bcu_1 (
    .Inputs(o_beq), .in_2(o_bne), .in_3(o_blez), .in_4(o_bgtz), .in_5(o_bltz), .in_6(o_j), .in_7(o_jr),
    .in_8(CLK), .Next(NextInst), .Dest(Dest), .Offset(Cte), .in_12({Rs, TTY_ASCII_Data}), .in_13(PC_Out),
    .ZF(ZF), .in_15(tunnel), .SF(_0), .PC_Out(PC_In));
  // Probe on Data
  Multiplexer #(.width(5)) multiplexer_2 (.in0(SelRt), .in1(SelRd), .out(multiplexer_2_out), .sel(RD));  // open: en
  // Probe on SelRt
  Adder #(.width(32)) adder_1 (.a({Rs, TTY_ASCII_Data}), .b(Cte), .out(adder_1_out));  // open: cin, cout
  Multiplexer #(.width(32), .enable("false")) multiplexer_3 (.in0(adder_1_out), .in1(SP), .out(Dir), .sel(or_11_out));
  or or_11 (or_11_out, push, pop);
  Multiplexer #(.width(32)) multiplexer_4 (.in0(Rt), .in1({Rs, TTY_ASCII_Data}), .out(Value), .sel(push));  // open: en
  multiplexer_3x8 multiplexer_3x8_1 (
    .in_1(slt_res_end), .in_2(RND), .in_3(Res), .in_4(Hi), .in_5(Lo), .in_6(MemData), .in_7(KBD_Data_end),
    .in_8(SelData), .in_9({32{1'b1}}), .out_10(Data));
  // Probe on Rt
  or or_12 (Ready_mem, Ready_2, ReadyW);
  RegisterFile registerfile_1 (
    .Clock(CLK), .push(push_RF), .R_W(R_W), .pop(pop_RF), .Reset(Reset), .enSP(enSP),
    .Register_Selector(multiplexer_2_out), .Register_Selector_O1(SelRs), .Register_Selector_O2(SelRt),
    .Data(Data), .Register_1({Rs, TTY_ASCII_Data}), .Register_2(Rt), .SP(SP));
  CU cu_1 (
    .nop(nop), .divu(divu), .pop(pop), .halt(halt), .andi(andi), .sw(sw), .Next(Next), .add(add),
    .\and (\and ), .slt(slt), .kbd(kbd), .ori(ori), .beq(beq), .OpCode(OpCode), .sub(sub), .\or (\or ),
    .sltu(sltu), .rnd(rnd_t), .xori(xori), .bne(bne), .Sign(Sign), .mul(mul), .\nor (\nor ), .jr(jr),
    .tty(tty), .slt_2(slti), .blez(blez), .beq_2(o_beq), .mulu(mulu), .\xor (\xor ), .mfhi(mfhi), .j(j),
    .sltiu(sltiu), .bgtz(bgtz), .bne_2(o_bne), .blez_2(o_blez), .div(div), .push(push), .mflo(mflo),
    .addi(addi), .lw(lw), .bltz(bltz), .bgtz_2(o_bgtz), .bltz_2(o_bltz), .j_2(o_j), .jr_2(o_jr),
    .enRND(enRND), .STOP(Stop), .enRead(enRead), .enWrite(enWrite), .pushRF(push_RF), .popRF(pop_RF),
    .enSP(enSP), .R_W(R_W), .ready_inst(Ready_1), .CLK(CLK), .InstEnab(InstEn), .TTYEnab(TTY_Enable),
    .KBDEnab(Kbd_Enable), .ready_mem(Ready_mem));
  ReadMemory readmemory_1 (
    .Dir(Dir), .in_2(CLK), .in_3(ReadyR), .in_4(Reset), .RAM_In1(RAM_In_0), .RAM_In2(RAM_In_1),
    .RAM_In3(RAM_In_2), .RAM_In4(RAM_In_3), .RAM_Out(MemData), .Finish(Ready_2));
  and and_5 (RD, or_13_out, ~SelD2);  // AND_Gate
  // Probe on OpCode
  or or_13 (or_13_out, sltu, pop, kbd, mflo, alu, rnd_t, mfhi, slt);
  CacheData cachedata_1 (
    .Address(Dir), .in_2(or_14_out), .in_3(Reset), .in_4(CLK), .in_5(enWrite), .RAM_Out_0(RAM_Out_0),
    .RAM_Out_1(RAM_Out_1), .RAM_Out_2(RAM_Out_2), .RAM_Out_3(RAM_Out_3), .Value(Value), .ReadTime(Read_Time),
    .WriteTime(Write_Time), .AddressOut(MemAddr), .CacheOut0(RAM_In_0), .CacheOut1(RAM_In_1),
    .CacheOut2(RAM_In_2), .CacheOut3(RAM_In_3), .CS(CS_2), .FinishRead(ReadyR), .RAM_R_W(nRead_Write),
    .Mask(Mask), .FinishWrt(ReadyW));
  or or_14 (or_14_out, enRead, enWrite);
  // Probe on {Rs, TTY_ASCII_Data}
  random random_1 (.Clock(CLK), .Enable(enRND), .Output(RND));
  Multiplexer #(.width(32), .enable("false")) multiplexer_5 (.in0(Rt), .in1(Cte), .out(multiplexer_5_out), .sel(SelD2));
  or or_15 (SelD2, addi, andi, ori, xori, slti, sltiu);
  Multiplexer #(.width(32), .enable("false")) multiplexer_6 (
    .in0(multiplexer_5_out), .in1({32{1'b0}}), .out(multiplexer_6_out), .sel(zero));
  ALU alu_1 (
    .Clock(CLK), .Sign(Sign), .Reset(Reset), .Data_In1({Rs, TTY_ASCII_Data}), .Data_In2(multiplexer_6_out),
    .ALU_Op_Code(OpCode), .Operation_Value(Res), .Hi_Value(Hi), .Lo_Value(Lo), .out_7(ZF), .out_8(_0),
    .out_9(tunnel), .out_10(slt_res));
  or or_16 (zero, blez, bgtz, bltz);
  // Probe on multiplexer_6_out
  // Probe on Res

  assign Kbd_Clear = Reset;

  // Other names for the same wires on the sheet: CS = Chip_Select; KBD_AVAIL = Kbd_Available; CLR = Reset;
  //   KBD_CLR = Reset; KBD_DATA[6:0] = Kbd_ASCII_Data; RAM_A[15:0] = Address; CACHE_OUTPUT_0[31:0] = RAM_In_0;
  //   RAM_INPUT_0[31:0] = RAM_In_0; CACHE_OUTPUT_1[31:0] = RAM_In_1; RAM_INPUT_1[31:0] = RAM_In_1;
  //   CACHE_OUTPUT_2[31:0] = RAM_In_2; RAM_INPUT_2[31:0] = RAM_In_2; CACHE_OUTPUT_3[31:0] = RAM_In_3;
  //   RAM_INPUT_3[31:0] = RAM_In_3; RAM_OUTPUT_0[31:0] = RAM_Out_0; RAM_OUTPUT_1[31:0] = RAM_Out_1;
  //   RAM_OUTPUT_2[31:0] = RAM_Out_2; RAM_OUTPUT_3[31:0] = RAM_Out_3; Rs[6:0] = TTY_ASCII_Data;
  //   TTY_DATA[6:0] = TTY_ASCII_Data; RW = nRead_Write

  // Notes on the sheet:
  //   RAM ADDRESS
  //   DATA FROM RAM
  //   DATA TO RAM
  //   DATA WRITE MASK
  //   RAM TIMING
  //   RAM CONTROL
  //   KEYBOARD
  //   TTY
  //   SEQUENCING
  //   TTY
endmodule

module RegisterFile (
  input  Clock,
  input  push,
  input  R_W,
  input  pop,
  input  Reset,
  input  enSP,
  input  [4:0] Register_Selector,
  input  [4:0] Register_Selector_O1,
  input  [4:0] Register_Selector_O2,
  input  [31:0] Data,
  output [31:0] Register_1,
  output [31:0] Register_2,
  output [31:0] SP
);

  wire enab_SP, L0, L1, L2, L3, L4, L5, L6, L7, L8, L9, L10, L11, L12, L13, L14, L15, L16, L17, L18, L19,
       L20, L21, L22, L23, L24, L25, L26, L27, L28, L29, L30, LSP, modify;
  wire [31:0] adder_1_out, LDSP, multiplexer_2_out, R0, R1, R2, R3, R4, R5, R6, R7, R8, R9, R10, R11, R12,
       R13, R14, R15, R16, R17, R18, R19, R20, R21, R22, R23, R24, R25, R26, R27, R28, R29, R30,
       subtractor_1_out;

  multiplexer multiplexer_1 (
    .in_1(R0), .in_2(R1), .in_3(R2), .in_4(R3), .in_5(R4), .in_6(R5), .in_7(R6), .in_8(R7), .in_9(R8),
    .in_10(R9), .in_11(R10), .in_12(R11), .in_13(R12), .in_14(R13), .in_15(R14), .in_16(R15), .in_17(R16),
    .in_18(R17), .in_19(R18), .in_20(R19), .in_21(R20), .in_22(R21), .in_23(R22), .in_24(R23), .in_25(R24),
    .in_26(R25), .in_27(R26), .in_28(R27), .in_29(R28), .in_30(R29), .in_31(R30), .in_33(SP),
    .in_32(Register_Selector_O1), .out_34(Register_1));
  Adder #(.width(32)) adder_1 (.a(SP), .b(32'h4), .out(adder_1_out));  // open: cin, cout
  Subtractor #(.width(32)) subtractor_1 (.a(SP), .b(32'h4), .out(subtractor_1_out));  // open: bin, bout
  Multiplexer #(.width(32), .enable("false")) multiplexer_2 (
    .in0(adder_1_out), .in1(subtractor_1_out), .out(multiplexer_2_out), .sel(push));
  Register #(.width(32)) R0_cte (.D({32{1'b0}}), .en(L0), .Q(R0), .clk(Clock), .clr(Reset));
  Register #(.width(32)) u_R1 (.D(Data), .en(L1), .Q(R1), .clk(Clock), .clr(Reset));
  Register #(.width(32)) u_R2 (.D(Data), .en(L2), .Q(R2), .clk(Clock), .clr(Reset));
  Register #(.width(32)) u_R3 (.D(Data), .en(L3), .Q(R3), .clk(Clock), .clr(Reset));
  Register #(.width(32)) u_R4 (.D(Data), .en(L4), .Q(R4), .clk(Clock), .clr(Reset));
  Register #(.width(32)) u_R5 (.D(Data), .en(L5), .Q(R5), .clk(Clock), .clr(Reset));
  Register #(.width(32)) u_R6 (.D(Data), .en(L6), .Q(R6), .clk(Clock), .clr(Reset));
  Register #(.width(32)) u_R7 (.D(Data), .en(L7), .Q(R7), .clk(Clock), .clr(Reset));
  Multiplexer #(.width(32), .enable("false")) multiplexer_3 (
    .in0(SP), .in1(multiplexer_2_out), .out(LDSP), .sel(modify));
  Register #(.width(32)) u_R8 (.D(Data), .en(L8), .Q(R8), .clk(Clock), .clr(Reset));
  Register #(.width(32)) u_R9 (.D(Data), .en(L9), .Q(R9), .clk(Clock), .clr(Reset));
  Register #(.width(32)) u_R10 (.D(Data), .en(L10), .Q(R10), .clk(Clock));  // open: clr
  Register #(.width(32)) u_R11 (.D(Data), .en(L11), .Q(R11), .clk(Clock), .clr(Reset));
  Register #(.width(32)) u_R12 (.D(Data), .en(L12), .Q(R12), .clk(Clock), .clr(Reset));
  Register #(.width(32)) u_R13 (.D(Data), .en(L13), .Q(R13), .clk(Clock), .clr(Reset));
  Register #(.width(32)) u_R14 (.D(Data), .en(L14), .Q(R14), .clk(Clock), .clr(Reset));
  Register #(.width(32)) u_R15 (.D(Data), .en(L15), .Q(R15), .clk(Clock), .clr(Reset));
  // Probe on Register_2
  Register #(.width(32)) u_R16 (.D(Data), .en(L16), .Q(R16), .clk(Clock), .clr(Reset));
  Register #(.width(32)) u_R17 (.D(Data), .en(L17), .Q(R17), .clk(Clock), .clr(Reset));
  Register #(.width(32)) u_R18 (.D(Data), .en(L18), .Q(R18), .clk(Clock), .clr(Reset));
  Register #(.width(32)) u_R19 (.D(Data), .en(L19), .Q(R19), .clk(Clock), .clr(Reset));
  Register #(.width(32)) u_R20 (.D(Data), .en(L20), .Q(R20), .clk(Clock), .clr(Reset));
  Register #(.width(32)) u_R21 (.D(Data), .en(L21), .Q(R21), .clk(Clock), .clr(Reset));
  Register #(.width(32)) u_R22 (.D(Data), .en(L22), .Q(R22), .clk(Clock), .clr(Reset));
  Register #(.width(32)) u_R23 (.D(Data), .en(L23), .Q(R23), .clk(Clock), .clr(Reset));
  multiplexer multiplexer_4 (
    .in_1(R0), .in_2(R1), .in_3(R2), .in_4(R3), .in_5(R4), .in_6(R5), .in_7(R6), .in_8(R7), .in_9(R8),
    .in_10(R9), .in_11(R10), .in_12(R11), .in_13(R12), .in_14(R13), .in_15(R14), .in_16(R15), .in_17(R16),
    .in_18(R17), .in_19(R18), .in_20(R19), .in_21(R20), .in_22(R21), .in_23(R22), .in_24(R23), .in_25(R24),
    .in_26(R25), .in_27(R26), .in_28(R27), .in_29(R28), .in_30(R29), .in_31(R30), .in_33(SP),
    .in_32(Register_Selector_O2), .out_34(Register_2));
  or or_1 (enab_SP, enSP, LSP);
  or or_2 (modify, pop, push);
  Register #(.width(32)) u_R24 (.D(Data), .en(L24), .Q(R24), .clk(Clock), .clr(Reset));
  Register #(.width(32)) u_R25 (.D(Data), .en(L25), .Q(R25), .clk(Clock), .clr(Reset));
  Register #(.width(32)) u_R26 (.D(Data), .en(L26), .Q(R26), .clk(Clock), .clr(Reset));
  Register #(.width(32)) u_R27 (.D(Data), .en(L27), .Q(R27), .clk(Clock), .clr(Reset));
  Register #(.width(32)) u_R28 (.D(Data), .en(L28), .Q(R28), .clk(Clock), .clr(Reset));
  Register #(.width(32)) u_R29 (.D(Data), .en(L29), .Q(R29), .clk(Clock), .clr(Reset));
  Register #(.width(32)) u_R30 (.D(Data), .en(L30), .Q(R30), .clk(Clock), .clr(Reset));
  Register #(.width(32)) SP_R31 (.D(LDSP), .en(enab_SP), .Q(SP), .clk(Clock), .clr(Reset));
  Demultiplexer #(.select(5), .enable("false")) demultiplexer_1 (
    .out0(L0), .out1(L1), .out2(L2), .out3(L3), .out4(L4), .out5(L5), .out6(L6), .out7(L7), .out8(L8),
    .out9(L9), .out10(L10), .out11(L11), .out12(L12), .out13(L13), .out14(L14), .out15(L15), .out16(L16),
    .out17(L17), .out18(L18), .out19(L19), .out20(L20), .out21(L21), .out22(L22), .out23(L23), .out24(L24),
    .out25(L25), .out26(L26), .out27(L27), .out28(L28), .out29(L29), .out30(L30), .out31(LSP), .in(R_W),
    .sel(Register_Selector));

  // Other names for the same wires on the sheet: CLK = Clock; LD[31:0] = Data; O1[31:0] = Register_1;
  //   O2[31:0] = Register_2; RO1[4:0] = Register_Selector_O1; RO2[4:0] = Register_Selector_O2;
  //   RS[4:0] = Register_Selector; RST = Reset

  // Notes on the sheet:
  //   INPUTS
  //   OUTPUTS
  //   SP
  //   REGISTERS
endmodule

module IDecoder (
  input  [31:0] Instruction,
  output [25:0] dest,
  output pop,
  output mfhi,
  output \and ,
  output sltu,
  output push,
  output mflo,
  output \or ,
  output kbd,
  output jr,
  output sub,
  output tty,
  output mulu,
  output \nor ,
  output rnd,
  output div,
  output \xor ,
  output add,
  output mult,
  output nop,
  output halt,
  output divu,
  output slt,
  output addi,
  output slti,
  output sltiu,
  output andi,
  output ori,
  output xori,
  output lw,
  output sw,
  output beq,
  output bne,
  output blez,
  output bgtz,
  output bltz,
  output j,
  output [31:0] Const,
  output [4:0] Rs,
  output [4:0] Rd,
  output [4:0] Rt
);

  wire _000000, _111000, _111111, and_2_out, and_6_out, and_9_out, and_t, div_t, divu_t, enableR, halt_t,
       jr_t, kbd_t, mfhi_t, mflo_t, mulu_t, nor_t, or_1_out, or_t, pop_t, push_t, rnd_t, slt_t, sltu_t,
       sub_t, tty_t, xor_t;

  and u_addi (addi, ~Instruction[31], ~Instruction[30], Instruction[29], ~Instruction[28], ~Instruction[27], ~Instruction[26]);  // AND_Gate
  and and_1 (_000000, ~Instruction[31], ~Instruction[30], ~Instruction[29], ~Instruction[28], ~Instruction[27], ~Instruction[26]);  // AND_Gate
  and and_2 (and_2_out, Instruction[5], ~Instruction[4], ~Instruction[3], ~Instruction[2], ~Instruction[1], ~Instruction[0]);  // AND_Gate
  and and_3 (add, and_2_out, _000000);
  and and_4 (j, ~Instruction[31], ~Instruction[30], ~Instruction[29], ~Instruction[28], Instruction[27], ~Instruction[26]);  // AND_Gate
  and and_5 (_111000, Instruction[31], Instruction[30], Instruction[29], ~Instruction[28], ~Instruction[27], ~Instruction[26]);  // AND_Gate
  and and_6 (and_6_out, ~Instruction[5], Instruction[4], Instruction[3], ~Instruction[2], ~Instruction[1], ~Instruction[0]);  // AND_Gate
  and u_slti (slti, ~Instruction[31], ~Instruction[30], Instruction[29], ~Instruction[28], Instruction[27], ~Instruction[26]);  // AND_Gate
  and and_7 (mult, and_6_out, _000000);
  and and_8 (_111111, Instruction[31], Instruction[30], Instruction[29], Instruction[28], Instruction[27], Instruction[26]);
  and and_9 (and_9_out, ~Instruction[5], ~Instruction[4], ~Instruction[3], ~Instruction[2], ~Instruction[1], ~Instruction[0]);  // AND_Gate
  and and_10 (nop, and_9_out, _000000);
  and u_sltiu (sltiu, ~Instruction[31], ~Instruction[30], Instruction[29], ~Instruction[28], Instruction[27], Instruction[26]);  // AND_Gate
  and u_andi (andi, ~Instruction[31], ~Instruction[30], Instruction[29], Instruction[28], ~Instruction[27], ~Instruction[26]);  // AND_Gate
  Decoder decoder_1 (.out0(pop_t), .out1(push_t), .sel(Instruction[0]), .en(_111000));
  and and_11 (enableR, _000000, ~add, ~mult, ~nop);  // AND_Gate
  and u_ori (ori, ~Instruction[31], ~Instruction[30], Instruction[29], Instruction[28], ~Instruction[27], Instruction[26]);  // AND_Gate
  Decoder #(.select(2)) decoder_2 (
    .out0(kbd_t), .out1(tty_t), .out2(rnd_t), .out3(halt_t), .sel(Instruction[1:0]), .en(_111111));
  and u_xori (xori, ~Instruction[31], ~Instruction[30], Instruction[29], Instruction[28], Instruction[27], ~Instruction[26]);  // AND_Gate
  Multiplexer #(.width(32), .enable("false")) multiplexer_1 (
    .in0({{17{Instruction[15]}}, Instruction[14:0]}), .in1({{16{1'b0}}, Instruction[15:0]}), .out(Const),
    .sel(or_1_out));
  or or_1 (or_1_out, andi, ori, xori);
  Decoder #(.select(4)) decoder_3 (
    .out0(mfhi_t), .out2(mflo_t), .out4(jr_t), .out5(mulu_t), .out6(div_t), .out7(divu_t), .out8(and_t),
    .out9(or_t), .out10(sub_t), .out11(nor_t), .out12(xor_t), .out14(slt_t), .out15(sltu_t),
    .sel({Instruction[5], Instruction[3], Instruction[1:0]}), .en(enableR));  // open: out1, out3, out13
  and u_lw (lw, Instruction[31], ~Instruction[30], ~Instruction[29], ~Instruction[28], Instruction[27], Instruction[26]);  // AND_Gate
  and u_sw (sw, Instruction[31], ~Instruction[30], Instruction[29], ~Instruction[28], Instruction[27], Instruction[26]);  // AND_Gate
  Multiplexer #(.enable("false")) multiplexer_2 (.in0(1'b0), .in1(pop_t), .out(pop), .sel(_111000));
  Multiplexer #(.enable("false")) multiplexer_3 (.in0(1'b0), .in1(push_t), .out(push), .sel(_111000));
  Multiplexer #(.enable("false")) multiplexer_4 (.in0(1'b0), .in1(kbd_t), .out(kbd), .sel(_111111));
  Multiplexer #(.enable("false")) multiplexer_5 (.in0(1'b0), .in1(tty_t), .out(tty), .sel(_111111));
  Multiplexer #(.enable("false")) multiplexer_6 (.in0(1'b0), .in1(rnd_t), .out(rnd), .sel(_111111));
  Multiplexer #(.enable("false")) multiplexer_7 (.in0(1'b0), .in1(halt_t), .out(halt), .sel(_111111));
  and u_beq (beq, ~Instruction[31], ~Instruction[30], ~Instruction[29], Instruction[28], ~Instruction[27], ~Instruction[26]);  // AND_Gate
  and u_bne (bne, ~Instruction[31], ~Instruction[30], ~Instruction[29], Instruction[28], ~Instruction[27], Instruction[26]);  // AND_Gate
  Multiplexer #(.enable("false")) multiplexer_8 (.in0(1'b0), .in1(mfhi_t), .out(mfhi), .sel(enableR));
  Multiplexer #(.enable("false")) multiplexer_9 (.in0(1'b0), .in1(mflo_t), .out(mflo), .sel(enableR));
  Multiplexer #(.enable("false")) multiplexer_10 (.in0(1'b0), .in1(jr_t), .out(jr), .sel(enableR));
  Multiplexer #(.enable("false")) multiplexer_11 (.in0(1'b0), .in1(mulu_t), .out(mulu), .sel(enableR));
  Multiplexer #(.enable("false")) multiplexer_12 (.in0(1'b0), .in1(div_t), .out(div), .sel(enableR));
  Multiplexer #(.enable("false")) multiplexer_13 (.in0(1'b0), .in1(divu_t), .out(divu), .sel(enableR));
  and branch (blez, ~Instruction[31], ~Instruction[30], ~Instruction[29], Instruction[28], Instruction[27], ~Instruction[26]);  // AND_Gate
  Multiplexer #(.enable("false")) multiplexer_14 (.in0(1'b0), .in1(and_t), .out(\and ), .sel(enableR));
  Multiplexer #(.enable("false")) multiplexer_15 (.in0(1'b0), .in1(or_t), .out(\or ), .sel(enableR));
  Multiplexer #(.enable("false")) multiplexer_16 (.in0(1'b0), .in1(sub_t), .out(sub), .sel(enableR));
  Multiplexer #(.enable("false")) multiplexer_17 (.in0(1'b0), .in1(nor_t), .out(\nor ), .sel(enableR));
  Multiplexer #(.enable("false")) multiplexer_18 (.in0(1'b0), .in1(xor_t), .out(\xor ), .sel(enableR));
  Multiplexer #(.enable("false")) multiplexer_19 (.in0(1'b0), .in1(slt_t), .out(slt), .sel(enableR));
  and branch_2 (bgtz, ~Instruction[31], ~Instruction[30], ~Instruction[29], Instruction[28], Instruction[27], Instruction[26]);  // AND_Gate
  and branch_3 (bltz, ~Instruction[31], ~Instruction[30], ~Instruction[29], ~Instruction[28], ~Instruction[27], Instruction[26]);  // AND_Gate
  Multiplexer #(.enable("false")) multiplexer_20 (.in0(1'b0), .in1(sltu_t), .out(sltu), .sel(enableR));

  assign dest = Instruction[25:0];
  assign Rd = Instruction[15:11];
  assign Rs = Instruction[25:21];
  assign Rt = Instruction[20:16];

  // Other names for the same wires on the sheet: _0 = Instruction[0]; Constant_C_2[15:0] = Instruction[15:0];
  //   _1 = Instruction[1]; _2 = Instruction[2]; _3 = Instruction[3]; _4 = Instruction[4]; _5 = Instruction[5];
  //   _6 = Instruction[6]; _7 = Instruction[7]; _8 = Instruction[8]; _9 = Instruction[9]; _10 = Instruction[10];
  //   _11 = Instruction[11]; _12 = Instruction[12]; _13 = Instruction[13]; _14 = Instruction[14];
  //   _15 = Instruction[15]; _16 = Instruction[16]; _17 = Instruction[17]; _18 = Instruction[18];
  //   _19 = Instruction[19]; _20 = Instruction[20]; _21 = Instruction[21]; _22 = Instruction[22];
  //   _23 = Instruction[23]; _24 = Instruction[24]; _25 = Instruction[25]; _26 = Instruction[26];
  //   _27 = Instruction[27]; _28 = Instruction[28]; _29 = Instruction[29]; _30 = Instruction[30];
  //   _31 = Instruction[31]

  // Notes on the sheet:
  //   I Instructions
  //   Jump
  //   R Instructions
endmodule

module PC (
  input  RST,
  input  CLK,
  input  En,
  input  [31:0] PC_Input,
  output [31:0] PC_Output
);

  Register #(.width(32)) register_1 (.D(PC_Input), .en(En), .Q(PC_Output), .clk(CLK), .clr(RST));

  // Other names for the same wires on the sheet: enable = En; PC_in[31:0] = PC_Input; PC_out[31:0] = PC_Output

  // Notes on the sheet:
  //   PC
  //   Inputs
  //   Outputs
endmodule

module BCU (
  input  Inputs,
  input  in_2,
  input  in_3,
  input  in_4,
  input  in_5,
  input  in_6,
  input  in_7,
  input  in_8,
  input  Next,
  input  [25:0] Dest,
  input  [31:0] Offset,
  input  [31:0] in_12,
  input  [31:0] in_13,
  input  ZF,
  input  in_15,
  input  SF,
  output [31:0] PC_Out
);

  wire and_1_out, and_2_out, and_3_out, and_4_out, and_5_out, and_6_out, branch, jmp, nor_1_out, not_1_out,
       not_2_out, or_1_out;
  wire [31:0] BranchAddress, multiplexer_1_out, multiplexer_2_out, PC_4;

  not not_1 (not_1_out, in_15);
  or or_1 (or_1_out, ZF, SF);
  nor nor_1 (nor_1_out, ZF, SF);
  not not_2 (not_2_out, ZF);
  Adder #(.width(32)) adder_1 (.a(in_13), .b(32'h4), .out(PC_4));  // open: cin, cout
  and and_1 (and_1_out, Inputs, in_15);
  and and_2 (and_2_out, not_1_out, in_2);
  and and_3 (and_3_out, in_3, or_1_out);
  and and_4 (and_4_out, in_4, nor_1_out);
  and and_5 (and_5_out, in_5, and_6_out);
  and and_6 (and_6_out, SF, not_2_out);
  or or_2 (branch, and_1_out, and_2_out, and_3_out, and_4_out, and_5_out);
  Adder #(.width(32)) adder_2 (.a(PC_4), .b({Offset[29:0], 2'b00}), .out(BranchAddress));  // open: cin, cout
  or or_3 (jmp, branch, in_6, in_7);
  Multiplexer #(.select(2), .width(32)) multiplexer_1 (
    .in0(BranchAddress), .in1(in_12), .in2({in_13[31:28], Dest, 2'b00}), .out(multiplexer_1_out),
    .sel({in_6, in_7}));  // open: in3, en
  Multiplexer #(.width(32)) multiplexer_2 (
    .in0(PC_4), .in1(multiplexer_1_out), .out(multiplexer_2_out), .sel(jmp));  // open: en
  Multiplexer #(.width(32)) multiplexer_3 (.in0(in_13), .in1(multiplexer_2_out), .out(PC_Out), .sel(Next));  // open: en

  // Other names for the same wires on the sheet: jr = in_7; j = in_6; _0 = SF; beq = Inputs; bgtz = in_4; blez = in_3;
  //   bltz = in_5; bne = in_2; CLK = in_8; Destination[31:2] = {in_13[31:28], Dest}; PC_In[31:0] = in_13;
  //   Rs[31:0] = in_12; S_Offset[31:2] = Offset[29:0]; tunnel = in_15
endmodule

module CU (
  input  nop,
  input  divu,
  input  pop,
  input  halt,
  input  andi,
  input  sw,
  input  ready_mem,
  input  ready_inst,
  input  add,
  input  \and ,
  input  slt,
  input  kbd,
  input  ori,
  input  beq,
  input  CLK,
  input  sub,
  input  \or ,
  input  sltu,
  input  rnd,
  input  xori,
  input  bne,
  input  mul,
  input  \nor ,
  input  jr,
  input  tty,
  input  slt_2,
  input  blez,
  input  mulu,
  input  \xor ,
  input  mfhi,
  input  j,
  input  sltiu,
  input  bgtz,
  input  div,
  input  push,
  input  mflo,
  input  addi,
  input  lw,
  input  bltz,
  output Next,
  output [2:0] OpCode,
  output Sign,
  output beq_2,
  output bne_2,
  output blez_2,
  output bgtz_2,
  output bltz_2,
  output j_2,
  output jr_2,
  output enRND,
  output STOP,
  output enRead,
  output enWrite,
  output pushRF,
  output popRF,
  output enSP,
  output R_W,
  output InstEnab,
  output TTYEnab,
  output KBDEnab
);

  wire _0, _0_t, _0_t_t, _0_t_t_t, _0_t_t_t_t, _0_t_t_t_t_t, _0_t_t_t_t_t_t, _1, _1_t, _1_t_t, _1_t_t_t,
       _1_t_t_t_t, _1_t_t_t_t_t, _1_t_t_t_t_t_t, _2, _2_t, _3, _4, and_37_out, d_ff_2_q, d_ff_2_qn,
       demultiplexer_1_out0, En, En_8, EnLect_0, EnLect_1, EnWrt_0, EnWrt_1, j_end, jr_end, mfhi_end,
       mflo_end, NextInst, nop_end, or_9_out, or_13_out, R__W_14, R__W_15, R__W_16, R__W_17, R_W_22, Sel,
       tunnel_t, tunnel_t_t, tunnel_t_t_t, tunnel_t_t_t_t, tunnel_t_t_t_t_t, tunnel_t_t_t_t_t_t,
       tunnel_t_t_t_t_t_t_t;
  wire [2:0] priority_encoder_1_out;

  Priority_Encoder priority_encoder_1 (
    .in0(tunnel_t_t_t), .in1(tunnel_t_t_t_t), .in2(tunnel_t), .in3(En_8), .in4(tunnel_t_t_t_t_t_t_t),
    .in5(tunnel_t_t_t_t_t_t), .in6(tunnel_t_t), .in7(tunnel_t_t_t_t_t), .out(priority_encoder_1_out),
    .en_in(En));  // open: gs, en_out
  and and_1 (_0_t_t, NextInst, add);
  and and_2 (_0_t_t_t, NextInst, sub);
  and and_3 (_0_t, NextInst, mul);
  and and_4 (_1_t, NextInst, mulu);
  and and_5 (_0_t_t_t_t, NextInst, div);
  and and_6 (_1_t_t_t_t, NextInst, divu);
  and and_7 (_0, NextInst, \and );
  and and_8 (_0_t_t_t_t_t_t, NextInst, \or );
  and and_9 (En_8, NextInst, \nor );
  and and_10 (_0_t_t_t_t_t, NextInst, \xor );
  and and_11 (_1_t_t, NextInst, addi);
  and and_12 (_1, NextInst, andi);
  and and_13 (_1_t_t_t_t_t_t, NextInst, ori);
  and and_14 (_1_t_t_t_t_t, NextInst, xori);
  and and_15 (R__W_14, NextInst, slt);
  and and_16 (R__W_15, NextInst, sltu);
  and and_17 (R__W_16, NextInst, slt_2);
  and and_18 (R__W_17, NextInst, sltiu);
  and and_19 (jr_end, NextInst, jr);
  and and_20 (_1_t_t_t, NextInst, beq);
  and and_21 (_2_t, NextInst, bne);
  and and_22 (_2, NextInst, blez);
  and and_23 (_3, NextInst, bgtz);
  and and_24 (_4, NextInst, bltz);
  and and_25 (mfhi_end, NextInst, mfhi);
  and and_26 (mflo_end, NextInst, mflo);
  and and_27 (enRND, NextInst, rnd);
  and and_28 (STOP, NextInst, halt);
  and and_29 (EnLect_0, NextInst, pop);
  and and_30 (pushRF, NextInst, push);
  and and_31 (EnLect_1, NextInst, lw);
  and and_32 (EnWrt_1, NextInst, sw);
  and and_33 (nop_end, NextInst, nop);
  and and_34 (j_end, NextInst, j);
  and and_35 (TTYEnab, NextInst, tty);
  and and_36 (KBDEnab, NextInst, kbd);
  Multiplexer #(.width(3), .enable("false")) multiplexer_1 (
    .in0(priority_encoder_1_out), .in1(3'b000), .out(OpCode), .sel(Sel));
  and and_37 (and_37_out, ~EnWrt_0, pushRF);  // AND_Gate
  or or_1 (tunnel_t_t_t, _0_t_t, _1_t_t, _2, _3, _4);
  or or_2 (tunnel_t_t_t_t, _0_t_t_t, _1_t_t_t, _2_t);
  or or_3 (tunnel_t_t, _0_t, _1_t);
  or or_4 (tunnel_t_t_t_t_t, _0_t_t_t_t, _1_t_t_t_t);
  or or_5 (tunnel_t, _0, _1);
  or or_6 (tunnel_t_t_t_t_t_t_t, _0_t_t_t_t_t_t, _1_t_t_t_t_t_t);
  or or_7 (tunnel_t_t_t_t_t_t, _0_t_t_t_t_t, _1_t_t_t_t_t);
  D_Flip_Flop d_ff_1 (.clk(CLK), .D(and_37_out), .Q(EnWrt_0));  // open: Qn, preset, en, reset
  and and_38 (R_W_22, lw, ready_mem);
  or or_8 (En, _2, _3, _1_t_t_t_t_t, _0_t_t, _0_t_t_t, _0_t, _1_t, _0_t_t_t_t, _1_t_t_t_t, _4, _0, _0_t_t_t_t_t_t, En_8, _0_t_t_t_t_t, _1_t_t, _1, _1_t_t_t_t_t_t, _1_t_t_t, _2_t);
  or or_9 (or_9_out, demultiplexer_1_out0, Next);
  and and_39 (popRF, ready_mem, pop);
  D_Flip_Flop d_ff_2 (.clk(CLK), .D(or_9_out), .Q(d_ff_2_q), .Qn(d_ff_2_qn), .preset(d_ff_2_qn));  // open: en, reset
  or or_10 (Sign, _0_t, _0_t_t_t_t, R__W_14, R__W_16, _1_t_t_t, _2_t, _2, _3, _4);
  or or_11 (enRead, EnLect_0, EnLect_1);
  or or_12 (enWrite, EnWrt_0, EnWrt_1);
  Demultiplexer #(.enable("false")) demultiplexer_1 (
    .out0(demultiplexer_1_out0), .out1(InstEnab), .in(d_ff_2_q), .sel(or_13_out));
  or or_13 (or_13_out, ready_inst, ready_mem);
  or or_14 (R_W, mfhi_end, mflo_end, _0_t_t, _0_t_t_t, _0_t, _1_t, _0_t_t_t_t, _1_t_t_t_t, _0, _0_t_t_t_t_t_t, En_8, _0_t_t_t_t_t, _1_t_t, _1, _1_t_t_t_t_t_t, _1_t_t_t_t_t, R__W_14, R__W_15, R__W_16, R__W_17, jr_end, popRF, R_W_22, KBDEnab);
  and and_40 (NextInst, InstEnab, ~ready_mem);  // AND_Gate
  or or_15 (enSP, popRF, pushRF);
  nor nor_1 (Sel, tunnel_t_t_t, tunnel_t_t_t_t, tunnel_t, En_8, tunnel_t_t_t_t_t_t_t, tunnel_t_t_t_t_t_t, tunnel_t_t, tunnel_t_t_t_t_t);
  or or_16 (Next, mflo_end, nop_end, _0_t_t, _0_t_t_t, _0_t, _1_t, _0_t_t_t_t, _1_t_t_t_t, _0, _0_t_t_t_t_t_t, En_8, _0_t_t_t_t_t, _1_t_t, _1, _1_t_t_t_t_t_t, _1_t_t_t_t_t, R__W_14, R__W_15, R__W_16, R__W_17, jr_end, j_end, _1_t_t_t, _2_t, _2, _3, _4, STOP, enRND, mfhi_end, KBDEnab, TTYEnab);

  assign beq_2 = beq;
  assign bgtz_2 = bgtz;
  assign blez_2 = blez;
  assign bltz_2 = bltz;
  assign bne_2 = bne;
  assign j_2 = j;
  assign jr_2 = jr;

  // Other names for the same wires on the sheet: En_7 = _0_t_t_t_t_t_t; or_end = _0_t_t_t_t_t_t;
  //   R__W_7 = _0_t_t_t_t_t_t; En_12 = _1_t_t_t_t_t_t; ori_end = _1_t_t_t_t_t_t; R__W_12 = _1_t_t_t_t_t_t;
  //   add_end = _0_t_t; En_0 = _0_t_t; R__W_0 = _0_t_t; addi_end = _1_t_t; En_10 = _1_t_t; R__W_10 = _1_t_t;
  //   and_end = _0; En_6 = _0; R__W_6 = _0; andi_end = _1; En_11 = _1; R__W_11 = _1; beq_end = _1_t_t_t;
  //   En_14 = _1_t_t_t; Sign_4 = _1_t_t_t; bgtz_end = _3; En_17 = _3; Sign_7 = _3; blez_end = _2; En_16 = _2;
  //   Sign_6 = _2; bltz_end = _4; En_18 = _4; Sign_8 = _4; bne_end = _2_t; En_15 = _2_t; Sign_5 = _2_t;
  //   div_end = _0_t_t_t_t; En_4 = _0_t_t_t_t; R__W_4 = _0_t_t_t_t; Sign_1 = _0_t_t_t_t; divu_end = _1_t_t_t_t;
  //   En_5 = _1_t_t_t_t; R__W_5 = _1_t_t_t_t; EnLect = enRead; enSP_0 = popRF; R_W_21 = popRF; enSP_1 = pushRF;
  //   EnWrt = enWrite; halt_end = STOP; R__W_18 = jr_end; kbd_enab = KBDEnab; kbd_end = KBDEnab; R_W_23 = KBDEnab;
  //   lw_end = EnLect_1; mem_ready = ready_mem; R_W_19 = mfhi_end; R_W_20 = mflo_end; En_2 = _0_t; mul_end = _0_t;
  //   R__W_2 = _0_t; Sign_0 = _0_t; En_3 = _1_t; mulu_end = _1_t; R__W_3 = _1_t; nor_end = En_8; R__W_8 = En_8;
  //   tunnel = En_8; pop_end = EnLect_0; push_end = EnWrt_0; R__W = R_W; rnd_end = enRND; Sign_2 = R__W_14;
  //   slt_end = R__W_14; slti = slt_2; Sign_3 = R__W_16; slti_end = R__W_16; sltiu_end = R__W_17; sltu_end = R__W_15;
  //   En_1 = _0_t_t_t; R__W_1 = _0_t_t_t; sub_end = _0_t_t_t; sw_end = EnWrt_1; time_ready = ready_inst;
  //   tty_enab = TTYEnab; tty_end = TTYEnab; En_9 = _0_t_t_t_t_t; R__W_9 = _0_t_t_t_t_t; xor_end = _0_t_t_t_t_t;
  //   En_13 = _1_t_t_t_t_t; R__W_13 = _1_t_t_t_t_t; xori_end = _1_t_t_t_t_t
endmodule

module ALU (
  input  Clock,
  input  Sign,
  input  Reset,
  input  [31:0] Data_In1,
  input  [31:0] Data_In2,
  input  [2:0] ALU_Op_Code,
  output out_7,
  output out_8,
  output out_9,
  output out_10,
  output [31:0] Operation_Value,
  output [31:0] Hi_Value,
  output [31:0] Lo_Value
);

  wire adder_3_cout, and_4_out, and_5_out, C2, Enable, NotPairs, Odds, tunnel, u;
  wire [31:0] add, adder_2_out, \and , DI1C2, DI2C2, Div, div_t, end_Div, end_Mul_U, end_Up_Mul_U, LoMul_end,
       Mul, mul_t, multiplexer_3_out, multiplexer_4_out, multiplexer_5_out, multiplexer_6_out,
       multiplexer_7_out, multiplexer_8_out, multiplexer_11_out, multiplexer_12_out, Mulu_Hi, Mulu_Lo,
       negator_2_out, \nor , \or , Rem, sub, subtractor_1_out, Up_Mul, UpMul_end, \xor ;

  Multiplexer #(.select(3), .width(32), .enable("false")) multiplexer_1 (
    .in0(add), .in1(sub), .in2(\and ), .in3(\nor ), .in4(\or ), .in5(\xor ), .in6(mul_t), .in7(div_t),
    .out(Operation_Value), .sel(ALU_Op_Code));
  and and_1 (Odds, Data_In1[0], Data_In2[0]);
  or or_1 (NotPairs, Data_In1[0], Data_In2[0]);
  Subtractor #(.width(32)) subtractor_1 (.a(Data_In1), .b(32'h1), .out(subtractor_1_out));  // open: bin, bout
  Adder #(.width(32)) adder_1 (.a(Data_In1), .b(Data_In2), .out(add));  // open: cin, cout
  assign \and  = Data_In1 & Data_In2;  // AND_Gate and_2, 32 bits wide
  assign \xor  = Data_In1 ^ Data_In2;  // XOR_Gate xor_1, 32 bits wide
  Comparator #(.width(32)) comparator_1 (.a(Data_In1), .b(Data_In2), .eq(out_9), .lt(tunnel));  // open: gt
  Multiplexer multiplexer_2 (.in0(u), .in1(tunnel), .out(out_10), .sel(Sign));  // open: en
  Multiplexer #(.width(32)) multiplexer_3 (
    .in0(UpMul_end), .in1(Rem), .out(multiplexer_3_out), .sel(ALU_Op_Code[0]));  // open: en
  Register #(.width(32)) Hi (.D(multiplexer_3_out), .en(Enable), .Q(Hi_Value), .clk(Clock), .clr(Reset));
  Multiplexer #(.width(32)) multiplexer_4 (
    .in0(LoMul_end), .in1(end_Div), .out(multiplexer_4_out), .sel(ALU_Op_Code[0]));  // open: en
  Register #(.width(32)) Lo (.D(multiplexer_4_out), .en(Enable), .Q(Lo_Value), .clk(Clock), .clr(Reset));
  Multiplexer #(.width(32), .enable("false")) multiplexer_5 (
    .in0(Data_In1), .in1(Data_In2), .out(multiplexer_5_out), .sel(Data_In1[0]));
  Adder #(.width(32)) adder_2 (.a(subtractor_1_out), .b(Data_In2), .out(adder_2_out));  // open: cin, cout
  nor nor_1 (out_7, Operation_Value[0], Operation_Value[1], Operation_Value[2], Operation_Value[3], Operation_Value[4], Operation_Value[5], Operation_Value[6], Operation_Value[7], Operation_Value[8], Operation_Value[9], Operation_Value[10], Operation_Value[11], Operation_Value[12], Operation_Value[13], Operation_Value[14], Operation_Value[15], Operation_Value[16], Operation_Value[17], Operation_Value[18], Operation_Value[19], Operation_Value[20], Operation_Value[21], Operation_Value[22], Operation_Value[23], Operation_Value[24], Operation_Value[25], Operation_Value[26], Operation_Value[27], Operation_Value[28], Operation_Value[29], Operation_Value[30], Operation_Value[31]);
  Subtractor #(.width(32)) subtractor_2 (.a(Data_In1), .b(Data_In2), .out(sub));  // open: bin, bout
  assign \or  = Data_In1 | Data_In2;  // OR_Gate or_2, 32 bits wide
  assign \nor  = ~(Data_In1 | Data_In2);  // NOR_Gate nor_2, 32 bits wide
  Comparator #(.width(32), .mode("unsigned")) comparator_2 (.a(Data_In1), .b(Data_In2), .lt(u));  // open: gt, eq
  Multiplexer #(.width(32), .enable("false")) multiplexer_6 (
    .in0({1'b0, Data_In1[31:1]}), .in1(Data_In1), .out(multiplexer_6_out), .sel(Sign));
  Multiplexer #(.width(32), .enable("false")) multiplexer_7 (
    .in0({1'b0, Data_In2[31:1]}), .in1(Data_In2), .out(multiplexer_7_out), .sel(Sign));
  Multiplexer #(.width(32), .enable("false")) multiplexer_8 (
    .in0(multiplexer_5_out), .in1(adder_2_out), .out(multiplexer_8_out), .sel(Odds));
  Multiplier #(.width(32)) multiplier_1 (
    .a(multiplexer_6_out), .b(multiplexer_7_out), .out(Mul), .cout(Up_Mul));  // open: cin
  Adder #(.width(32)) adder_3 (
    .a(multiplexer_8_out), .b({Mul[29:0], 2'b00}), .out(end_Mul_U), .cout(adder_3_cout));  // open: cin
  Adder #(.width(32)) adder_4 (
    .a({Up_Mul[29:0], Mul[31:30]}), .b({32{1'b0}}), .out(end_Up_Mul_U), .cin(adder_3_cout));  // open: cout
  and and_3 (Enable, ALU_Op_Code[1], ALU_Op_Code[2]);
  Negator #(.width(32)) negator_1 (.in(Data_In1), .out(DI1C2));
  and and_4 (and_4_out, Data_In1[31], Sign);
  and and_5 (and_5_out, Sign, Data_In2[31]);
  Negator #(.width(32)) negator_2 (.in(Div), .out(negator_2_out));
  xor xor_2 (C2, Data_In1[31], Data_In2[31]);
  Multiplexer #(.width(32), .enable("false")) multiplexer_9 (
    .in0({Mul[29:0], 2'b00}), .in1(end_Mul_U), .out(Mulu_Lo), .sel(NotPairs));
  Multiplexer #(.width(32), .enable("false")) multiplexer_10 (
    .in0({Up_Mul[29:0], Mul[31:30]}), .in1(end_Up_Mul_U), .out(Mulu_Hi), .sel(NotPairs));
  Multiplexer #(.width(32), .enable("false")) multiplexer_11 (
    .in0(Data_In1), .in1(DI1C2), .out(multiplexer_11_out), .sel(and_4_out));
  Multiplexer #(.width(32), .enable("false")) multiplexer_12 (
    .in0(Data_In2), .in1(DI1C2), .out(multiplexer_12_out), .sel(and_5_out));
  Multiplexer #(.width(32), .enable("false")) multiplexer_13 (.in0(Div), .in1(negator_2_out), .out(end_Div), .sel(C2));
  Negator #(.width(32)) negator_3 (.in(Data_In2), .out(DI2C2));
  Divider #(.width(32)) divider_1 (
    .a(multiplexer_11_out), .b(multiplexer_12_out), .out(Div), .rem(Rem));  // open: upper
  Multiplexer #(.width(32), .enable("false")) multiplexer_14 (.in0(Mulu_Lo), .in1(Mul), .out(LoMul_end), .sel(Sign));
  Multiplexer #(.width(32), .enable("false")) multiplexer_15 (.in0(Mulu_Hi), .in1(Up_Mul), .out(UpMul_end), .sel(Sign));

  assign out_8 = Operation_Value[31];

  // Other names for the same wires on the sheet: A1[30:0] = Data_In1[31:1]; DI1[31:0] = Data_In1;
  //   SignD1 = Data_In1[31]; B1[30:0] = Data_In2[31:1]; DI2[31:0] = Data_In2; SignD2 = Data_In2[31]; CLK = Clock;
  //   _1A = Data_In1[0]; _1B = Data_In2[0]; end_slt = out_10; Hi[31:0] = Hi_Value; Lo[31:0] = Lo_Value;
  //   Up_Mul_U[31:0] = {Up_Mul[29:0], Mul[31:30]}; Mul_U[31:2] = Mul[29:0]; Div_Mult = ALU_Op_Code[0];
  //   OpCod[2:0] = ALU_Op_Code; OpVal[31:0] = Operation_Value; Sign_Bit = Operation_Value[31]; RST = Reset;
  //   tunnel_t = out_9; ZF = out_7

  // Notes on the sheet:
  //   Multiplicar
endmodule

module random (
  input  Clock,
  input  Enable,
  output [31:0] Output
);

  Random #(.width(32)) Random (.clk(Clock), .next(Enable), .out(Output));  // open: clr

  // Other names for the same wires on the sheet: CLK = Clock
endmodule

module ReadMemory (
  input  [31:0] Dir,
  input  in_2,
  input  in_3,
  input  in_4,
  input  [31:0] RAM_In1,
  input  [31:0] RAM_In2,
  input  [31:0] RAM_In3,
  input  [31:0] RAM_In4,
  output [31:0] RAM_Out,
  output Finish
);

  wire [31:0] Out;

  Multiplexer #(.select(2), .width(32)) multiplexer_1 (
    .in0(RAM_In1), .in1(RAM_In2), .in2(RAM_In3), .in3(RAM_In4),
    .out({Out[7:0], Out[15:8], Out[23:16], Out[31:24]}), .sel(Dir[3:2]));  // open: en
  Register #(.width(32)) register_1 (.D(Out), .en(in_3), .Q(RAM_Out), .clk(in_2), .clr(in_4));
  D_Flip_Flop d_ff_1 (.clk(in_2), .D(in_3), .Q(Finish));  // open: Qn, preset, en, reset

  // Other names for the same wires on the sheet: CLK = in_2; Bank[1:0] = Dir[3:2]; Address[15:0] = Dir[19:4];
  //   Ready = in_3; Reset = in_4
endmodule

module WriteMemory (
  input  [31:0] in_1,
  input  in_2,
  input  in_3,
  input  in_4,
  input  [3:0] Write_Time,
  input  [31:0] Dir,
  output [31:0] RAM_Input_1,
  output [3:0] out_8,
  output [31:0] RAM_Input_2,
  output [15:0] out_10,
  output [31:0] RAM_Input_3,
  output [31:0] RAM_Input_4,
  output CS,
  output Finish
);

  wire [31:0] WD_q;

  Decoder #(.select(2), .enable("false")) decoder_1 (
    .out0(out_8[0]), .out1(out_8[1]), .out2(out_8[2]), .out3(out_8[3]), .sel(Dir[3:2]));
  Demultiplexer #(.select(2), .width(32)) demultiplexer_1 (
    .out0(RAM_Input_1), .out1(RAM_Input_2), .out2(RAM_Input_3), .out3(RAM_Input_4), .in(WD_q), .sel(Dir[3:2]));  // open: en
  Register #(.width(32)) WD (
    .D({in_1[7:0], in_1[15:8], in_1[23:16], in_1[31:24]}), .en(in_3), .Q(WD_q), .clk(in_2));  // open: clr
  WaitCircuit waitcircuit_1 (.Wait_Time(Write_Time), .Start(in_3), .Clear(in_4), .Clock(in_2), .Ready(Finish), .CS(CS));

  assign out_10 = Dir[19:4];

  // Other names for the same wires on the sheet: Value[31:0] = in_1; CLK = in_2; Bank[1:0] = Dir[3:2];
  //   Address[15:0] = Dir[19:4]; Enable = in_3; Mask[3:0] = out_8; Reset = in_4; WT[3:0] = Write_Time
endmodule

module WaitCircuit (
  input  [3:0] Wait_Time,
  input  Start,
  input  Clear,
  input  Clock,
  output Ready,
  output CS
);

  wire Count__0, CS1, d_ff_1_q, Load;
  wire [3:0] counter_1_q, multiplexer_1_out;

  or or_1 (CS, CS1, Ready);
  Multiplexer #(.width(4), .enable("false")) multiplexer_1 (
    .in0(4'b0001), .in1(Wait_Time), .out(multiplexer_1_out), .sel(Start));
  or or_2 (Load, CS1, Start);
  Demultiplexer #(.enable("false")) demultiplexer_1 (.out0(CS1), .out1(Ready), .in(d_ff_1_q), .sel(Count__0));
  D_Flip_Flop d_ff_1 (.clk(Clock), .D(Load), .Q(d_ff_1_q));  // open: Qn, preset, en, reset
  Counter #(.width(4), .max('hf)) counter_1 (
    .load(Load), .D(multiplexer_1_out), .count(CS1), .Q(counter_1_q), .clk(Clock));  // open: carry, clr
  Comparator #(.width(4)) comparator_1 (.a(counter_1_q), .b(4'b0000), .eq(Count__0));  // open: gt, lt

  // Other names for the same wires on the sheet: CLK = Clock; CLR = Clear; CS2 = Ready; Dec = CS1;
  //   WT[3:0] = Wait_Time
endmodule

module InstFetcher (
  input  [31:0] Dir,
  input  in_2,
  input  in_3,
  input  Ready,
  input  [31:0] RAM_In1,
  input  [31:0] RAM_In2,
  input  [31:0] RAM_In3,
  input  [31:0] RAM_In4,
  output Finish,
  output [31:0] Instruction
);

  wire [31:0] Out;

  Multiplexer #(.select(2), .width(32)) multiplexer_1 (
    .in0(RAM_In1), .in1(RAM_In2), .in2(RAM_In3), .in3(RAM_In4),
    .out({Out[7:0], Out[15:8], Out[23:16], Out[31:24]}), .sel(Dir[3:2]));  // open: en
  Register #(.width(32)) register_1 (.D(Out), .en(Ready), .Q(Instruction), .clk(in_2), .clr(in_3));
  D_Flip_Flop d_ff_1 (.clk(in_2), .D(Ready), .Q(Finish));  // open: Qn, preset, en, reset

  // Other names for the same wires on the sheet: CLK = in_2; Bank[1:0] = Dir[3:2]; Address[15:0] = Dir[19:4];
  //   Reset = in_3
endmodule

module multiplexer_3x8 (
  input  [31:0] in_1,
  input  [31:0] in_2,
  input  [31:0] in_3,
  input  [31:0] in_4,
  input  [31:0] in_5,
  input  [31:0] in_6,
  input  [31:0] in_7,
  input  [2:0] in_8,
  input  [31:0] in_9,
  output [31:0] out_10
);

  wire a0, a1, a2, a3, a4, a5, a6, a7;

  assign out_10 = a0 ? in_1 : 32'bz;  // Controlled_Buffer controlled_buffer_1
  assign out_10 = a1 ? in_2 : 32'bz;  // Controlled_Buffer controlled_buffer_2
  assign out_10 = a2 ? in_3 : 32'bz;  // Controlled_Buffer controlled_buffer_3
  assign out_10 = a3 ? in_4 : 32'bz;  // Controlled_Buffer controlled_buffer_4
  assign out_10 = a4 ? in_5 : 32'bz;  // Controlled_Buffer controlled_buffer_5
  assign out_10 = a5 ? in_6 : 32'bz;  // Controlled_Buffer controlled_buffer_6
  assign out_10 = a6 ? in_7 : 32'bz;  // Controlled_Buffer controlled_buffer_7
  assign out_10 = a7 ? in_9 : 32'bz;  // Controlled_Buffer controlled_buffer_8
  Decoder #(.select(3)) decoder_1 (
    .out0(a0), .out1(a1), .out2(a2), .out3(a3), .out4(a4), .out5(a5), .out6(a6), .out7(a7), .sel(in_8));  // open: en

  // Other names for the same wires on the sheet: out[31:0] = out_10
endmodule

module CacheInst (
  input  [31:0] Address,
  input  in_2,
  input  in_3,
  input  in_4,
  input  [31:0] RAM_Out_0,
  input  [31:0] RAM_Out_1,
  input  [31:0] RAM_Out_2,
  input  [31:0] RAM_Out_3,
  input  [3:0] ReadTime,
  output CS,
  output Finish,
  output [31:0] CacheOut0,
  output [31:0] CacheOut1,
  output [31:0] CacheOut2,
  output [31:0] CacheOut3,
  output [15:0] AddressOut
);

  wire and_2_out, controlled_buffer_1_out, controlled_buffer_2_out, controlled_buffer_3_out,
       controlled_buffer_4_out, controlled_buffer_5_out, controlled_buffer_6_out, controlled_buffer_7_out,
       controlled_buffer_8_out, decoder_1_out0, decoder_1_out1, decoder_1_out2, decoder_1_out3,
       decoder_1_out4, decoder_1_out5, decoder_1_out6, decoder_1_out7, demultiplexer_1_out0,
       demultiplexer_2_out0, demultiplexer_2_out1, Finish_t, hit, miss, not_2_out, not_3_out, not_4_out,
       not_5_out, not_6_out, not_7_out, not_8_out, not_9_out, or_1_out, Ready, start, start_q, v0, v1, v2,
       v3, v4, v5, v6, v7, Val, wait_q;
  wire [12:0] tagOut, xnor_1_out;

  RAM_part #(.addrWidth(3), .dataWidth(32), .bus("separate")) ram_1 (
    .addr(Address[6:4]), .din(RAM_Out_0), .data(CacheOut0), .str(Finish_t), .clk(in_4), .ld(1'b1), .clr(in_3));  // open: sel
  RAM_part #(.addrWidth(3), .dataWidth(32), .bus("separate")) ram_2 (
    .addr(Address[6:4]), .din(RAM_Out_1), .data(CacheOut1), .str(Finish_t), .clk(in_4), .ld(1'b1), .clr(in_3));  // open: sel
  RAM_part #(.addrWidth(3), .dataWidth(32), .bus("separate")) ram_3 (
    .addr(Address[6:4]), .din(RAM_Out_2), .data(CacheOut2), .str(Finish_t), .clk(in_4), .ld(1'b1), .clr(in_3));  // open: sel
  RAM_part #(.addrWidth(3), .dataWidth(32), .bus("separate")) ram_4 (
    .addr(Address[6:4]), .din(RAM_Out_3), .data(CacheOut3), .str(Finish_t), .clk(in_4), .ld(1'b1), .clr(in_3));  // open: sel
  RAM_part #(.addrWidth(3), .dataWidth(13), .bus("separate")) ram_5 (
    .addr(Address[6:4]), .din(Address[19:7]), .data(tagOut), .str(Finish_t), .clk(in_4), .ld(1'b1), .clr(in_3));  // open: sel
  Multiplexer #(.select(3)) multiplexer_1 (
    .in0(v0), .in1(v1), .in2(v2), .in3(v3), .in4(v4), .in5(v5), .in6(v6), .in7(v7), .out(Val),
    .sel(Address[6:4]));  // open: en
  assign xnor_1_out = ~(tagOut ^ Address[19:7]);  // XNOR_Gate xnor_1, 13 bits wide
  and and_1 (hit, Val, and_2_out);
  D_Flip_Flop u_start (.clk(in_4), .D(in_2), .Q(start_q));  // open: Qn, preset, en, reset
  Demultiplexer #(.enable("false")) demultiplexer_1 (
    .out0(demultiplexer_1_out0), .out1(start), .in(start_q), .sel(miss));
  and and_2 (and_2_out, xnor_1_out[12], xnor_1_out[11], xnor_1_out[10], xnor_1_out[9], xnor_1_out[8], xnor_1_out[7], xnor_1_out[6], xnor_1_out[5], xnor_1_out[4], xnor_1_out[3], xnor_1_out[2], xnor_1_out[1], xnor_1_out[0]);
  not not_1 (miss, hit);
  WaitCircuit waitcircuit_1 (
    .Wait_Time(ReadTime), .Start(start), .Clear(in_3), .Clock(in_4), .Ready(Finish_t), .CS(CS));
  or or_1 (or_1_out, demultiplexer_2_out0, start);
  D_Flip_Flop \wait  (.clk(in_4), .D(or_1_out), .Q(wait_q));  // open: Qn, preset, en, reset
  Decoder #(.select(3)) decoder_1 (
    .out0(decoder_1_out0), .out1(decoder_1_out1), .out2(decoder_1_out2), .out3(decoder_1_out3),
    .out4(decoder_1_out4), .out5(decoder_1_out5), .out6(decoder_1_out6), .out7(decoder_1_out7),
    .sel(Address[6:4]));  // open: en
  Demultiplexer #(.enable("false")) demultiplexer_2 (
    .out0(demultiplexer_2_out0), .out1(demultiplexer_2_out1), .in(wait_q), .sel(Finish_t));
  D_Flip_Flop d_ff_1 (.clk(in_4), .D(Ready), .Q(Finish));  // open: Qn, preset, en, reset
  or or_2 (Ready, demultiplexer_1_out0, demultiplexer_2_out1);
  not not_2 (not_2_out, v0);
  assign controlled_buffer_1_out = not_2_out ? decoder_1_out0 : 1'bz;  // Controlled_Buffer controlled_buffer_1
  not not_3 (not_3_out, v1);
  assign controlled_buffer_2_out = not_3_out ? decoder_1_out1 : 1'bz;  // Controlled_Buffer controlled_buffer_2
  not not_4 (not_4_out, v2);
  assign controlled_buffer_3_out = not_4_out ? decoder_1_out2 : 1'bz;  // Controlled_Buffer controlled_buffer_3
  not not_5 (not_5_out, v3);
  assign controlled_buffer_4_out = not_5_out ? decoder_1_out3 : 1'bz;  // Controlled_Buffer controlled_buffer_4
  not not_6 (not_6_out, v4);
  assign controlled_buffer_5_out = not_6_out ? decoder_1_out4 : 1'bz;  // Controlled_Buffer controlled_buffer_5
  not not_7 (not_7_out, v5);
  assign controlled_buffer_6_out = not_7_out ? decoder_1_out5 : 1'bz;  // Controlled_Buffer controlled_buffer_6
  not not_8 (not_8_out, v6);
  assign controlled_buffer_7_out = not_8_out ? decoder_1_out6 : 1'bz;  // Controlled_Buffer controlled_buffer_7
  not not_9 (not_9_out, v7);
  assign controlled_buffer_8_out = not_9_out ? decoder_1_out7 : 1'bz;  // Controlled_Buffer controlled_buffer_8
  D_Flip_Flop d_ff_2 (.clk(in_4), .D(controlled_buffer_1_out), .Q(v0), .reset(in_3));  // open: Qn, preset, en
  D_Flip_Flop d_ff_3 (.clk(in_4), .D(controlled_buffer_2_out), .Q(v1), .reset(in_3));  // open: Qn, preset, en
  D_Flip_Flop d_ff_4 (.clk(in_4), .D(controlled_buffer_3_out), .Q(v2), .reset(in_3));  // open: Qn, preset, en
  D_Flip_Flop d_ff_5 (.clk(in_4), .D(controlled_buffer_4_out), .Q(v3), .reset(in_3));  // open: Qn, preset, en
  D_Flip_Flop d_ff_6 (.clk(in_4), .D(controlled_buffer_5_out), .Q(v4), .reset(in_3));  // open: Qn, preset, en
  D_Flip_Flop d_ff_7 (.clk(in_4), .D(controlled_buffer_6_out), .Q(v5), .reset(in_3));  // open: Qn, preset, en
  D_Flip_Flop d_ff_8 (.clk(in_4), .D(controlled_buffer_7_out), .Q(v6), .reset(in_3));  // open: Qn, preset, en
  D_Flip_Flop d_ff_9 (.clk(in_4), .D(controlled_buffer_8_out), .Q(v7), .reset(in_3));  // open: Qn, preset, en

  assign AddressOut = Address[19:4];

  // Other names for the same wires on the sheet: offset[1:0] = Address[3:2]; Address_t[15:0] = Address[19:4];
  //   idx[2:0] = Address[6:4]; tag[12:0] = Address[19:7]; Clear = in_3; CLK = in_4; Enable = in_2;
  //   RAM_OUTPUT_0[31:0] = RAM_Out_0; RAM_OUTPUT_1[31:0] = RAM_Out_1; RAM_OUTPUT_2[31:0] = RAM_Out_2;
  //   RAM_OUTPUT_3[31:0] = RAM_Out_3; Read_Time[3:0] = ReadTime

  // Notes on the sheet:
  //   DATA FROM RAM
  //   RAM TIMING
  //   Bank 0
  //   Bank 1
  //   Bank 2
  //   Bank 3
  //   Tag
endmodule

module CacheData (
  input  [31:0] Address,
  input  in_2,
  input  in_3,
  input  in_4,
  input  in_5,
  input  [31:0] RAM_Out_0,
  input  [31:0] RAM_Out_1,
  input  [31:0] RAM_Out_2,
  input  [31:0] RAM_Out_3,
  input  [31:0] Value,
  input  [3:0] ReadTime,
  input  [3:0] WriteTime,
  output CS,
  output [15:0] AddressOut,
  output FinishRead,
  output RAM_R_W,
  output FinishWrt,
  output [3:0] Mask,
  output [31:0] CacheOut0,
  output [31:0] CacheOut1,
  output [31:0] CacheOut2,
  output [31:0] CacheOut3
);

  wire and_1_out, and_2_out, and_3_out, and_5_out, and_7_out, and_9_out, and_16_out, and_18_out, and_20_out,
       and_22_out, btag, btag_0, btag_1, controlled_buffer_1_out, controlled_buffer_2_out,
       controlled_buffer_3_out, controlled_buffer_4_out, controlled_buffer_5_out, controlled_buffer_6_out,
       controlled_buffer_7_out, controlled_buffer_8_out, d, d0, d1, d2, d3, d4, d5, d6, d7, d_ff_1_q,
       decoder_1_out0, decoder_1_out1, decoder_1_out2, decoder_1_out3, decoder_2_out0, decoder_2_out1,
       decoder_2_out2, decoder_2_out3, decoder_2_out4, decoder_2_out5, decoder_2_out6, decoder_2_out7,
       decoder_3_out0, decoder_3_out1, decoder_3_out2, decoder_3_out3, decoder_3_out4, decoder_3_out5,
       decoder_3_out6, decoder_3_out7, decoder_4_out0, decoder_4_out1, decoder_4_out2, decoder_4_out3,
       decoder_4_out4, decoder_4_out5, decoder_4_out6, decoder_4_out7, demultiplexer_1_out0,
       demultiplexer_1_out1, demultiplexer_2_out0, demultiplexer_2_out1, demultiplexer_3_out0,
       demultiplexer_3_out1, demultiplexer_4_out0, demultiplexer_4_out1, demultiplexer_5_out0,
       demultiplexer_6_out0, demultiplexer_7_out0, demultiplexer_8_out0, demultiplexer_9_out1,
       demultiplexer_10_out0, dirty, empty, en0, en1, en2, en3, en4, en5, en6, en7, enDirty0, enDirty1,
       enDirty2, enDirty3, enDirty4, enDirty5, enDirty6, enDirty7, enRnd, enRnd_0, enRnd_1, enV, enV_0,
       Finish, Finish_1, Finish_3, full, hit, hit0, hit1, hit2, hit3, hit4, hit5, hit6, hit7, LdDirty,
       LdDirty_0, miss, not_3_out, not_4_out, not_5_out, not_6_out, not_7_out, not_8_out, not_9_out,
       not_10_out, or_8_out, or_9_out, or_10_out, or_11_out, or_12_out, or_17_out, or_18_out, R, R_0, R_1,
       read_2_q, read_q, Ready, start, str0, str1, str2, str3, v0, v1, v2, v3, v4, v5, v6, v7, wrt_2_q;
  wire [2:0] adder_1_out, idx, idx0, idx1, idxHit, multiplexer_8_out, priority_encoder_1_out;
  wire [3:0] multiplexer_10_out;
  wire [15:0] tag0, tag1, tag2, tag3, tag4, tag5, tag6, tag7, tagAddr, xnor_1_out, xnor_2_out, xnor_3_out,
       xnor_4_out, xnor_5_out, xnor_6_out, xnor_7_out, xnor_8_out;
  wire [31:0] multiplexer_2_out, multiplexer_3_out, multiplexer_4_out, multiplexer_5_out;

  Register #(.width(16)) register_1 (.D(Address[19:4]), .en(en0), .Q(tag0), .clk(in_4), .clr(in_3));
  Register #(.width(16)) register_2 (.D(Address[19:4]), .en(en1), .Q(tag1), .clk(in_4), .clr(in_3));
  Register #(.width(16)) register_3 (.D(Address[19:4]), .en(en2), .Q(tag2), .clk(in_4), .clr(in_3));
  Register #(.width(16)) register_4 (.D(Address[19:4]), .en(en3), .Q(tag3), .clk(in_4), .clr(in_3));
  Multiplexer #(.width(16)) multiplexer_1 (
    .in0(Address[19:4]), .in1(tagAddr), .out(AddressOut), .sel(btag));  // open: en
  or or_1 (RAM_R_W, btag_0, btag_1);
  Register #(.width(16)) register_5 (.D(Address[19:4]), .en(en4), .Q(tag4), .clk(in_4), .clr(in_3));
  Register #(.width(16)) register_6 (.D(Address[19:4]), .en(en5), .Q(tag5), .clk(in_4), .clr(in_3));
  Register #(.width(16)) register_7 (.D(Address[19:4]), .en(en6), .Q(tag6), .clk(in_4), .clr(in_3));
  Register #(.width(16)) register_8 (.D(Address[19:4]), .en(en7), .Q(tag7), .clk(in_4), .clr(in_3));
  Multiplexer #(.width(32)) multiplexer_2 (
    .in0(RAM_Out_0), .in1({Value[7:0], Value[15:8], Value[23:16], Value[31:24]}), .out(multiplexer_2_out),
    .sel(dirty));  // open: en
  Multiplexer #(.width(32)) multiplexer_3 (
    .in0(RAM_Out_1), .in1({Value[7:0], Value[15:8], Value[23:16], Value[31:24]}), .out(multiplexer_3_out),
    .sel(dirty));  // open: en
  Multiplexer #(.width(32)) multiplexer_4 (
    .in0(RAM_Out_2), .in1({Value[7:0], Value[15:8], Value[23:16], Value[31:24]}), .out(multiplexer_4_out),
    .sel(dirty));  // open: en
  Multiplexer #(.width(32)) multiplexer_5 (
    .in0(RAM_Out_3), .in1({Value[7:0], Value[15:8], Value[23:16], Value[31:24]}), .out(multiplexer_5_out),
    .sel(dirty));  // open: en
  or or_2 (btag, btag_0, btag_1);
  or or_3 (start, R_0, enRnd_1, R_1, enRnd_0);
  or or_4 (LdDirty, LdDirty_0, dirty);
  or or_5 (R, R_0, R_1);
  or or_6 (enV, enV_0, dirty);
  or or_7 (enRnd, enRnd_0, enRnd_1);
  or or_8 (or_8_out, Finish, str0);
  or or_9 (or_9_out, Finish, str1);
  or or_10 (or_10_out, Finish, str2);
  or or_11 (or_11_out, Finish, str3);
  Multiplexer #(.select(3)) multiplexer_6 (
    .in0(d0), .in1(d1), .in2(d2), .in3(d3), .in4(d4), .in5(d5), .in6(d6), .in7(d7), .out(d), .sel(idx));  // open: en
  RAM_part #(.addrWidth(3), .dataWidth(32), .bus("separate")) ram_1 (
    .addr(idx), .din(multiplexer_2_out), .data(CacheOut0), .str(or_8_out), .clk(in_4), .ld(1'b1), .clr(in_3));  // open: sel
  RAM_part #(.addrWidth(3), .dataWidth(32), .bus("separate")) ram_2 (
    .addr(idx), .din(multiplexer_3_out), .data(CacheOut1), .str(or_9_out), .clk(in_4), .ld(1'b1), .clr(in_3));  // open: sel
  RAM_part #(.addrWidth(3), .dataWidth(32), .bus("separate")) ram_3 (
    .addr(idx), .din(multiplexer_4_out), .data(CacheOut2), .str(or_10_out), .clk(in_4), .ld(1'b1), .clr(in_3));  // open: sel
  RAM_part #(.addrWidth(3), .dataWidth(32), .bus("separate")) ram_4 (
    .addr(idx), .din(multiplexer_5_out), .data(CacheOut3), .str(or_11_out), .clk(in_4), .ld(1'b1), .clr(in_3));  // open: sel
  and and_1 (and_1_out, ~in_5, in_2);  // AND_Gate
  assign xnor_1_out = ~(tag0 ^ Address[19:4]);  // XNOR_Gate xnor_1, 16 bits wide
  assign xnor_2_out = ~(tag2 ^ Address[19:4]);  // XNOR_Gate xnor_2, 16 bits wide
  assign xnor_3_out = ~(tag4 ^ Address[19:4]);  // XNOR_Gate xnor_3, 16 bits wide
  assign xnor_4_out = ~(tag6 ^ Address[19:4]);  // XNOR_Gate xnor_4, 16 bits wide
  Demultiplexer #(.enable("false")) demultiplexer_1 (
    .out0(demultiplexer_1_out0), .out1(demultiplexer_1_out1), .in(and_1_out), .sel(miss));
  Demultiplexer #(.enable("false")) demultiplexer_2 (
    .out0(demultiplexer_2_out0), .out1(demultiplexer_2_out1), .in(and_2_out), .sel(miss));
  and and_2 (and_2_out, in_5, in_2);
  and and_3 (and_3_out, xnor_1_out[15], xnor_1_out[14], xnor_1_out[13], xnor_1_out[12], xnor_1_out[11], xnor_1_out[10], xnor_1_out[9], xnor_1_out[8], xnor_1_out[7], xnor_1_out[6], xnor_1_out[5], xnor_1_out[4], xnor_1_out[3], xnor_1_out[2], xnor_1_out[1], xnor_1_out[0]);
  and and_4 (hit0, v0, and_3_out);
  and and_5 (and_5_out, xnor_2_out[15], xnor_2_out[14], xnor_2_out[13], xnor_2_out[12], xnor_2_out[11], xnor_2_out[10], xnor_2_out[9], xnor_2_out[8], xnor_2_out[7], xnor_2_out[6], xnor_2_out[5], xnor_2_out[4], xnor_2_out[3], xnor_2_out[2], xnor_2_out[1], xnor_2_out[0]);
  and and_6 (hit2, v2, and_5_out);
  and and_7 (and_7_out, xnor_3_out[15], xnor_3_out[14], xnor_3_out[13], xnor_3_out[12], xnor_3_out[11], xnor_3_out[10], xnor_3_out[9], xnor_3_out[8], xnor_3_out[7], xnor_3_out[6], xnor_3_out[5], xnor_3_out[4], xnor_3_out[3], xnor_3_out[2], xnor_3_out[1], xnor_3_out[0]);
  and and_8 (hit4, v4, and_7_out);
  and and_9 (and_9_out, xnor_4_out[15], xnor_4_out[14], xnor_4_out[13], xnor_4_out[12], xnor_4_out[11], xnor_4_out[10], xnor_4_out[9], xnor_4_out[8], xnor_4_out[7], xnor_4_out[6], xnor_4_out[5], xnor_4_out[4], xnor_4_out[3], xnor_4_out[2], xnor_4_out[1], xnor_4_out[0]);
  and and_10 (hit6, v6, and_9_out);
  Demultiplexer #(.enable("false")) demultiplexer_3 (
    .out0(demultiplexer_3_out0), .out1(demultiplexer_3_out1), .in(demultiplexer_1_out1), .sel(full));
  or or_12 (or_12_out, v0, v1, v2, v3, v4, v5, v6, v7);
  Priority_Encoder priority_encoder_1 (
    .in0(v0), .in1(v1), .in2(v2), .in3(v3), .in4(v4), .in5(v5), .in6(v6), .in7(v7),
    .out(priority_encoder_1_out), .en_in(1'b1));  // open: gs, en_out
  Priority_Encoder priority_encoder_2 (
    .in0(hit0), .in1(hit1), .in2(hit2), .in3(hit3), .in4(hit4), .in5(hit5), .in6(hit6), .in7(hit7),
    .out(idxHit), .en_in(1'b1));  // open: gs, en_out
  or or_13 (R_0, demultiplexer_5_out0, demultiplexer_7_out0, demultiplexer_3_out0, LdDirty_0);
  Demultiplexer #(.enable("false")) demultiplexer_4 (
    .out0(demultiplexer_4_out0), .out1(demultiplexer_4_out1), .in(demultiplexer_2_out1), .sel(full));
  and and_11 (full, v0, v1, v2, v3, v4, v5, v6, v7);
  not not_1 (empty, or_12_out);
  or or_14 (hit, hit0, hit1, hit2, hit3, hit4, hit5, hit6, hit7);
  not not_2 (miss, hit);
  Adder #(.width(3)) adder_1 (.a(priority_encoder_1_out), .b(3'b001), .out(adder_1_out));  // open: cin, cout
  D_Flip_Flop read (.clk(in_4), .D(R_0), .Q(read_q), .reset(in_3));  // open: Qn, preset, en
  Demultiplexer #(.enable("false")) demultiplexer_5 (
    .out0(demultiplexer_5_out0), .out1(Finish_3), .in(read_q), .sel(Ready));
  Demultiplexer #(.enable("false")) demultiplexer_6 (
    .out0(demultiplexer_6_out0), .out1(enRnd_0), .in(demultiplexer_4_out1), .sel(d));
  Decoder #(.select(2)) decoder_1 (
    .out0(decoder_1_out0), .out1(decoder_1_out1), .out2(decoder_1_out2), .out3(decoder_1_out3),
    .sel(Address[3:2]));  // open: en
  Multiplexer #(.width(3)) multiplexer_7 (.in0(adder_1_out), .in1(3'b000), .out(idx0), .sel(empty));  // open: en
  assign xnor_5_out = ~(tag3 ^ Address[19:4]);  // XNOR_Gate xnor_5, 16 bits wide
  assign xnor_6_out = ~(tag7 ^ Address[19:4]);  // XNOR_Gate xnor_6, 16 bits wide
  Demultiplexer #(.enable("false")) demultiplexer_7 (
    .out0(demultiplexer_7_out0), .out1(enRnd_1), .in(demultiplexer_3_out1), .sel(d));
  or or_15 (R_1, demultiplexer_8_out0, demultiplexer_4_out0, demultiplexer_6_out0, demultiplexer_9_out1);
  Random #(.width(3)) random_1 (.clk(in_4), .next(enRnd), .out(idx1));  // open: clr
  Multiplexer #(.width(3)) multiplexer_8 (.in0(idx0), .in1(idx1), .out(multiplexer_8_out), .sel(full));  // open: en
  assign xnor_7_out = ~(tag1 ^ Address[19:4]);  // XNOR_Gate xnor_7, 16 bits wide
  assign xnor_8_out = ~(tag5 ^ Address[19:4]);  // XNOR_Gate xnor_8, 16 bits wide
  or or_16 (enV_0, demultiplexer_1_out0, Finish_3);
  or or_17 (or_17_out, demultiplexer_10_out0, enRnd_1);
  D_Flip_Flop read_2 (.clk(in_4), .D(R_1), .Q(read_2_q), .reset(in_3));  // open: Qn, preset, en
  or or_18 (or_18_out, btag_1, enRnd_0);
  and and_12 (str0, decoder_1_out0, dirty);
  and and_13 (str1, decoder_1_out1, dirty);
  and and_14 (str2, dirty, decoder_1_out2);
  and and_15 (str3, dirty, decoder_1_out3);
  Multiplexer #(.width(3)) multiplexer_9 (.in0(multiplexer_8_out), .in1(idxHit), .out(idx), .sel(hit));  // open: en
  and and_16 (and_16_out, xnor_7_out[15], xnor_7_out[14], xnor_7_out[13], xnor_7_out[12], xnor_7_out[11], xnor_7_out[10], xnor_7_out[9], xnor_7_out[8], xnor_7_out[7], xnor_7_out[6], xnor_7_out[5], xnor_7_out[4], xnor_7_out[3], xnor_7_out[2], xnor_7_out[1], xnor_7_out[0]);
  and and_17 (hit1, v1, and_16_out);
  and and_18 (and_18_out, xnor_5_out[15], xnor_5_out[14], xnor_5_out[13], xnor_5_out[12], xnor_5_out[11], xnor_5_out[10], xnor_5_out[9], xnor_5_out[8], xnor_5_out[7], xnor_5_out[6], xnor_5_out[5], xnor_5_out[4], xnor_5_out[3], xnor_5_out[2], xnor_5_out[1], xnor_5_out[0]);
  and and_19 (hit3, v3, and_18_out);
  and and_20 (and_20_out, xnor_8_out[15], xnor_8_out[14], xnor_8_out[13], xnor_8_out[12], xnor_8_out[11], xnor_8_out[10], xnor_8_out[9], xnor_8_out[8], xnor_8_out[7], xnor_8_out[6], xnor_8_out[5], xnor_8_out[4], xnor_8_out[3], xnor_8_out[2], xnor_8_out[1], xnor_8_out[0]);
  and and_21 (hit5, v5, and_20_out);
  and and_22 (and_22_out, xnor_6_out[15], xnor_6_out[14], xnor_6_out[13], xnor_6_out[12], xnor_6_out[11], xnor_6_out[10], xnor_6_out[9], xnor_6_out[8], xnor_6_out[7], xnor_6_out[6], xnor_6_out[5], xnor_6_out[4], xnor_6_out[3], xnor_6_out[2], xnor_6_out[1], xnor_6_out[0]);
  and and_23 (hit7, v7, and_22_out);
  D_Flip_Flop wrt (.clk(in_4), .D(or_17_out), .Q(btag_0), .reset(in_3));  // open: Qn, preset, en
  Demultiplexer #(.enable("false")) demultiplexer_8 (
    .out0(demultiplexer_8_out0), .out1(Finish_1), .in(read_2_q), .sel(Ready));
  Demultiplexer #(.enable("false")) demultiplexer_9 (
    .out0(btag_1), .out1(demultiplexer_9_out1), .in(wrt_2_q), .sel(Ready));
  D_Flip_Flop wrt_2 (.clk(in_4), .D(or_18_out), .Q(wrt_2_q), .reset(in_3));  // open: Qn, preset, en
  Decoder #(.select(3)) decoder_2 (
    .out0(decoder_2_out0), .out1(decoder_2_out1), .out2(decoder_2_out2), .out3(decoder_2_out3),
    .out4(decoder_2_out4), .out5(decoder_2_out5), .out6(decoder_2_out6), .out7(decoder_2_out7), .sel(idx),
    .en(enV));
  Demultiplexer #(.enable("false")) demultiplexer_10 (
    .out0(demultiplexer_10_out0), .out1(LdDirty_0), .in(btag_0), .sel(Ready));
  not not_3 (not_3_out, v0);
  assign controlled_buffer_1_out = not_3_out ? decoder_2_out0 : 1'bz;  // Controlled_Buffer controlled_buffer_1
  not not_4 (not_4_out, v1);
  assign controlled_buffer_2_out = not_4_out ? decoder_2_out1 : 1'bz;  // Controlled_Buffer controlled_buffer_2
  not not_5 (not_5_out, v2);
  assign controlled_buffer_3_out = not_5_out ? decoder_2_out2 : 1'bz;  // Controlled_Buffer controlled_buffer_3
  not not_6 (not_6_out, v3);
  assign controlled_buffer_4_out = not_6_out ? decoder_2_out3 : 1'bz;  // Controlled_Buffer controlled_buffer_4
  not not_7 (not_7_out, v4);
  assign controlled_buffer_5_out = not_7_out ? decoder_2_out4 : 1'bz;  // Controlled_Buffer controlled_buffer_5
  not not_8 (not_8_out, v5);
  assign controlled_buffer_6_out = not_8_out ? decoder_2_out5 : 1'bz;  // Controlled_Buffer controlled_buffer_6
  not not_9 (not_9_out, v6);
  assign controlled_buffer_7_out = not_9_out ? decoder_2_out6 : 1'bz;  // Controlled_Buffer controlled_buffer_7
  not not_10 (not_10_out, v7);
  assign controlled_buffer_8_out = not_10_out ? decoder_2_out7 : 1'bz;  // Controlled_Buffer controlled_buffer_8
  Decoder #(.select(3)) decoder_3 (
    .out0(decoder_3_out0), .out1(decoder_3_out1), .out2(decoder_3_out2), .out3(decoder_3_out3),
    .out4(decoder_3_out4), .out5(decoder_3_out5), .out6(decoder_3_out6), .out7(decoder_3_out7), .sel(idx));  // open: en
  D_Flip_Flop d_ff_1 (.clk(in_4), .D(Finish_1), .Q(d_ff_1_q), .reset(in_3));  // open: Qn, preset, en
  D_Flip_Flop d_ff_2 (.clk(in_4), .D(controlled_buffer_1_out), .Q(v0), .reset(in_3));  // open: Qn, preset, en
  D_Flip_Flop d_ff_3 (.clk(in_4), .D(controlled_buffer_2_out), .Q(v1), .reset(in_3));  // open: Qn, preset, en
  D_Flip_Flop d_ff_4 (.clk(in_4), .D(controlled_buffer_3_out), .Q(v2), .reset(in_3));  // open: Qn, preset, en
  D_Flip_Flop d_ff_5 (.clk(in_4), .D(controlled_buffer_4_out), .Q(v3), .reset(in_3));  // open: Qn, preset, en
  D_Flip_Flop d_ff_6 (.clk(in_4), .D(controlled_buffer_5_out), .Q(v4), .reset(in_3));  // open: Qn, preset, en
  D_Flip_Flop d_ff_7 (.clk(in_4), .D(controlled_buffer_6_out), .Q(v5), .reset(in_3));  // open: Qn, preset, en
  D_Flip_Flop d_ff_8 (.clk(in_4), .D(controlled_buffer_7_out), .Q(v6), .reset(in_3));  // open: Qn, preset, en
  D_Flip_Flop d_ff_9 (.clk(in_4), .D(controlled_buffer_8_out), .Q(v7), .reset(in_3));  // open: Qn, preset, en
  and and_24 (en0, decoder_3_out0, Finish);
  and and_25 (en1, decoder_3_out1, Finish);
  and and_26 (en2, decoder_3_out2, Finish);
  and and_27 (en3, decoder_3_out3, Finish);
  and and_28 (en4, Finish, decoder_3_out4);
  and and_29 (en5, Finish, decoder_3_out5);
  and and_30 (en6, Finish, decoder_3_out6);
  and and_31 (en7, Finish, decoder_3_out7);
  or or_19 (dirty, demultiplexer_2_out0, d_ff_1_q);
  Multiplexer #(.width(4)) multiplexer_10 (
    .in0(WriteTime), .in1(ReadTime), .out(multiplexer_10_out), .sel(R));  // open: en
  Decoder #(.select(3)) decoder_4 (
    .out0(decoder_4_out0), .out1(decoder_4_out1), .out2(decoder_4_out2), .out3(decoder_4_out3),
    .out4(decoder_4_out4), .out5(decoder_4_out5), .out6(decoder_4_out6), .out7(decoder_4_out7), .sel(idx));  // open: en
  WaitCircuit waitcircuit_1 (
    .Wait_Time(multiplexer_10_out), .Start(start), .Clear(in_3), .Clock(in_4), .Ready(Ready), .CS(CS));
  D_Flip_Flop d_ff_10 (.clk(in_4), .D(enV_0), .Q(FinishRead));  // open: Qn, preset, en, reset
  D_Flip_Flop d_ff_11 (.clk(in_4), .D(dirty), .Q(FinishWrt));  // open: Qn, preset, en, reset
  or or_20 (Finish, Finish_3, Finish_1);
  Register #(.width(1)) register_9 (.D(dirty), .en(enDirty0), .Q(d0), .clk(in_4), .clr(in_3));
  Register #(.width(1)) register_10 (.D(dirty), .en(enDirty1), .Q(d1), .clk(in_4), .clr(in_3));
  Register #(.width(1)) register_11 (.D(dirty), .en(enDirty2), .Q(d2), .clk(in_4), .clr(in_3));
  Register #(.width(1)) register_12 (.D(dirty), .en(enDirty3), .Q(d3), .clk(in_4), .clr(in_3));
  Multiplexer #(.select(3), .width(16)) multiplexer_11 (
    .in0(tag0), .in1(tag1), .in2(tag2), .in3(tag3), .in4(tag4), .in5(tag5), .in6(tag6), .in7(tag7),
    .out(tagAddr), .sel(idx));  // open: en
  and and_32 (enDirty0, decoder_4_out0, LdDirty);
  and and_33 (enDirty1, decoder_4_out1, LdDirty);
  and and_34 (enDirty2, decoder_4_out2, LdDirty);
  and and_35 (enDirty3, decoder_4_out3, LdDirty);
  and and_36 (enDirty4, LdDirty, decoder_4_out4);
  and and_37 (enDirty5, LdDirty, decoder_4_out5);
  and and_38 (enDirty6, LdDirty, decoder_4_out6);
  and and_39 (enDirty7, LdDirty, decoder_4_out7);
  Register #(.width(1)) register_13 (.D(dirty), .en(enDirty4), .Q(d4), .clk(in_4), .clr(in_3));
  Register #(.width(1)) register_14 (.D(dirty), .en(enDirty5), .Q(d5), .clk(in_4), .clr(in_3));
  Register #(.width(1)) register_15 (.D(dirty), .en(enDirty6), .Q(d6), .clk(in_4), .clr(in_3));
  Register #(.width(1)) register_16 (.D(dirty), .en(enDirty7), .Q(d7), .clk(in_4), .clr(in_3));

  assign Mask = 4'b1111;

  // Other names for the same wires on the sheet: offset[1:0] = Address[3:2]; Address_t[15:0] = Address[19:4];
  //   tag[15:0] = Address[19:4]; Clear = in_3; CLK = in_4; Enable = in_2; Finish_0 = enV_0; R_W = in_5;
  //   r_w_0 = btag_0; r_w_1 = btag_1; RAM_OUTPUT_0[31:0] = RAM_Out_0; RAM_OUTPUT_1[31:0] = RAM_Out_1;
  //   RAM_OUTPUT_2[31:0] = RAM_Out_2; RAM_OUTPUT_3[31:0] = RAM_Out_3; Read_Time[3:0] = ReadTime; enV_1 = dirty;
  //   Finish_2 = dirty; LdDirty_1 = dirty; selVal = dirty; start_0 = R_0; start_1 = enRnd_1; start_2 = R_1;
  //   start_3 = enRnd_0; Value_t[31:0] = {Value[7:0], Value[15:8], Value[23:16], Value[31:24]};
  //   Write_Time[3:0] = WriteTime

  // Notes on the sheet:
  //   DATA FROM RAM
  //   RAM TIMING
  //   RAM CONTROL
  //   Bank 0
  //   Bank 1
  //   Bank 2
  //   Bank 3
  //   Reading
  //   Writing
endmodule
